// Logisim project Processador_Redux_2.circ as structural Verilog: 11 circuits, main circuit Redux_V
module Redux_V (
  input  MUX_SumPC,
  output [7:0] out_2,
  output [7:0] out_3,
  output [3:0] out_4,
  output [7:0] out_5,
  output [3:0] out_6,
  output [7:0] out_7,
  output [7:0] out_8,
  output [7:0] out_9,
  output [7:0] out_10,
  output [7:0] out_11,
  output [7:0] out_12
);

  wire clk_mem_out, digital_oscilloscope_1_p1, digital_oscilloscope_1_p3, dualram_1_p1, dualram_1_p2, MUX_PC;
  wire [1:0] multiplexer_1_out;
  wire [7:0] adder_1_out, multiplexer_2_out, multiplexer_3_out, multiplexer_5_out;

  Clock #(.highDuration(2), .lowDuration(2), .phaseOffset(3)) clk_processador ();  // open: out
  assign out_9 = {{4{out_2[3]}}, out_2[3:0]};  // Bit_Extender bit_extender_1
  // Digital_Oscilloscope digital_oscilloscope_1: pin names not known; wires that end beside it: digital_oscilloscope_1_p1, digital_oscilloscope_1_p1, digital_oscilloscope_1_p3, digital_oscilloscope_1_p3
  Multiplexer #(.width(2)) multiplexer_1 (.in0(out_2[3:2]), .in1(2'b00), .out(multiplexer_1_out));  // open: sel
  Circuito_de_Salto circuito_de_salto_1 (.R_r0(out_10), .MUX_PC(MUX_PC));  // open: JAR, Branch
  Banco_de_Registradores banco_de_registradores_1 (
    .rd(multiplexer_1_out), .ra(multiplexer_1_out), .rb(out_2[1:0]), .R_ra(out_10), .R_rb(out_11));  // open: clk, RegIn, RegWrite
  Multiplexer #(.width(8)) multiplexer_2 (.in0(out_11), .in1(out_9), .out(multiplexer_2_out));  // open: sel
  Shifter shifter_1 (.in(out_9), .\dist (3'b100), .out(out_8));
  ULA ula_1 (.ULA_A(out_10), .ULA_B(multiplexer_2_out), .ULA_OUT(out_12));  // open: ALUOp
  Unidade_de_Controle Controle (.opcode(out_2[7:4]));  // open: MUX_Type, ALUOp, RegWrite, MemWrite, MUX_RegIn, MUX_ULA_B, JAR, Branch, MUX_SumPC
  Clock #(.phaseOffset(3)) clk_mem (.out(clk_mem_out));
  // DualRAM #(.asyncread("true"), .clearpin("true")) dualram_1: pin names not known; wires that end beside it: dualram_1_p1, dualram_1_p2, dualram_1_p2, out_3, 1'b0, 1'b1, clk_mem_out, {8{1'b0}}, out_11, 1'b1, clk_mem_out, out_10, out_2, out_7
  Adder adder_1 (.a(out_3), .b(multiplexer_3_out), .out(adder_1_out));  // open: cin, cout
  Multiplexer #(.width(8)) multiplexer_3 (.in0(8'h1), .in1(out_9), .out(multiplexer_3_out), .sel(MUX_SumPC));
  Multiplexer #(.width(8)) multiplexer_4 (.in0(adder_1_out), .in1(out_11), .out(out_5), .sel(MUX_PC));
  PC pc_1 (.PC_In(out_5), .PC_Out(out_3));  // open: PCWrite, clk
  Multiplexer #(.select(2), .width(8)) multiplexer_5 (
    .in0(out_12), .in1(out_7), .in2(out_9), .in3(out_8), .out(multiplexer_5_out));  // open: sel

  assign out_4 = out_2[7:4];
  assign out_6 = out_2[3:0];

  // Other names for the same wires on the sheet: Imm_Ext[7:0] = out_9; Imediato[3:0] = out_2[3:0];
  //   Instrucao[7:0] = out_2; Opcode[3:0] = out_2[7:4]; MemDataOut[7:0] = out_7; PC_In[7:0] = out_5;
  //   PC_OUT[7:0] = out_3; R_ra[7:0] = out_10; R_rb[7:0] = out_11; ULA_OUT[7:0] = out_12; Upper_Imm[7:0] = out_8

  // Notes on the sheet:
  //   I. DECODE (ID)
  //   EXECUTE (EX)
  //   Memória de Instruções
  //   Memória de Dados
  //   I. FETCH (IF)
  //   MEMORY (MEM)
  //   WRITE BACK (WB)
endmodule

module Banco_de_Registradores (
  input  clk,
  input  [7:0] RegIn,
  input  RegWrite,
  input  [1:0] rd,
  input  [1:0] ra,
  input  [1:0] rb,
  output [7:0] R_ra,
  output [7:0] R_rb
);

  wire decoder_1_out0, decoder_1_out1, decoder_1_out2, decoder_1_out3;
  wire [7:0] registradores_1_r_r0, registradores_1_r_r1, registradores_1_r_r2, registradores_1_r_r3;

  Decoder #(.enable("false"), .select(2)) decoder_1 (
    .out0(decoder_1_out0), .out1(decoder_1_out1), .out2(decoder_1_out2), .out3(decoder_1_out3), .sel(rd));
  Registradores registradores_1 (
    .RegWrite(RegWrite), .RegIn(RegIn), .clk(clk), .En0(decoder_1_out0), .En1(decoder_1_out1),
    .En2(decoder_1_out2), .En3(decoder_1_out3), .R_r0(registradores_1_r_r0), .R_r1(registradores_1_r_r1),
    .R_r2(registradores_1_r_r2), .R_r3(registradores_1_r_r3));
  Multiplexer #(.select(2), .width(8)) multiplexer_1 (
    .in0(registradores_1_r_r0), .in1(registradores_1_r_r1), .in2(registradores_1_r_r2),
    .in3(registradores_1_r_r3), .out(R_ra), .sel(ra));
  Multiplexer #(.select(2), .width(8)) multiplexer_2 (
    .in0(registradores_1_r_r0), .in1(registradores_1_r_r1), .in2(registradores_1_r_r2),
    .in3(registradores_1_r_r3), .out(R_rb), .sel(rb));
endmodule

module Registradores (
  input  RegWrite,
  input  [7:0] RegIn,
  input  clk,
  input  En0,
  input  En1,
  input  En2,
  input  En3,
  output [7:0] R_r0,
  output [7:0] R_r1,
  output [7:0] R_r2,
  output [7:0] R_r3
);

  wire and_1_out, and_2_out, and_3_out, and_4_out;

  and and_1 (and_1_out, En0, RegWrite);
  and and_2 (and_2_out, En1, RegWrite);
  and and_3 (and_3_out, En2, RegWrite);
  and and_4 (and_4_out, En3, RegWrite);
  Register r0 (.D(RegIn), .en(and_1_out), .clk(clk), .Q(R_r0));  // open: clr
  Register r1 (.D(RegIn), .en(and_2_out), .clk(clk), .Q(R_r1));  // open: clr
  Register r2 (.D(RegIn), .en(and_3_out), .clk(clk), .Q(R_r2));  // open: clr
  Register r3 (.D(RegIn), .en(and_4_out), .clk(clk), .Q(R_r3));  // open: clr
endmodule

module PC (
  input  [7:0] PC_In,
  input  PCWrite,
  input  clk,
  output [7:0] PC_Out
);

  Register register_1 (.D(PC_In), .en(PCWrite), .clk(clk), .Q(PC_Out));  // open: clr
endmodule

module ULA (
  input  [7:0] ULA_A,
  input  [7:0] ULA_B,
  input  [2:0] ALUOp,
  output [7:0] ULA_OUT
);

  wire [7:0] adder_1_out, and_1_out, negator_1_out, or_1_out, shift_right_1_ula_out, shifter_left_1_ula_out,
       subtractor_1_out, xor_1_out;

  Negator negator_1 (.in(ULA_B), .out(negator_1_out));
  assign and_1_out = ULA_A & ULA_B;  // AND_Gate and_1, 8 bits wide
  assign or_1_out = ULA_A | ULA_B;  // OR_Gate or_1, 8 bits wide
  Adder adder_1 (.a(ULA_A), .b(ULA_B), .out(adder_1_out));  // open: cin, cout
  Subtractor subtractor_1 (.a(ULA_A), .b(ULA_B), .out(subtractor_1_out));  // open: bin, bout
  assign xor_1_out = ULA_A ^ ULA_B;  // XOR_Gate xor_1, 8 bits wide
  Shifter_Left shifter_left_1 (.ULA_A(ULA_A), .ULA_B(ULA_B), .ULA_OUT(shifter_left_1_ula_out));
  Shift_Right shift_right_1 (.ULA_A(ULA_A), .ULA_B(ULA_B), .ULA_OUT(shift_right_1_ula_out));
  Multiplexer #(.select(3), .width(8)) multiplexer_1 (
    .in0(negator_1_out), .in1(and_1_out), .in2(or_1_out), .in3(xor_1_out), .in4(adder_1_out),
    .in5(subtractor_1_out), .in6(shifter_left_1_ula_out), .in7(shift_right_1_ula_out), .out(ULA_OUT),
    .sel(ALUOp));
endmodule

module Circuito_de_Salto (
  input  JAR,
  input  Branch,
  input  [7:0] R_r0,
  output MUX_PC
);

  wire and_1_out, nor_1_out;

  and and_1 (and_1_out, Branch, nor_1_out);
  nor nor_1 (nor_1_out, R_r0[0], R_r0[1], R_r0[2], R_r0[3], R_r0[4], R_r0[5], R_r0[6], R_r0[7]);
  or or_1 (MUX_PC, JAR, and_1_out);

  // Notes on the sheet:
  //   Se 'for branch' e R[r0] == 0 OU 'for salto incondional', então desvie
endmodule

module Proximo_PC (
  input  MUX_PC,
  input  [7:0] PC_OUT,
  input  [7:0] Imm_Ext,
  input  [7:0] R_rb,
  input  MUX_SumPC,
  output [7:0] PC_In
);

  wire [7:0] adder_1_out, multiplexer_1_out;

  Multiplexer #(.width(8)) multiplexer_1 (.in0(8'h1), .in1(Imm_Ext), .out(multiplexer_1_out), .sel(MUX_SumPC));
  Multiplexer #(.width(8)) multiplexer_2 (.in0(adder_1_out), .in1(R_rb), .out(PC_In), .sel(MUX_PC));
  Adder adder_1 (.a(PC_OUT), .b(multiplexer_1_out), .out(adder_1_out));  // open: cin, cout
endmodule

module Shifter_Left (
  input  [7:0] ULA_A,
  input  [7:0] ULA_B,
  output [7:0] ULA_OUT
);

  wire or_1_out;
  wire [7:0] shifter_1_out;

  Shifter shifter_1 (.in(ULA_A), .\dist (ULA_B[2:0]), .out(shifter_1_out));
  Multiplexer #(.width(8)) multiplexer_1 (.in0(shifter_1_out), .in1({8{1'b0}}), .out(ULA_OUT), .sel(or_1_out));
  or or_1 (or_1_out, ULA_B[3], ULA_B[4], ULA_B[5], ULA_B[6], ULA_B[7]);

  // Notes on the sheet:
  //   Se o shift tiver overflow, então o resultado do shift será 0
endmodule

module Shift_Right (
  input  [7:0] ULA_A,
  input  [7:0] ULA_B,
  output [7:0] ULA_OUT
);

  wire or_1_out;
  wire [7:0] shifter_1_out;

  Shifter #(.shift("lr")) shifter_1 (.in(ULA_A), .\dist (ULA_B[2:0]), .out(shifter_1_out));
  Multiplexer #(.width(8)) multiplexer_1 (.in0(shifter_1_out), .in1({8{1'b0}}), .out(ULA_OUT), .sel(or_1_out));
  or or_1 (or_1_out, ULA_B[3], ULA_B[4], ULA_B[5], ULA_B[6], ULA_B[7]);

  // Notes on the sheet:
  //   Se o shift tiver overflow, então o resultado do shift será 0
endmodule

module Unidade_de_Controle (
  input  [3:0] opcode,
  output MUX_Type,
  output [2:0] ALUOp,
  output RegWrite,
  output MemWrite,
  output [1:0] MUX_RegIn,
  output MUX_ULA_B,
  output JAR,
  output Branch,
  output MUX_SumPC
);

  wire and_1_out, and_2_out, and_3_out, and_4_out, and_6_out, and_7_out, not_2_out, not_3_out, not_4_out;

  not not_1 (MUX_ULA_B, opcode[3]);
  not not_2 (not_2_out, opcode[2]);
  not not_3 (not_3_out, opcode[1]);
  not not_4 (not_4_out, opcode[0]);
  and and_1 (and_1_out, MUX_ULA_B, not_3_out, opcode[0]);
  and and_2 (and_2_out, MUX_ULA_B, opcode[2], not_4_out);
  and and_3 (and_3_out, opcode[1], not_4_out);
  and and_4 (and_4_out, opcode[2], not_3_out);
  and and_5 (MemWrite, MUX_ULA_B, not_2_out, opcode[1], opcode[0]);
  and and_6 (and_6_out, MUX_ULA_B, opcode[0]);
  and and_7 (and_7_out, MUX_ULA_B, opcode[2], opcode[1]);
  and and_8 (MUX_RegIn[0], MUX_ULA_B, opcode[1]);
  and and_9 (JAR, MUX_ULA_B, opcode[2], opcode[1], opcode[0]);
  and and_10 (Branch, MUX_ULA_B, not_2_out, not_3_out, not_4_out);
  and and_11 (MUX_SumPC, MUX_ULA_B, not_2_out, not_3_out, opcode[0]);
  or or_1 (MUX_Type, and_1_out, and_2_out);
  or or_2 (RegWrite, and_3_out, and_4_out, opcode[3]);
  or or_3 (MUX_RegIn[1], and_6_out, and_7_out);

  assign ALUOp = opcode[2:0];
endmodule

module Teste_clk (
);

  wire clock_1_out, clock_2_out;

  Clock #(.phaseOffset(3)) clock_1 (.out(clock_1_out));
  Clock #(.highDuration(2), .lowDuration(2), .phaseOffset(3)) clock_2 (.out(clock_2_out));
  // Digital_Oscilloscope digital_oscilloscope_1: pin names not known; wires that end beside it: clock_1_out, clock_2_out
endmodule
