// Logisim project Processador_Redux_Pipeline.circ as structural Verilog: 17 circuits, main circuit Redux_V
module Redux_V (
  output [7:0] out_1,
  output [7:0] out_2,
  output [3:0] out_3,
  output [7:0] out_4,
  output [3:0] out_5,
  output [7:0] out_6,
  output [7:0] out_7,
  output [7:0] out_8,
  output [7:0] out_9,
  output [7:0] out_10,
  output [7:0] out_11
);

  wire and_1_out, Branch_EX, Branch_ID_EX_q, Controle_branch, Controle_jar, Controle_memwrite,
       Controle_mux_sumpc, Controle_mux_type, Controle_mux_ula_b, Controle_regwrite,
       digital_oscilloscope_1_p1, digital_oscilloscope_1_p3, dualram_1_p1, dualram_1_p5, Flush, JAR_ID_EX_q,
       MemWrite_EX, MemWrite_EX_MEM_q, multiplexer_4_out, multiplexer_5_out, MUX_PC, MUX_SumPC, MUX_Type,
       MUX_ULA_B, not_1_out, or_2_out, PCWrite_Hazard, PredictTaken, PredictTaken_EX, PredictTaken_IF_ID,
       RegWrite_EX, RegWrite_MEM, RegWrite_WB, Stall, Taken_EX, Write_IF_ID, xor_1_out;
  wire [1:0] Controle_mux_regin, MUX_RegIn_EX, MUX_RegIn_MEM, MUX_RegIn_MEM_WB_q, ra_IF_ID, ra_q, rb_q,
       rd_ID_EX, rd_MEM, rd_WB, unidade_forwarding_1_fwa, unidade_forwarding_1_fwb;
  wire [2:0] ALUop_ID_EX_q, Controle_aluop, multiplexer_3_out;
  wire [3:0] multiplexer_6_out, Opcode_EX;
  wire [7:0] adder_1_out, banco_de_registradores_1_r_ra, banco_de_registradores_1_r_rb, DataWB,
       dualram_1_p12, dualram_1_p13, Endereco_Previsto, Imm_Ext_EX, Imm_Ext_MEM, Imm_Ext_MEM_WB_q,
       MemDataOut1_q, multiplexer_7_out, multiplexer_8_out, multiplexer_9_out, multiplexer_11_out,
       multiplexer_13_out, multiplexer_14_out, PC_Out_EX, PC_Out_IF_ID, PC_Out_t, Proximo_PC, R_ra_EX,
       R_ra_EX_MEM_q, R_rb_EX, R_rb_EX_MEM_q, shifter_1_out, ula_1_ula_out, ULA_OUT_MEM, ULA_Out_MEM_WB_q,
       unidade_forwarding_1_dataexmem, Upper_Imm_MEM, Upper_Imm_MEM_WB_q;

  Clock #(.highDuration(2), .lowDuration(2), .phaseOffset(3)) clk_processador ();  // open: out
  assign out_8 = {{4{out_1[3]}}, out_1[3:0]};  // Bit_Extender bit_extender_1
  Multiplexer #(.width(2)) multiplexer_1 (.in0(out_1[3:2]), .in1(2'b00), .out(ra_IF_ID), .sel(MUX_Type));
  // Digital_Oscilloscope digital_oscilloscope_1: pin names not known; wires that end beside it: digital_oscilloscope_1_p1, digital_oscilloscope_1_p1, digital_oscilloscope_1_p3, digital_oscilloscope_1_p3
  Unidade_de_Controle Controle (
    .opcode(out_3), .MUX_Type(Controle_mux_type), .ALUOp(Controle_aluop), .MUX_ULA_B(Controle_mux_ula_b),
    .Branch(Controle_branch), .JAR(Controle_jar), .MUX_SumPC(Controle_mux_sumpc),
    .MemWrite(Controle_memwrite), .RegWrite(Controle_regwrite), .MUX_RegIn(Controle_mux_regin));
  Hazard_Detectation_Unit hazard_detectation_unit_1 (
    .Opcode_ID_EX(Opcode_EX), .Opcode_IF_ID(out_1[7:4]), .ra_IF_ID(ra_IF_ID), .rd_ID_EX(rd_ID_EX),
    .rb_IF_ID(out_1[1:0]), .PCWrite(PCWrite_Hazard), .Write_IF_ID(Write_IF_ID), .Stall(Stall));
  Banco_de_Registradores banco_de_registradores_1 (
    .RegIn(DataWB), .rd(rd_WB), .ra(ra_IF_ID), .rb(out_1[1:0]), .R_ra(banco_de_registradores_1_r_ra),
    .R_rb(banco_de_registradores_1_r_rb));  // open: clk, RegWrite
  Multiplexer multiplexer_2 (.in0(Controle_mux_type), .in1(1'b1), .out(MUX_Type), .sel(xor_1_out));
  xor xor_1 (xor_1_out, Stall, Flush);
  Multiplexer #(.width(3)) multiplexer_3 (.in0(Controle_aluop), .in1(3'b100), .out(multiplexer_3_out), .sel(xor_1_out));
  Multiplexer multiplexer_4 (.in0(Controle_mux_ula_b), .in1(1'b1), .out(multiplexer_4_out), .sel(xor_1_out));
  Multiplexer multiplexer_5 (.in0(Controle_regwrite), .in1(1'b1), .out(multiplexer_5_out), .sel(xor_1_out));
  Multiplexer #(.width(4)) multiplexer_6 (.in0(out_1[7:4]), .in1(4'b0100), .out(multiplexer_6_out), .sel(xor_1_out));
  Register #(.width(3)) ALUop_ID_EX (.D(multiplexer_3_out), .Q(ALUop_ID_EX_q));  // open: en, clk, clr
  Register #(.width(1)) MUX_ULA_B_ID_EX (.D(multiplexer_4_out), .Q(MUX_ULA_B));  // open: en, clk, clr
  Register #(.width(1)) Branch_ID_EX (.D(Controle_branch), .Q(Branch_ID_EX_q), .clr(xor_1_out));  // open: en, clk
  Register #(.width(1)) JAR_ID_EX (.D(Controle_jar), .Q(JAR_ID_EX_q), .clr(xor_1_out));  // open: en, clk
  Register #(.width(1)) Mux_SumPC_ID_EX (.D(Controle_mux_sumpc), .Q(MUX_SumPC), .clr(xor_1_out));  // open: en, clk
  Register #(.width(1)) MemWrite_ID_EX (.D(Controle_memwrite), .Q(MemWrite_EX), .clr(xor_1_out));  // open: en, clk
  Register #(.width(1)) RegWrite_ID_EX (.D(multiplexer_5_out), .Q(RegWrite_EX));  // open: en, clk, clr
  Register #(.width(2)) MUX_RegIn_ID_EX (.D(Controle_mux_regin), .Q(MUX_RegIn_EX), .clr(xor_1_out));  // open: en, clk
  Register #(.width(1)) PredictTaken_ID_EX (
    .D(PredictTaken_IF_ID), .Q(PredictTaken_EX), .clr(xor_1_out));  // open: en, clk
  Register PC_Out_ID_EX (.D(PC_Out_IF_ID), .Q(PC_Out_EX), .clr(xor_1_out));  // open: en, clk
  Register R_ra_ID_EX (.D(banco_de_registradores_1_r_ra), .Q(R_ra_EX), .clr(xor_1_out));  // open: en, clk
  Register R_rb_ID_EX (.D(banco_de_registradores_1_r_rb), .Q(R_rb_EX), .clr(xor_1_out));  // open: en, clk
  Register Imm_Ext_ID_EX (.D(out_8), .Q(Imm_Ext_EX), .clr(xor_1_out));  // open: en, clk
  Register #(.width(2)) u_rd_ID_EX (.D(ra_IF_ID), .Q(rd_ID_EX), .clr(xor_1_out));  // open: en, clk
  Register #(.width(2)) ra (.D(ra_IF_ID), .Q(ra_q), .clr(xor_1_out));  // open: en, clk
  Register #(.width(2)) rb (.D(out_1[1:0]), .Q(rb_q), .clr(xor_1_out));  // open: en, clk
  Register #(.width(4)) Opcode_ID_EX (.D(multiplexer_6_out), .Q(Opcode_EX));  // open: en, clk, clr
  Multiplexer #(.width(8)) multiplexer_7 (.in0(R_rb_EX), .in1(Imm_Ext_EX), .out(multiplexer_7_out), .sel(MUX_ULA_B));
  Unidade_Forwarding unidade_forwarding_1 (
    .RegWrite_WB(RegWrite_MEM), .RegWrite_MEM(RegWrite_WB), .ra(ra_q), .rb(rb_q), .rd_MEM(rd_MEM),
    .rd_WB(rd_WB), .Opcode_ID_EX(Opcode_EX), .ULA_Out(ULA_OUT_MEM), .Imm_Ext(Imm_Ext_MEM),
    .Upper_Immediate(Upper_Imm_MEM), .FwA(unidade_forwarding_1_fwa), .FwB(unidade_forwarding_1_fwb),
    .DataExMem(unidade_forwarding_1_dataexmem));
  Multiplexer #(.select(2), .width(8)) multiplexer_8 (
    .in0(R_ra_EX), .in1(unidade_forwarding_1_dataexmem), .in2(DataWB), .out(multiplexer_8_out),
    .sel(unidade_forwarding_1_fwa));  // open: in3
  Multiplexer #(.select(2), .width(8)) multiplexer_9 (
    .in0(R_ra_EX), .in1(unidade_forwarding_1_dataexmem), .in2(DataWB), .out(multiplexer_9_out),
    .sel(unidade_forwarding_1_fwa));  // open: in3
  Multiplexer #(.select(2), .width(8)) multiplexer_10 (
    .in0(multiplexer_7_out), .in1(unidade_forwarding_1_dataexmem), .in2(DataWB), .out(R_rb_EX),
    .sel(unidade_forwarding_1_fwb));  // open: in3
  or or_1 (Taken_EX, MUX_PC, MUX_SumPC);
  Shifter shifter_1 (.in(Imm_Ext_EX), .\dist (3'b100), .out(shifter_1_out));
  Multiplexer #(.width(8)) multiplexer_11 (.in0(8'h1), .in1(Imm_Ext_EX), .out(multiplexer_11_out), .sel(MUX_SumPC));
  Circuito_de_Salto circuito_de_salto_1 (
    .JAR(JAR_ID_EX_q), .Branch(Branch_ID_EX_q), .R_ra(multiplexer_8_out), .MUX_PC(MUX_PC));
  ULA ula_1 (.ULA_A(multiplexer_9_out), .ULA_B(R_rb_EX), .ALUOp(ALUop_ID_EX_q), .ULA_OUT(ula_1_ula_out));
  xor xor_2 (Flush, PredictTaken_EX, Taken_EX);
  Multiplexer #(.width(8)) multiplexer_12 (.in0(adder_1_out), .in1(R_rb_EX), .out(Proximo_PC), .sel(MUX_PC));
  Adder adder_1 (.a(PC_Out_EX), .b(multiplexer_11_out), .out(adder_1_out));  // open: cin, cout
  Register ULA_Out_0 (.D(ula_1_ula_out), .Q(ULA_OUT_MEM));  // open: en, clk, clr
  Register Upper_Imm_EX_MEM (.D(shifter_1_out), .Q(Upper_Imm_MEM));  // open: en, clk, clr
  Register R_ra_EX_MEM (.D(R_ra_EX), .Q(R_ra_EX_MEM_q));  // open: en, clk, clr
  Register R_rb_EX_MEM (.D(R_rb_EX), .Q(R_rb_EX_MEM_q));  // open: en, clk, clr
  Register #(.width(2)) rd_EX_MEM (.D(rd_ID_EX), .Q(rd_MEM));  // open: en, clk, clr
  Register Imm_Ext_EX_MEM (.D(Imm_Ext_EX), .Q(Imm_Ext_MEM));  // open: en, clk, clr
  Register #(.width(1)) MemWrite_EX_MEM (.D(MemWrite_EX), .Q(MemWrite_EX_MEM_q));  // open: en, clk, clr
  Register #(.width(1)) RegWrite_EX_MEM (.D(RegWrite_EX), .Q(RegWrite_MEM));  // open: en, clk, clr
  Register #(.width(2)) MUX_RegIn_EX_MEM (.D(MUX_RegIn_EX), .Q(MUX_RegIn_MEM));  // open: en, clk, clr
  or or_2 (or_2_out, Flush, PCWrite_Hazard);
  // DualRAM #(.asyncread("true"), .clearpin("true")) dualram_1: pin names not known; wires that end beside it: dualram_1_p1, out_2, 1'b0, 1'b1, dualram_1_p5, {8{1'b0}}, R_rb_EX_MEM_q, MemWrite_EX_MEM_q, 1'b1, dualram_1_p5, R_ra_EX_MEM_q, dualram_1_p12, dualram_1_p13
  Clock #(.phaseOffset(3)) clk_mem (.out(dualram_1_p5));
  Multiplexer #(.width(8)) multiplexer_13 (
    .in0(Endereco_Previsto), .in1(Proximo_PC), .out(multiplexer_13_out), .sel(PredictTaken));
  PC pc_1 (.PC_In(multiplexer_13_out), .PCWrite(or_2_out), .PC_Out(PC_Out_t));  // open: clk
  BTB_e_Preditor btb_e_preditor_1 (
    .Taken_EX(Taken_EX), .JI_EX(MUX_SumPC), .JAR_EX(MUX_PC), .Branch_EX(Branch_EX), .Proximo_PC(Proximo_PC),
    .PC_Out_Ex(PC_Out_EX), .PC_Out(PC_Out_t), .Endereco_Previsto(Endereco_Previsto),
    .PredictTaken(PredictTaken));
  Multiplexer #(.width(8)) multiplexer_14 (.in0(dualram_1_p12), .in1(8'h4), .out(multiplexer_14_out), .sel(Flush));
  Register #(.width(1)) u_PredictTaken_IF_ID (
    .D(PredictTaken), .en(and_1_out), .Q(PredictTaken_IF_ID), .clr(Flush));  // open: clk
  Register u_PC_Out_IF_ID (.D(PC_Out_t), .en(and_1_out), .Q(PC_Out_IF_ID), .clr(Flush));  // open: clk
  Register Instrucao (.D(multiplexer_14_out), .en(and_1_out), .Q(out_1));  // open: clk, clr
  and and_1 (and_1_out, not_1_out, Stall);
  not not_1 (not_1_out, Flush);
  Register #(.width(1)) RegWrite_MEM_WB (.D(RegWrite_MEM), .Q(RegWrite_WB));  // open: en, clk, clr
  Register #(.width(2)) MUX_RegIn_MEM_WB (.D(MUX_RegIn_MEM), .Q(MUX_RegIn_MEM_WB_q));  // open: en, clk, clr
  Register ULA_Out_MEM_WB (.D(ULA_OUT_MEM), .Q(ULA_Out_MEM_WB_q));  // open: en, clk, clr
  Register MemDataOut1 (.D(dualram_1_p13), .Q(MemDataOut1_q));  // open: en, clk, clr
  Register Imm_Ext_MEM_WB (.D(Imm_Ext_MEM), .Q(Imm_Ext_MEM_WB_q));  // open: en, clk, clr
  Register Upper_Imm_MEM_WB (.D(Upper_Imm_MEM), .Q(Upper_Imm_MEM_WB_q));  // open: en, clk, clr
  Register #(.width(2)) rd_MEM_WB (.D(rd_MEM), .Q(rd_WB));  // open: en, clk, clr
  Multiplexer #(.select(2), .width(8)) multiplexer_15 (
    .in0(ULA_Out_MEM_WB_q), .in1(MemDataOut1_q), .in2(Imm_Ext_MEM_WB_q), .in3(Upper_Imm_MEM_WB_q),
    .out(DataWB), .sel(MUX_RegIn_MEM_WB_q));

  assign out_5 = out_1[3:0];

  // Other names for the same wires on the sheet: Imm_Ext[7:0] = out_8; Imediato[3:0] = out_1[3:0];
  //   Instrucao[7:0] = out_1; rb_IF_ID[1:0] = out_1[1:0]; MemDataOut[7:0] = out_6; Opcode[3:0] = out_3;
  //   PC_In[7:0] = out_4; PC_OUT[7:0] = out_2; R_ra[7:0] = out_9; R_rb[7:0] = out_10; Taken_1 = MUX_PC;
  //   Taken_2 = MUX_SumPC; ULA_OUT[7:0] = out_11; Upper_Imm[7:0] = out_7

  // Notes on the sheet:
  //   I. DECODE (ID)
  //   ID/EX
  //   EXECUTE (EX)
  //   EX/MEM
  //   I. FETCH (IF)
  //   Memória de Instruções
  //   Memória de Dados
  //   MEMORY (MEM)
  //   IF/ID
  //   WRITE BACK (WB)
endmodule

module Banco_de_Registradores (
  input  clk,
  input  [7:0] RegIn,
  input  RegWrite,
  input  [1:0] rd,
  input  [1:0] ra,
  input  [1:0] rb,
  output [7:0] R_ra,
  output [7:0] R_rb
);

  wire decoder_1_out0, decoder_1_out1, decoder_1_out2, decoder_1_out3;
  wire [7:0] registradores_1_r_r0, registradores_1_r_r1, registradores_1_r_r2, registradores_1_r_r3;

  Decoder #(.enable("false"), .select(2)) decoder_1 (
    .out0(decoder_1_out0), .out1(decoder_1_out1), .out2(decoder_1_out2), .out3(decoder_1_out3), .sel(rd));
  Registradores registradores_1 (
    .RegWrite(RegWrite), .RegIn(RegIn), .clk(clk), .En0(decoder_1_out0), .En1(decoder_1_out1),
    .En2(decoder_1_out2), .En3(decoder_1_out3), .R_r0(registradores_1_r_r0), .R_r1(registradores_1_r_r1),
    .R_r2(registradores_1_r_r2), .R_r3(registradores_1_r_r3));
  Multiplexer #(.select(2), .width(8)) multiplexer_1 (
    .in0(registradores_1_r_r0), .in1(registradores_1_r_r1), .in2(registradores_1_r_r2),
    .in3(registradores_1_r_r3), .out(R_ra), .sel(ra));
  Multiplexer #(.select(2), .width(8)) multiplexer_2 (
    .in0(registradores_1_r_r0), .in1(registradores_1_r_r1), .in2(registradores_1_r_r2),
    .in3(registradores_1_r_r3), .out(R_rb), .sel(rb));
endmodule

module Registradores (
  input  RegWrite,
  input  [7:0] RegIn,
  input  clk,
  input  En0,
  input  En1,
  input  En2,
  input  En3,
  output [7:0] R_r0,
  output [7:0] R_r1,
  output [7:0] R_r2,
  output [7:0] R_r3
);

  wire and_1_out, and_2_out, and_3_out, and_4_out;

  and and_1 (and_1_out, En0, RegWrite);
  and and_2 (and_2_out, En1, RegWrite);
  and and_3 (and_3_out, En2, RegWrite);
  and and_4 (and_4_out, En3, RegWrite);
  Register r0 (.D(RegIn), .en(and_1_out), .clk(clk), .Q(R_r0));  // open: clr
  Register r1 (.D(RegIn), .en(and_2_out), .clk(clk), .Q(R_r1));  // open: clr
  Register r2 (.D(RegIn), .en(and_3_out), .clk(clk), .Q(R_r2));  // open: clr
  Register r3 (.D(RegIn), .en(and_4_out), .clk(clk), .Q(R_r3));  // open: clr
endmodule

module PC (
  input  [7:0] PC_In,
  input  PCWrite,
  input  clk,
  output [7:0] PC_Out
);

  Register register_1 (.D(PC_In), .en(PCWrite), .clk(clk), .Q(PC_Out));  // open: clr
endmodule

module ULA (
  input  [7:0] ULA_A,
  input  [7:0] ULA_B,
  input  [2:0] ALUOp,
  output [7:0] ULA_OUT
);

  wire [7:0] adder_1_out, and_1_out, negator_1_out, or_1_out, shift_right_1_ula_out, shifter_left_1_ula_out,
       subtractor_1_out, xor_1_out;

  Negator negator_1 (.in(ULA_B), .out(negator_1_out));
  assign and_1_out = ULA_A & ULA_B;  // AND_Gate and_1, 8 bits wide
  assign or_1_out = ULA_A | ULA_B;  // OR_Gate or_1, 8 bits wide
  Adder adder_1 (.a(ULA_A), .b(ULA_B), .out(adder_1_out));  // open: cin, cout
  Subtractor subtractor_1 (.a(ULA_A), .b(ULA_B), .out(subtractor_1_out));  // open: bin, bout
  assign xor_1_out = ULA_A ^ ULA_B;  // XOR_Gate xor_1, 8 bits wide
  Shifter_Left shifter_left_1 (.ULA_A(ULA_A), .ULA_B(ULA_B), .ULA_OUT(shifter_left_1_ula_out));
  Shift_Right shift_right_1 (.ULA_A(ULA_A), .ULA_B(ULA_B), .ULA_OUT(shift_right_1_ula_out));
  Multiplexer #(.select(3), .width(8)) multiplexer_1 (
    .in0(negator_1_out), .in1(and_1_out), .in2(or_1_out), .in3(xor_1_out), .in4(adder_1_out),
    .in5(subtractor_1_out), .in6(shifter_left_1_ula_out), .in7(shift_right_1_ula_out), .out(ULA_OUT),
    .sel(ALUOp));
endmodule

module Circuito_de_Salto (
  input  JAR,
  input  Branch,
  input  [7:0] R_ra,
  output MUX_PC
);

  wire and_1_out, nor_1_out;

  and and_1 (and_1_out, Branch, nor_1_out);
  nor nor_1 (nor_1_out, R_ra[0], R_ra[1], R_ra[2], R_ra[3], R_ra[4], R_ra[5], R_ra[6], R_ra[7]);
  or or_1 (MUX_PC, JAR, and_1_out);

  // Notes on the sheet:
  //   Se 'for branch' e R[r0] == 0 OU 'for salto incondional', então desvie
endmodule

module Proximo_PC (
  input  MUX_PC,
  input  [7:0] PC_OUT,
  input  [7:0] Imm_Ext,
  input  [7:0] R_rb,
  input  MUX_SumPC,
  output [7:0] PC_In
);

  wire [7:0] adder_1_out, multiplexer_1_out;

  Multiplexer #(.width(8)) multiplexer_1 (.in0(8'h1), .in1(Imm_Ext), .out(multiplexer_1_out), .sel(MUX_SumPC));
  Multiplexer #(.width(8)) multiplexer_2 (.in0(adder_1_out), .in1(R_rb), .out(PC_In), .sel(MUX_PC));
  Adder adder_1 (.a(PC_OUT), .b(multiplexer_1_out), .out(adder_1_out));  // open: cin, cout
endmodule

module Shifter_Left (
  input  [7:0] ULA_A,
  input  [7:0] ULA_B,
  output [7:0] ULA_OUT
);

  wire or_1_out;
  wire [7:0] shifter_1_out;

  Shifter shifter_1 (.in(ULA_A), .\dist (ULA_B[2:0]), .out(shifter_1_out));
  Multiplexer #(.width(8)) multiplexer_1 (.in0(shifter_1_out), .in1({8{1'b0}}), .out(ULA_OUT), .sel(or_1_out));
  or or_1 (or_1_out, ULA_B[3], ULA_B[4], ULA_B[5], ULA_B[6], ULA_B[7]);

  // Notes on the sheet:
  //   Se o shift tiver overflow, então o resultado do shift será 0
endmodule

module Shift_Right (
  input  [7:0] ULA_A,
  input  [7:0] ULA_B,
  output [7:0] ULA_OUT
);

  wire or_1_out;
  wire [7:0] shifter_1_out;

  Shifter #(.shift("lr")) shifter_1 (.in(ULA_A), .\dist (ULA_B[2:0]), .out(shifter_1_out));
  Multiplexer #(.width(8)) multiplexer_1 (.in0(shifter_1_out), .in1({8{1'b0}}), .out(ULA_OUT), .sel(or_1_out));
  or or_1 (or_1_out, ULA_B[3], ULA_B[4], ULA_B[5], ULA_B[6], ULA_B[7]);

  // Notes on the sheet:
  //   Se o shift tiver overflow, então o resultado do shift será 0
endmodule

module Unidade_de_Controle (
  input  [3:0] opcode,
  output MUX_Type,
  output [2:0] ALUOp,
  output MUX_ULA_B,
  output Branch,
  output JAR,
  output MUX_SumPC,
  output MemWrite,
  output RegWrite,
  output [1:0] MUX_RegIn
);

  wire and_1_out, and_2_out, and_7_out, and_8_out, and_9_out, and_10_out, not_2_out, not_3_out, not_4_out;

  not not_1 (MUX_ULA_B, opcode[3]);
  not not_2 (not_2_out, opcode[2]);
  not not_3 (not_3_out, opcode[1]);
  not not_4 (not_4_out, opcode[0]);
  and and_1 (and_1_out, MUX_ULA_B, not_3_out, opcode[0]);
  and and_2 (and_2_out, MUX_ULA_B, opcode[2], not_4_out);
  and and_3 (Branch, MUX_ULA_B, not_2_out, not_3_out, not_4_out);
  and and_4 (JAR, MUX_ULA_B, opcode[2], opcode[1], opcode[0]);
  and and_5 (MUX_SumPC, MUX_ULA_B, not_2_out, not_3_out, opcode[0]);
  and and_6 (MemWrite, MUX_ULA_B, not_2_out, opcode[1], opcode[0]);
  and and_7 (and_7_out, opcode[1], not_4_out);
  and and_8 (and_8_out, opcode[2], not_3_out);
  and and_9 (and_9_out, MUX_ULA_B, opcode[0]);
  and and_10 (and_10_out, MUX_ULA_B, opcode[2], opcode[1]);
  and and_11 (MUX_RegIn[0], MUX_ULA_B, opcode[1]);
  or or_1 (MUX_Type, and_1_out, and_2_out);
  or or_2 (RegWrite, and_7_out, and_8_out, opcode[3]);
  or or_3 (MUX_RegIn[1], and_9_out, and_10_out);

  assign ALUOp = opcode[2:0];
endmodule

module Teste_clk (
);

  wire clock_1_out, clock_2_out;

  Clock #(.phaseOffset(3)) clock_1 (.out(clock_1_out));
  Clock #(.highDuration(2), .lowDuration(2), .phaseOffset(3)) clock_2 (.out(clock_2_out));
  // Digital_Oscilloscope digital_oscilloscope_1: pin names not known; wires that end beside it: clock_1_out, clock_2_out
endmodule

module Controle_Forwading (
  input  ra_igual_rd_MEM,
  input  rb_igual_rd_MEM,
  input  ra_igual_rd_WB,
  input  rb_igual_rd_WB,
  output [1:0] ForwardA,
  output [1:0] ForwardB
);

  wire not_1_out, not_2_out;

  not not_1 (not_1_out, ra_igual_rd_MEM);
  not not_2 (not_2_out, rb_igual_rd_MEM);
  and and_1 (ForwardA[1], not_1_out, ra_igual_rd_WB);
  and and_2 (ForwardB[1], not_2_out, rb_igual_rd_WB);

  assign ForwardA[0] = ra_igual_rd_MEM;
  assign ForwardB[0] = rb_igual_rd_MEM;
endmodule

// UnidadeFowarding
module Unidade_Forwarding (
  input  RegWrite_WB,
  input  RegWrite_MEM,
  input  [1:0] ra,
  input  [1:0] rb,
  input  [1:0] rd_MEM,
  input  [1:0] rd_WB,
  input  [3:0] Opcode_ID_EX,
  input  [7:0] ULA_Out,
  input  [7:0] Imm_Ext,
  input  [7:0] Upper_Immediate,
  output [1:0] FwA,
  output [1:0] FwB,
  output [7:0] DataExMem
);

  wire and_1_out, and_2_out, and_3_out, and_4_out, comparator_1_eq, comparator_2_eq, comparator_3_eq,
       comparator_4_eq, detector_de_leitura_1_regreada, detector_de_leitura_1_regreadb;
  wire [1:0] controle_forwading_1_forwarda, controle_forwading_1_forwardb;

  Comparator #(.width(2)) comparator_1 (.a(ra), .b(rd_MEM), .eq(comparator_1_eq));  // open: gt, lt
  Comparator #(.width(2)) comparator_2 (.a(rb), .b(rd_MEM), .eq(comparator_2_eq));  // open: gt, lt
  Comparator #(.width(2)) comparator_3 (.a(ra), .b(rd_WB), .eq(comparator_3_eq));  // open: gt, lt
  Comparator #(.width(2)) comparator_4 (.a(rb), .b(rd_WB), .eq(comparator_4_eq));  // open: gt, lt
  Multiplexer #(.select(2), .width(8)) multiplexer_1 (
    .in0(ULA_Out), .in2(Imm_Ext), .in3(Upper_Immediate), .out(DataExMem));  // open: in1, sel
  and and_1 (and_1_out, RegWrite_MEM, comparator_1_eq);
  and and_2 (and_2_out, RegWrite_MEM, comparator_2_eq);
  and and_3 (and_3_out, RegWrite_WB, comparator_3_eq);
  and and_4 (and_4_out, RegWrite_WB, comparator_4_eq);
  Controle_Forwading controle_forwading_1 (
    .ra_igual_rd_MEM(and_1_out), .rb_igual_rd_MEM(and_2_out), .ra_igual_rd_WB(and_3_out),
    .rb_igual_rd_WB(and_4_out), .ForwardA(controle_forwading_1_forwarda),
    .ForwardB(controle_forwading_1_forwardb));
  Detector_de_Leitura detector_de_leitura_1 (
    .Opcode(Opcode_ID_EX), .RegReadA(detector_de_leitura_1_regreada),
    .RegReadB(detector_de_leitura_1_regreadb));
  Multiplexer #(.width(2)) multiplexer_2 (
    .in0(2'b00), .in1(controle_forwading_1_forwarda), .out(FwA), .sel(detector_de_leitura_1_regreada));
  Multiplexer #(.width(2)) multiplexer_3 (
    .in0(2'b00), .in1(controle_forwading_1_forwardb), .out(FwB), .sel(detector_de_leitura_1_regreadb));

  // Notes on the sheet:
  //   RegWrite
endmodule

module Detector_de_Leitura (
  input  [3:0] Opcode,
  output RegReadA,
  output RegReadB
);

  wire and_1_out, and_2_out, and_3_out, and_4_out, and_5_out, and_6_out, and_7_out, and_8_out, and_9_out,
       not_1_out, not_2_out, not_3_out, not_4_out;

  not not_1 (not_1_out, Opcode[3]);
  not not_2 (not_2_out, Opcode[2]);
  not not_3 (not_3_out, Opcode[1]);
  not not_4 (not_4_out, Opcode[0]);
  and and_1 (and_1_out, not_2_out, Opcode[1]);
  and and_2 (and_2_out, Opcode[3], Opcode[0]);
  and and_3 (and_3_out, not_1_out, not_3_out, not_4_out);
  and and_4 (and_4_out, Opcode[3], Opcode[2]);
  and and_5 (and_5_out, not_1_out, not_2_out, not_4_out);
  and and_6 (and_6_out, Opcode[1], Opcode[0]);
  and and_7 (and_7_out, Opcode[3], Opcode[0]);
  and and_8 (and_8_out, Opcode[3], Opcode[2]);
  and and_9 (and_9_out, not_2_out, Opcode[1]);
  or or_1 (RegReadA, and_1_out, and_2_out, and_3_out, and_4_out);
  or or_2 (RegReadB, and_5_out, and_6_out, and_7_out, and_8_out, and_9_out);
endmodule

module Hazard_Detectation_Unit (
  input  [3:0] Opcode_ID_EX,
  input  [3:0] Opcode_IF_ID,
  input  [1:0] ra_IF_ID,
  input  [1:0] rd_ID_EX,
  input  [1:0] rb_IF_ID,
  output PCWrite,
  output Write_IF_ID,
  output Stall
);

  wire and_1_out, and_2_out, and_3_out, comparator_1_eq, comparator_2_eq, detector_de_leitura_1_regreada,
       detector_de_leitura_1_regreadb, or_1_out;

  and and_1 (and_1_out, ~Opcode_ID_EX[0], Opcode_ID_EX[1], ~Opcode_ID_EX[2], ~Opcode_ID_EX[3]);  // AND_Gate
  Comparator #(.width(2)) comparator_1 (.a(ra_IF_ID), .b(rd_ID_EX), .eq(comparator_1_eq));  // open: gt, lt
  Comparator #(.width(2)) comparator_2 (.a(rd_ID_EX), .b(rb_IF_ID), .eq(comparator_2_eq));  // open: gt, lt
  Detector_de_Leitura detector_de_leitura_1 (
    .Opcode(Opcode_IF_ID), .RegReadA(detector_de_leitura_1_regreada),
    .RegReadB(detector_de_leitura_1_regreadb));
  and and_2 (and_2_out, detector_de_leitura_1_regreada, comparator_1_eq);
  and and_3 (and_3_out, detector_de_leitura_1_regreadb, comparator_2_eq);
  or or_1 (or_1_out, and_2_out, and_3_out);
  and and_4 (Stall, and_1_out, or_1_out);
  not not_1 (PCWrite, Stall);
  not not_2 (Write_IF_ID, Stall);

  // Notes on the sheet:
  //   É Load
  //   Existe dependência
  //   Stall
endmodule

module BTB_e_Preditor (
  input  Taken_EX,
  input  JI_EX,
  input  JAR_EX,
  input  Branch_EX,
  input  [7:0] Proximo_PC,
  input  [7:0] PC_Out_Ex,
  input  [7:0] PC_Out,
  output [7:0] Endereco_Previsto,
  output PredictTaken
);

  wire comparator_1_eq, or_1_out, Validade_dout;
  wire [1:0] Estado_dout, novo_estado_1_novo_estado;
  wire [3:0] Endereco_Instrucao_dout, undriven;

  or or_1 (or_1_out, JI_EX, JAR_EX, Branch_EX);
  Multiplexer #(.width(4)) multiplexer_1 (.in0(PC_Out[3:0]), .in1(PC_Out_Ex[3:0]), .sel(or_1_out));  // open: out
  RAM #(.addrWidth(4), .asyncread("true"), .dataWidth(4)) Endereco_Instrucao (
    .addr(undriven), .we(or_1_out), .oe(1'b1), .din(PC_Out_Ex[7:4]), .dout(Endereco_Instrucao_dout));  // open: clk
  RAM #(.addrWidth(4), .asyncread("true")) Endereco_Desvio (
    .addr(undriven), .we(or_1_out), .oe(1'b1), .din(Proximo_PC), .dout(Endereco_Previsto));  // open: clk
  Comparator #(.width(4)) comparator_1 (
    .a(Endereco_Instrucao_dout), .b(PC_Out[7:4]), .eq(comparator_1_eq));  // open: gt, lt
  RAM #(.addrWidth(4), .asyncread("true"), .dataWidth(1)) Validade (
    .addr(undriven), .we(or_1_out), .oe(1'b1), .din(1'b1), .dout(Validade_dout));  // open: clk
  Novo_Estado novo_estado_1 (.Estado_Atual(Estado_dout), .Taken(Taken_EX), .Novo_Estado(novo_estado_1_novo_estado));
  RAM #(.addrWidth(4), .asyncread("true"), .dataWidth(2)) Estado (
    .addr(undriven), .we(or_1_out), .oe(1'b1), .din(novo_estado_1_novo_estado), .dout(Estado_dout));  // open: clk
  and and_1 (PredictTaken, Estado_dout[1], Validade_dout, ~or_1_out, comparator_1_eq);  // AND_Gate

  // Notes on the sheet:
  //   Taken?
  //   Valid?
  //   Esta lendo?
  //   Hit?
endmodule

// NovoEstado
module Novo_Estado (
  input  [1:0] Estado_Atual,
  input  Taken,
  output [1:0] Novo_Estado
);

  wire and_1_out, and_2_out, and_3_out, and_4_out, and_5_out, not_1_out;

  not not_1 (not_1_out, Estado_Atual[0]);
  and and_1 (and_1_out, Estado_Atual[0], Taken);
  and and_2 (and_2_out, Estado_Atual[1], Taken);
  and and_3 (and_3_out, Estado_Atual[1], Estado_Atual[0]);
  and and_4 (and_4_out, not_1_out, Taken);
  and and_5 (and_5_out, Estado_Atual[1], Taken);
  or or_1 (Novo_Estado[1], and_1_out, and_2_out, and_3_out);
  or or_2 (Novo_Estado[0], and_4_out, and_5_out);
endmodule
