// Logisim project Processador_Vetorial.circ as structural Verilog: 31 circuits, main circuit Sagui_Vetorial
module Sagui_Vetorial (
  input  Reset
);

  wire ALUOp_ID_EX_V, Branch_ID, Branch_ID_EX, clk_mem, clk_proc, dualram_1_p1, Flush, LI_ID, LI_ID_EX,
       MemWrite_EX_MEM_S, MemWrite_EX_MEM_V, MemWrite_ID, MemWrite_ID_EX_S, MemWrite_ID_EX_V, Move_ID,
       Move_ID_EX_S, Move_ID_EX_V, multiplexer_3_out, multiplexer_9_out, multiplexer_10_out,
       multiplexer_11_out, multiplexer_12_out, multiplexer_14_out, multiplexer_26_out, multiplexer_28_out,
       multiplexer_29_out, multiplexer_30_out, multiplexer_32_out, multiplexer_33_out, or_1_out, or_2_out,
       or_3_out, or_4_out, or_5_out, or_6_out, or_7_out, PE_ID, PE_ID_EX, PredictTaken_ID_EX,
       PredictTaken_IF, PredictTaken_IF_ID, RegWrite_EX_MEM_S, RegWrite_EX_MEM_V, RegWrite_ID,
       RegWrite_ID_EX_S, RegWrite_ID_EX_V, RegWrite_MEM_WB_S, RegWrite_MEM_WB_V, Reset_ID_EX, Reset_IF_ID,
       Stall, Stall_V, Taken_EX, Type_ID, Write_IF_ID;
  wire [1:0] ALUOp_ID, ALUOp_ID_EX_S, FwA_S, FwA_V, FwB_S, FwB_V, multiplexer_13_out, multiplexer_16_out,
       multiplexer_17_out, multiplexer_18_out, multiplexer_27_out, multiplexer_31_out, multiplexer_39_out,
       multiplexer_40_out, multiplexer_41_out, MUX_RegIn_EX_MEM_S, MUX_RegIn_EX_MEM_V, MUX_RegIn_ID,
       MUX_RegIn_ID_EX_S, MUX_RegIn_ID_EX_V, MUX_RegIn_MEM_WB_S, MUX_RegIn_MEM_WB_V, ra_ID, ra_ID_EX_S,
       ra_ID_EX_V, rb_ID_EX_S, rb_ID_EX_V, rd_EX_MEM_S, rd_EX_MEM_V, rd_ID_EX_S, rd_ID_EX_V, rd_MEM_WB_S,
       rd_MEM_WB_V;
  wire [3:0] Imm_ID, Imm_ID_EX_S, Imm_ID_EX_V, multiplexer_15_out, multiplexer_19_out, multiplexer_38_out,
       multiplexer_42_out, Opcode_ID_EX_S, Opcode_ID_EX_V;
  wire [7:0] adder_1_out, adder_2_out, Data_EX_MEM_S, Data_EX_MEM_V0, Data_EX_MEM_V1, Data_EX_MEM_V2,
       Data_EX_MEM_V3, Data_WB_S, Data_WB_V0, Data_WB_V1, Data_WB_V2, Data_WB_V3, Endereco_Corrigido,
       Endereco_Previsto_IF, Instrucao_IF, LImm_Ext_ID, LImm_Ext_ID_EX, MemDataOut_MEM_S, MemDataOut_MEM_V0,
       MemDataOut_MEM_V1, MemDataOut_MEM_V2, MemDataOut_MEM_V3, MemDataOut_MEM_WB_S, MemDataOut_MEM_WB_V0,
       MemDataOut_MEM_WB_V1, MemDataOut_MEM_WB_V2, MemDataOut_MEM_WB_V3, multiplexer_1_out,
       multiplexer_4_out, multiplexer_5_out, multiplexer_7_out, multiplexer_8_out, multiplexer_20_out,
       multiplexer_21_out, multiplexer_22_out, multiplexer_23_out, multiplexer_24_out, multiplexer_25_out,
       multiplexer_34_out, multiplexer_35_out, multiplexer_36_out, multiplexer_37_out, PC_Next, PC_Out_ID_EX,
       PC_Out_IF, PC_Out_IF_ID, R_ra_EX_MEM_S, R_ra_EX_MEM_V0, R_ra_EX_MEM_V1, R_ra_EX_MEM_V2,
       R_ra_EX_MEM_V3, R_ra_EX_S, R_ra_EX_V0, R_ra_EX_V1, R_ra_EX_V2, R_ra_EX_V3, R_ra_ID_EX_S,
       R_ra_ID_EX_V0, R_ra_ID_EX_V1, R_ra_ID_EX_V2, R_ra_ID_EX_V3, R_ra_ID_S, R_ra_ID_V0, R_ra_ID_V1,
       R_ra_ID_V2, R_ra_ID_V3, R_rb_EX_1_S, R_rb_EX_2_S, R_rb_EX_MEM_S, R_rb_EX_MEM_V0, R_rb_EX_MEM_V1,
       R_rb_EX_MEM_V2, R_rb_EX_MEM_V3, R_rb_EX_V0, R_rb_EX_V1, R_rb_EX_V2, R_rb_EX_V3, R_rb_ID_EX_S,
       R_rb_ID_EX_V0, R_rb_ID_EX_V1, R_rb_ID_EX_V2, R_rb_ID_EX_V3, R_rb_ID_S, R_rb_ID_V0, R_rb_ID_V1,
       R_rb_ID_V2, R_rb_ID_V3, R_rb_MEM_WB_S, Reg_Mv_EX_MEM_S, Reg_Mv_EX_MEM_V0, Reg_Mv_EX_MEM_V1,
       Reg_Mv_EX_MEM_V2, Reg_Mv_EX_MEM_V3, Reg_Mv_EX_S, Reg_Mv_EX_V0, Reg_Mv_EX_V1, Reg_Mv_EX_V2,
       Reg_Mv_EX_V3, Reg_Mv_MEM_WB_S, Reg_Mv_MEM_WB_V0, Reg_Mv_MEM_WB_V1, Reg_Mv_MEM_WB_V2, Reg_Mv_MEM_WB_V3,
       ULA_Out_EX_MEM_S, ULA_Out_EX_MEM_V0, ULA_Out_EX_MEM_V1, ULA_Out_EX_MEM_V2, ULA_Out_EX_MEM_V3,
       ULA_Out_EX_S, ULA_Out_EX_V0, ULA_Out_EX_V1, ULA_Out_EX_V2, ULA_Out_EX_V3, ULA_Out_MEM_WB_S,
       ULA_Out_MEM_WB_V0, ULA_Out_MEM_WB_V1, ULA_Out_MEM_WB_V2, ULA_Out_MEM_WB_V3;
  wire [7:4] Instrucao_IF_ID;

  BTB_e_Preditor btb_e_preditor_1 (
    .clk(clk_proc), .Reset(Reset), .Taken_EX(Taken_EX), .Branch_ID_EX(Branch_ID_EX), .R_rb(R_rb_EX_2_S),
    .PC_Out_ID_EX(PC_Out_ID_EX), .PC_Out_IF(PC_Out_IF), .PredictTaken(PredictTaken_IF),
    .Endereco_Previsto(Endereco_Previsto_IF));
  Adder adder_1 (.a(PC_Out_IF), .b(8'h1), .out(adder_1_out));  // open: cin, cout
  Multiplexer #(.width(8)) multiplexer_1 (
    .in0(adder_1_out), .in1(Endereco_Previsto_IF), .out(multiplexer_1_out), .sel(PredictTaken_IF));
  Multiplexer #(.width(8)) multiplexer_2 (
    .in0(multiplexer_1_out), .in1(Endereco_Corrigido), .out(PC_Next), .sel(Flush));
  Clock #(.phaseOffset(3)) clock_1 (.out(clk_mem));
  Clock #(.highDuration(2), .lowDuration(2), .phaseOffset(3)) clock_2 (.out(clk_proc));
  or or_1 (or_1_out, Flush, ~Stall);  // OR_Gate
  // DualRAM #(.asyncread("true"), .clearpin("true")) dualram_1: pin names not known; wires that end beside it: dualram_1_p1, PC_Out_IF, 1'b0, 1'b1, clk_mem, {8{1'b0}}, R_rb_EX_MEM_S, MemWrite_EX_MEM_S, 1'b1, clk_mem, R_ra_EX_MEM_S, Instrucao_IF, MemDataOut_MEM_S
  // Digital_Oscilloscope digital_oscilloscope_1: pin names not known; wires that end beside it: clk_mem, clk_proc
  Unidade_de_Reset unidade_de_reset_1 (
    .Flush(Flush), .Stall(Stall), .Reset(Reset), .Write_IF_ID(Write_IF_ID), .Reset_IF_ID(Reset_IF_ID),
    .Reset_ID_EX(Reset_ID_EX));
  PC pc_1 (.PC_In(PC_Next), .PCWrite(or_1_out), .clk(clk_proc), .Reset(Reset), .PC_Out(PC_Out_IF));
  Multiplexer multiplexer_3 (.in0(PredictTaken_IF), .in1(1'b0), .out(multiplexer_3_out), .sel(Reset_IF_ID));
  Multiplexer #(.width(8)) multiplexer_4 (.in0(PC_Out_IF), .in1({8{1'b0}}), .out(multiplexer_4_out), .sel(Reset_IF_ID));
  Multiplexer #(.width(8)) multiplexer_5 (.in0(Instrucao_IF), .in1(8'h40), .out(multiplexer_5_out), .sel(Reset_IF_ID));
  Register #(.width(1)) u_PredictTaken_IF_ID (
    .D(multiplexer_3_out), .en(Write_IF_ID), .Q(PredictTaken_IF_ID), .clk(clk_proc), .clr(Reset));
  Register u_PC_Out_IF_ID (.D(multiplexer_4_out), .en(Write_IF_ID), .Q(PC_Out_IF_ID), .clk(clk_proc), .clr(Reset));
  Register u_Instrucao_IF_ID (
    .D(multiplexer_5_out), .en(Write_IF_ID), .Q({Instrucao_IF_ID, Imm_ID}), .clk(clk_proc), .clr(Reset));
  assign LImm_Ext_ID = {{6{Imm_ID[1]}}, Imm_ID[1:0]};  // Bit_Extender bit_extender_1
  Unidade_de_Controle Controle (
    .Opcode(Instrucao_IF_ID), .AluOp(ALUOp_ID), .MUX_RegIn(MUX_RegIn_ID), .RegWrite(RegWrite_ID),
    .MemWrite(MemWrite_ID), .Type_Inst(Type_ID), .PE(PE_ID), .Branch(Branch_ID), .LI(LI_ID), .Move(Move_ID));
  Multiplexer #(.width(2)) multiplexer_6 (.in0(Imm_ID[3:2]), .in1(2'b01), .out(ra_ID), .sel(Type_ID));
  not not_1 (Stall_V, PE_ID);
  Hazard_Detectation_Unit hazard_detectation_unit_1 (
    .Opcode_ID_EX_S(Opcode_ID_EX_S), .ra_ID(ra_ID), .rd_ID_EX_S(rd_ID_EX_S), .rb_ID(Imm_ID[1:0]),
    .Opcode_ID_EX_V(Opcode_ID_EX_V), .rd_ID_EX_V(rd_ID_EX_V), .PE_ID(PE_ID), .PE_ID_EX(PE_ID_EX),
    .Opcode_ID(Instrucao_IF_ID), .Stall(Stall));
  Banco_de_Registradores_V3 banco_de_registradores_v3_1 (
    .clk(clk_mem), .RegIn(Data_WB_V3), .rd(rd_MEM_WB_V), .RegWrite(RegWrite_MEM_WB_V), .Reset(Reset),
    .ra(ra_ID), .rb(Imm_ID[1:0]), .R_ra(R_ra_ID_V3), .R_rb(R_rb_ID_V3));
  Banco_de_Registradores_V2 banco_de_registradores_v2_1 (
    .clk(clk_mem), .RegIn(Data_WB_V2), .rd(rd_MEM_WB_V), .RegWrite(RegWrite_MEM_WB_V), .Reset(Reset),
    .ra(ra_ID), .rb(Imm_ID[1:0]), .R_ra(R_ra_ID_V2), .R_rb(R_rb_ID_V2));
  Banco_de_Registradores_V1 banco_de_registradores_v1_1 (
    .clk(clk_mem), .RegIn(Data_WB_V1), .rd(rd_MEM_WB_V), .RegWrite(RegWrite_MEM_WB_V), .Reset(Reset),
    .ra(ra_ID), .rb(Imm_ID[1:0]), .R_ra(R_ra_ID_V1), .R_rb(R_rb_ID_V1));
  Banco_de_Registradores_V0 banco_de_registradores_v0_1 (
    .clk(clk_mem), .RegIn(Data_WB_V0), .rd(rd_MEM_WB_V), .RegWrite(RegWrite_MEM_WB_V), .Reset(Reset),
    .ra(ra_ID), .rb(Imm_ID[1:0]), .R_ra(R_ra_ID_V0), .R_rb(R_rb_ID_V0));
  Banco_de_Registradores_S banco_de_registradores_s_1 (
    .clk(clk_mem), .RegIn(Data_WB_S), .rd(rd_MEM_WB_S), .RegWrite(RegWrite_MEM_WB_S), .Reset(Reset),
    .ra(ra_ID), .rb(Imm_ID[1:0]), .R_ra(R_ra_ID_S), .R_rb(R_rb_ID_S));
  Multiplexer #(.width(8)) multiplexer_7 (.in0(R_ra_ID_V3), .in1({8{1'b0}}), .out(multiplexer_7_out), .sel(or_2_out));
  Multiplexer #(.width(8)) multiplexer_8 (.in0(R_rb_ID_V3), .in1({8{1'b0}}), .out(multiplexer_8_out), .sel(or_2_out));
  Multiplexer multiplexer_9 (.in0(RegWrite_ID), .in1(1'b0), .out(multiplexer_9_out), .sel(or_6_out));
  Multiplexer multiplexer_10 (.in0(ALUOp_ID[0]), .in1(1'b0), .out(multiplexer_10_out), .sel(or_7_out));
  Multiplexer multiplexer_11 (.in0(MemWrite_ID), .in1(1'b0), .out(multiplexer_11_out), .sel(or_7_out));
  Multiplexer multiplexer_12 (.in0(RegWrite_ID), .in1(1'b0), .out(multiplexer_12_out), .sel(or_7_out));
  Multiplexer #(.width(2)) multiplexer_13 (.in0(MUX_RegIn_ID), .in1(2'b00), .out(multiplexer_13_out), .sel(or_7_out));
  Multiplexer multiplexer_14 (.in0(Move_ID), .in1(1'b0), .out(multiplexer_14_out), .sel(or_7_out));
  Multiplexer #(.width(4)) multiplexer_15 (.in0(Imm_ID), .in1(4'b0000), .out(multiplexer_15_out), .sel(or_7_out));
  Multiplexer #(.width(2)) multiplexer_16 (.in0(ra_ID), .in1(2'b00), .out(multiplexer_16_out), .sel(or_7_out));
  Multiplexer #(.width(2)) multiplexer_17 (.in0(ra_ID), .in1(2'b00), .out(multiplexer_17_out), .sel(or_7_out));
  Multiplexer #(.width(2)) multiplexer_18 (.in0(Imm_ID[1:0]), .in1(2'b00), .out(multiplexer_18_out), .sel(or_7_out));
  Multiplexer #(.width(4)) multiplexer_19 (
    .in0(Instrucao_IF_ID), .in1(4'b0000), .out(multiplexer_19_out), .sel(or_7_out));
  Multiplexer #(.width(8)) multiplexer_20 (.in0(R_ra_ID_V2), .in1({8{1'b0}}), .out(multiplexer_20_out), .sel(or_3_out));
  Multiplexer #(.width(8)) multiplexer_21 (.in0(R_rb_ID_V2), .in1({8{1'b0}}), .out(multiplexer_21_out), .sel(or_3_out));
  Multiplexer #(.width(8)) multiplexer_22 (.in0(R_ra_ID_V1), .in1({8{1'b0}}), .out(multiplexer_22_out), .sel(or_4_out));
  Multiplexer #(.width(8)) multiplexer_23 (.in0(R_rb_ID_V1), .in1({8{1'b0}}), .out(multiplexer_23_out), .sel(or_4_out));
  Multiplexer #(.width(8)) multiplexer_24 (.in0(R_ra_ID_V0), .in1({8{1'b0}}), .out(multiplexer_24_out), .sel(or_5_out));
  Multiplexer #(.width(8)) multiplexer_25 (.in0(R_rb_ID_V0), .in1({8{1'b0}}), .out(multiplexer_25_out), .sel(or_5_out));
  Multiplexer multiplexer_26 (.in0(PE_ID), .in1(1'b1), .out(multiplexer_26_out), .sel(or_6_out));
  Multiplexer #(.width(2)) multiplexer_27 (.in0(ALUOp_ID), .in1(2'b00), .out(multiplexer_27_out), .sel(or_6_out));
  Multiplexer multiplexer_28 (.in0(Branch_ID), .in1(1'b0), .out(multiplexer_28_out), .sel(or_6_out));
  Multiplexer multiplexer_29 (.in0(LI_ID), .in1(1'b0), .out(multiplexer_29_out), .sel(or_6_out));
  Multiplexer multiplexer_30 (.in0(MemWrite_ID), .in1(1'b0), .out(multiplexer_30_out), .sel(or_6_out));
  Multiplexer #(.width(2)) multiplexer_31 (.in0(MUX_RegIn_ID), .in1(2'b00), .out(multiplexer_31_out), .sel(or_6_out));
  Multiplexer multiplexer_32 (.in0(Move_ID), .in1(1'b0), .out(multiplexer_32_out), .sel(or_6_out));
  Multiplexer multiplexer_33 (.in0(PredictTaken_IF_ID), .in1(1'b0), .out(multiplexer_33_out), .sel(or_6_out));
  Multiplexer #(.width(8)) multiplexer_34 (
    .in0(PC_Out_IF_ID), .in1({8{1'b0}}), .out(multiplexer_34_out), .sel(or_6_out));
  Multiplexer #(.width(8)) multiplexer_35 (.in0(R_ra_ID_S), .in1({8{1'b0}}), .out(multiplexer_35_out), .sel(or_6_out));
  Multiplexer #(.width(8)) multiplexer_36 (.in0(R_rb_ID_S), .in1({8{1'b0}}), .out(multiplexer_36_out), .sel(or_6_out));
  Multiplexer #(.width(8)) multiplexer_37 (
    .in0(LImm_Ext_ID), .in1({8{1'b0}}), .out(multiplexer_37_out), .sel(or_6_out));
  Multiplexer #(.width(4)) multiplexer_38 (.in0(Imm_ID), .in1(4'b0000), .out(multiplexer_38_out), .sel(or_6_out));
  Multiplexer #(.width(2)) multiplexer_39 (.in0(ra_ID), .in1(2'b00), .out(multiplexer_39_out), .sel(or_6_out));
  Multiplexer #(.width(2)) multiplexer_40 (.in0(ra_ID), .in1(2'b00), .out(multiplexer_40_out), .sel(or_6_out));
  Multiplexer #(.width(2)) multiplexer_41 (.in0(Imm_ID[1:0]), .in1(2'b00), .out(multiplexer_41_out), .sel(or_6_out));
  Multiplexer #(.width(4)) multiplexer_42 (
    .in0(Instrucao_IF_ID), .in1(4'b0100), .out(multiplexer_42_out), .sel(or_6_out));
  Register register_1 (.D(multiplexer_7_out), .Q(R_ra_ID_EX_V3), .clk(clk_proc), .clr(Reset));  // open: en
  Register register_2 (.D(multiplexer_8_out), .Q(R_rb_ID_EX_V3), .clk(clk_proc), .clr(Reset));  // open: en
  Register register_3 (.D(multiplexer_20_out), .Q(R_ra_ID_EX_V2), .clk(clk_proc), .clr(Reset));  // open: en
  Register register_4 (.D(multiplexer_21_out), .Q(R_rb_ID_EX_V2), .clk(clk_proc), .clr(Reset));  // open: en
  Register register_5 (.D(multiplexer_22_out), .Q(R_ra_ID_EX_V1), .clk(clk_proc), .clr(Reset));  // open: en
  Register register_6 (.D(multiplexer_23_out), .Q(R_rb_ID_EX_V1), .clk(clk_proc), .clr(Reset));  // open: en
  Register u_R_ra_ID_EX_V0 (.D(multiplexer_24_out), .Q(R_ra_ID_EX_V0), .clk(clk_proc), .clr(Reset));  // open: en
  Register u_R_rb_ID_EX_V0 (.D(multiplexer_25_out), .Q(R_rb_ID_EX_V0), .clk(clk_proc), .clr(Reset));  // open: en
  Register #(.width(1)) u_PE_ID_EX (.D(multiplexer_26_out), .Q(PE_ID_EX), .clk(clk_proc), .clr(Reset));  // open: en
  Register #(.width(2)) u_ALUop_ID_EX_S (
    .D(multiplexer_27_out), .Q(ALUOp_ID_EX_S), .clk(clk_proc), .clr(Reset));  // open: en
  Register #(.width(1)) u_Branch_ID_EX (
    .D(multiplexer_28_out), .Q(Branch_ID_EX), .clk(clk_proc), .clr(Reset));  // open: en
  Register #(.width(1)) u_LI_ID_EX (.D(multiplexer_29_out), .Q(LI_ID_EX), .clk(clk_proc), .clr(Reset));  // open: en
  Register #(.width(1)) u_MemWrite_ID_EX_S (
    .D(multiplexer_30_out), .Q(MemWrite_ID_EX_S), .clk(clk_proc), .clr(Reset));  // open: en
  Register #(.width(1)) u_RegWrite_ID_EX_S (
    .D(multiplexer_9_out), .Q(RegWrite_ID_EX_S), .clk(clk_proc), .clr(Reset));  // open: en
  Register #(.width(2)) u_MUX_RegIn_ID_EX_S (
    .D(multiplexer_31_out), .Q(MUX_RegIn_ID_EX_S), .clk(clk_proc), .clr(Reset));  // open: en
  Register #(.width(1)) u_Move_ID_EX_S (
    .D(multiplexer_32_out), .Q(Move_ID_EX_S), .clk(clk_proc), .clr(Reset));  // open: en
  Register #(.width(1)) u_PredictTaken_ID_EX (
    .D(multiplexer_33_out), .Q(PredictTaken_ID_EX), .clk(clk_proc), .clr(Reset));  // open: en
  Register u_PC_Out_ID_EX (.D(multiplexer_34_out), .Q(PC_Out_ID_EX), .clk(clk_proc), .clr(Reset));  // open: en
  Register u_R_ra_ID_EX_S (.D(multiplexer_35_out), .Q(R_ra_ID_EX_S), .clk(clk_proc), .clr(Reset));  // open: en
  Register u_R_rb_ID_EX_S (.D(multiplexer_36_out), .Q(R_rb_ID_EX_S), .clk(clk_proc), .clr(Reset));  // open: en
  Register u_LImm_Ext_ID_EX (.D(multiplexer_37_out), .Q(LImm_Ext_ID_EX), .clk(clk_proc), .clr(Reset));  // open: en
  Register #(.width(4)) u_Imm_ID_EX_S (
    .D(multiplexer_38_out), .Q(Imm_ID_EX_S), .clk(clk_proc), .clr(Reset));  // open: en
  Register #(.width(2)) u_rd_ID_EX_S (.D(multiplexer_39_out), .Q(rd_ID_EX_S), .clk(clk_proc), .clr(Reset));  // open: en
  Register #(.width(2)) u_ra_ID_EX_S (.D(multiplexer_40_out), .Q(ra_ID_EX_S), .clk(clk_proc), .clr(Reset));  // open: en
  Register #(.width(2)) u_rb_ID_EX_S (.D(multiplexer_41_out), .Q(rb_ID_EX_S), .clk(clk_proc), .clr(Reset));  // open: en
  Register #(.width(4)) u_Opcode_ID_EX_S (
    .D(multiplexer_42_out), .Q(Opcode_ID_EX_S), .clk(clk_proc), .clr(Reset));  // open: en
  Register #(.width(1)) u_ALUOp_ID_EX_V (
    .D(multiplexer_10_out), .Q(ALUOp_ID_EX_V), .clk(clk_proc), .clr(Reset));  // open: en
  Register #(.width(1)) u_MemWrite_ID_EX_V (
    .D(multiplexer_11_out), .Q(MemWrite_ID_EX_V), .clk(clk_proc), .clr(Reset));  // open: en
  Register #(.width(1)) u_RegWrite_ID_EX_V (
    .D(multiplexer_12_out), .Q(RegWrite_ID_EX_V), .clk(clk_proc), .clr(Reset));  // open: en
  Register #(.width(2)) u_MUX_RegIn_ID_EX_V (
    .D(multiplexer_13_out), .Q(MUX_RegIn_ID_EX_V), .clk(clk_proc), .clr(Reset));  // open: en
  Register #(.width(1)) u_Move_ID_EX_V (
    .D(multiplexer_14_out), .Q(Move_ID_EX_V), .clk(clk_proc), .clr(Reset));  // open: en
  Register #(.width(4)) u_Imm_ID_EX_V (
    .D(multiplexer_15_out), .Q(Imm_ID_EX_V), .clk(clk_proc), .clr(Reset));  // open: en
  Register #(.width(2)) u_rd_ID_EX_V (.D(multiplexer_16_out), .Q(rd_ID_EX_V), .clk(clk_proc), .clr(Reset));  // open: en
  Register #(.width(2)) u_ra_ID_EX_V (.D(multiplexer_17_out), .Q(ra_ID_EX_V), .clk(clk_proc));  // open: en, clr
  Register #(.width(2)) u_rb_ID_EX_V (.D(multiplexer_18_out), .Q(rb_ID_EX_V), .clk(clk_proc));  // open: en, clr
  Register #(.width(4)) u_Opcode_ID_EX_V (
    .D(multiplexer_19_out), .Q(Opcode_ID_EX_V), .clk(clk_proc), .clr(Reset));  // open: en
  or or_2 (or_2_out, Reset_ID_EX, Stall_V);
  or or_3 (or_3_out, Reset_ID_EX, Stall_V);
  or or_4 (or_4_out, Reset_ID_EX, Stall_V);
  or or_5 (or_5_out, Reset_ID_EX, Stall_V);
  or or_6 (or_6_out, Reset_ID_EX, PE_ID);
  or or_7 (or_7_out, Reset_ID_EX, Stall_V);
  Unidade_Forwarding_S unidade_forwarding_s_1 (
    .ra_ID_EX(ra_ID_EX_S), .rb_ID_EX(rb_ID_EX_S), .rd_MEM(rd_EX_MEM_S), .rd_WB(rd_MEM_WB_S),
    .RegWrite_EX_MEM(RegWrite_EX_MEM_S), .RegWrite_MEM_WB(RegWrite_MEM_WB_S), .Opcode_ID_EX(Opcode_ID_EX_S),
    .ULA_Out_EX_MEM(ULA_Out_EX_MEM_S), .Reg_mv_EX_MEM(Reg_Mv_EX_MEM_S), .R_rb_EX_MEM(R_rb_EX_MEM_S),
    .MUX_RegIn_EX_MEM(MUX_RegIn_EX_MEM_S), .FwA(FwA_S), .FwB(FwB_S), .Data_EX_MEM(Data_EX_MEM_S));
  Unidade_Forwarding_V unidade_forwarding_v_1 (
    .ra_ID_EX(ra_ID_EX_V), .rb_ID_EX(rb_ID_EX_V), .rd_MEM(rd_EX_MEM_V), .rd_WB(rd_MEM_WB_V),
    .RegWrite_EX_MEM(RegWrite_EX_MEM_V), .RegWrite_MEM_WB(RegWrite_MEM_WB_V), .Opcode_ID_EX(Opcode_ID_EX_V),
    .FwA(FwA_V), .FwB(FwB_V));
  Multiplexer #(.width(8)) multiplexer_43 (.in0(R_rb_ID_EX_S), .in1(LImm_Ext_ID_EX), .out(R_rb_EX_1_S), .sel(LI_ID_EX));
  Multiplexer #(.width(8)) multiplexer_44 (
    .in0(ULA_Out_EX_MEM_V3), .in1(Reg_Mv_EX_MEM_V3), .out(Data_EX_MEM_V3), .sel(MUX_RegIn_EX_MEM_V[1]));
  Multiplexer #(.width(8)) multiplexer_45 (
    .in0(ULA_Out_EX_MEM_V2), .in1(Reg_Mv_EX_MEM_V2), .out(Data_EX_MEM_V2), .sel(MUX_RegIn_EX_MEM_V[1]));
  Multiplexer #(.width(8)) multiplexer_46 (
    .in0(ULA_Out_EX_MEM_V1), .in1(Reg_Mv_EX_MEM_V1), .out(Data_EX_MEM_V1), .sel(MUX_RegIn_EX_MEM_V[1]));
  Multiplexer #(.width(8)) multiplexer_47 (
    .in0(ULA_Out_EX_MEM_V0), .in1(Reg_Mv_EX_MEM_V0), .out(Data_EX_MEM_V0), .sel(MUX_RegIn_EX_MEM_V[1]));
  Multiplexer #(.select(2), .width(8)) multiplexer_48 (
    .in0(R_ra_ID_EX_S), .in1(Data_EX_MEM_S), .in2(Data_WB_S), .out(R_ra_EX_S), .sel(FwA_S));  // open: in3
  Multiplexer #(.select(2), .width(8)) multiplexer_49 (
    .in0(R_rb_EX_1_S), .in1(Data_EX_MEM_S), .in2(Data_WB_S), .out(R_rb_EX_2_S), .sel(FwB_S));  // open: in3
  Multiplexer #(.select(2), .width(8)) multiplexer_50 (
    .in0(R_ra_ID_EX_V3), .in1(Data_EX_MEM_V3), .in2(Data_WB_V3), .out(R_ra_EX_V3), .sel(FwA_V));  // open: in3
  Multiplexer #(.select(2), .width(8)) multiplexer_51 (
    .in0(R_rb_ID_EX_V3), .in1(Data_EX_MEM_V3), .in2(Data_WB_V3), .out(R_rb_EX_V3), .sel(FwB_V));  // open: in3
  Multiplexer #(.select(2), .width(8)) multiplexer_52 (
    .in0(R_ra_ID_EX_V2), .in1(Data_EX_MEM_V2), .in2(Data_WB_V2), .out(R_ra_EX_V2), .sel(FwA_V));  // open: in3
  Multiplexer #(.select(2), .width(8)) multiplexer_53 (
    .in0(R_rb_ID_EX_V2), .in1(Data_EX_MEM_V2), .in2(Data_WB_V2), .out(R_rb_EX_V2), .sel(FwB_V));  // open: in3
  Multiplexer #(.select(2), .width(8)) multiplexer_54 (
    .in0(R_ra_ID_EX_V1), .in1(Data_EX_MEM_V1), .in2(Data_WB_V1), .out(R_ra_EX_V1), .sel(FwA_V));  // open: in3
  Multiplexer #(.select(2), .width(8)) multiplexer_55 (
    .in0(R_rb_ID_EX_V1), .in1(Data_EX_MEM_V1), .in2(Data_WB_V1), .out(R_rb_EX_V1), .sel(FwB_V));  // open: in3
  Multiplexer #(.select(2), .width(8)) multiplexer_56 (
    .in0(R_ra_ID_EX_V0), .in1(Data_EX_MEM_V0), .in2(Data_WB_V0), .out(R_ra_EX_V0), .sel(FwA_V));  // open: in3
  Multiplexer #(.select(2), .width(8)) multiplexer_57 (
    .in0(R_rb_ID_EX_V0), .in1(Data_EX_MEM_V0), .in2(Data_WB_V0), .out(R_rb_EX_V0), .sel(FwB_V));  // open: in3
  Branch_Control branch_control_1 (.Branch(Branch_ID_EX), .R_ra(R_ra_EX_S), .Taken(Taken_EX));
  ULA_S ula_s_1 (.ULA_A(R_ra_EX_S), .ULA_B(R_rb_EX_2_S), .ALUOp(ALUOp_ID_EX_S), .ULA_Out(ULA_Out_EX_S));
  Juntador juntador_1 (.R_ra(R_ra_EX_S), .Imm(Imm_ID_EX_S), .Move(Move_ID_EX_S), .Reg_Moved(Reg_Mv_EX_S));
  Adder adder_2 (.a(8'h1), .b(PC_Out_ID_EX), .out(adder_2_out));  // open: cin, cout
  ULA_V ula_v_1 (.ULA_A(R_ra_EX_V3), .ULA_B(R_rb_EX_V3), .ALUOp(ALUOp_ID_EX_V), .ULA_OUT(ULA_Out_EX_V3));
  Juntador juntador_2 (.R_ra(R_ra_EX_V3), .Imm(Imm_ID_EX_V), .Move(Move_ID_EX_V), .Reg_Moved(Reg_Mv_EX_V3));
  ULA_V ula_v_2 (.ULA_A(R_ra_EX_V2), .ULA_B(R_rb_EX_V2), .ALUOp(ALUOp_ID_EX_V), .ULA_OUT(ULA_Out_EX_V2));
  Juntador juntador_3 (.R_ra(R_ra_EX_V2), .Imm(Imm_ID_EX_V), .Move(Move_ID_EX_V), .Reg_Moved(Reg_Mv_EX_V2));
  ULA_V ula_v_3 (.ULA_A(R_ra_EX_V1), .ULA_B(R_rb_EX_V1), .ALUOp(ALUOp_ID_EX_V), .ULA_OUT(ULA_Out_EX_V1));
  Juntador juntador_4 (.R_ra(R_ra_EX_V1), .Imm(Imm_ID_EX_V), .Move(Move_ID_EX_V), .Reg_Moved(Reg_Mv_EX_V1));
  ULA_V ula_v_4 (.ULA_A(R_ra_EX_V0), .ULA_B(R_rb_EX_V0), .ALUOp(ALUOp_ID_EX_V), .ULA_OUT(ULA_Out_EX_V0));
  Juntador juntador_5 (.R_ra(R_ra_EX_V0), .Imm(Imm_ID_EX_V), .Move(Move_ID_EX_V), .Reg_Moved(Reg_Mv_EX_V0));
  Multiplexer #(.width(8)) multiplexer_58 (
    .in0(adder_2_out), .in1(R_rb_EX_2_S), .out(Endereco_Corrigido), .sel(Taken_EX));
  xor xor_1 (Flush, PredictTaken_ID_EX, Taken_EX);
  Register #(.width(2)) register_7 (.D(rd_ID_EX_V), .Q(rd_EX_MEM_V), .clk(clk_proc), .clr(Reset));  // open: en
  Register #(.width(1)) register_8 (
    .D(MemWrite_ID_EX_V), .Q(MemWrite_EX_MEM_V), .clk(clk_proc), .clr(Reset));  // open: en
  Register #(.width(1)) register_9 (
    .D(RegWrite_ID_EX_V), .Q(RegWrite_EX_MEM_V), .clk(clk_proc), .clr(Reset));  // open: en
  Register #(.width(2)) register_10 (
    .D(MUX_RegIn_ID_EX_V), .Q(MUX_RegIn_EX_MEM_V), .clk(clk_proc), .clr(Reset));  // open: en
  Register register_11 (.D(ULA_Out_EX_V3), .Q(ULA_Out_EX_MEM_V3), .clk(clk_proc), .clr(Reset));  // open: en
  Register register_12 (.D(R_ra_EX_V3), .Q(R_ra_EX_MEM_V3), .clk(clk_proc), .clr(Reset));  // open: en
  Register register_13 (.D(R_rb_EX_V3), .Q(R_rb_EX_MEM_V3), .clk(clk_proc), .clr(Reset));  // open: en
  Register register_14 (.D(Reg_Mv_EX_V3), .Q(Reg_Mv_EX_MEM_V3), .clk(clk_proc), .clr(Reset));  // open: en
  Register register_15 (.D(ULA_Out_EX_V2), .Q(ULA_Out_EX_MEM_V2), .clk(clk_proc), .clr(Reset));  // open: en
  Register register_16 (.D(R_ra_EX_V2), .Q(R_ra_EX_MEM_V2), .clk(clk_proc), .clr(Reset));  // open: en
  Register register_17 (.D(R_rb_EX_V2), .Q(R_rb_EX_MEM_V2), .clk(clk_proc), .clr(Reset));  // open: en
  Register register_18 (.D(Reg_Mv_EX_V2), .Q(Reg_Mv_EX_MEM_V2), .clk(clk_proc), .clr(Reset));  // open: en
  Register register_19 (.D(ULA_Out_EX_V1), .Q(ULA_Out_EX_MEM_V1), .clk(clk_proc), .clr(Reset));  // open: en
  Register register_20 (.D(R_ra_EX_V1), .Q(R_ra_EX_MEM_V1), .clk(clk_proc), .clr(Reset));  // open: en
  Register register_21 (.D(R_rb_EX_V1), .Q(R_rb_EX_MEM_V1), .clk(clk_proc), .clr(Reset));  // open: en
  Register register_22 (.D(Reg_Mv_EX_V1), .Q(Reg_Mv_EX_MEM_V1), .clk(clk_proc), .clr(Reset));  // open: en
  Register register_23 (.D(ULA_Out_EX_V0), .Q(ULA_Out_EX_MEM_V0), .clk(clk_proc), .clr(Reset));  // open: en
  Register register_24 (.D(R_ra_EX_V0), .Q(R_ra_EX_MEM_V0), .clk(clk_proc), .clr(Reset));  // open: en
  Register register_25 (.D(R_rb_EX_V0), .Q(R_rb_EX_MEM_V0), .clk(clk_proc), .clr(Reset));  // open: en
  Register register_26 (.D(Reg_Mv_EX_V0), .Q(Reg_Mv_EX_MEM_V0), .clk(clk_proc), .clr(Reset));  // open: en
  Register u_ULA_Out_EX_MEM_S (.D(ULA_Out_EX_S), .Q(ULA_Out_EX_MEM_S), .clk(clk_proc), .clr(Reset));  // open: en
  Register u_R_ra_EX_MEM_S (.D(R_ra_EX_S), .Q(R_ra_EX_MEM_S), .clk(clk_proc), .clr(Reset));  // open: en
  Register u_R_rb_EX_MEM_S (.D(R_rb_EX_2_S), .Q(R_rb_EX_MEM_S), .clk(clk_proc), .clr(Reset));  // open: en
  Register #(.width(2)) u_rd_EX_MEM_S (.D(rd_ID_EX_S), .Q(rd_EX_MEM_S), .clk(clk_proc), .clr(Reset));  // open: en
  Register u_Reg_Mv_EX_MEM_S (.D(Reg_Mv_EX_S), .Q(Reg_Mv_EX_MEM_S), .clk(clk_proc), .clr(Reset));  // open: en
  Register #(.width(1)) u_MemWrite_EX_MEM_S (
    .D(MemWrite_ID_EX_S), .Q(MemWrite_EX_MEM_S), .clk(clk_proc), .clr(Reset));  // open: en
  Register #(.width(1)) u_RegWrite_EX_MEM_S (
    .D(RegWrite_ID_EX_S), .Q(RegWrite_EX_MEM_S), .clk(clk_proc), .clr(Reset));  // open: en
  Register #(.width(2)) u_MUX_RegIn_EX_MEM_S (
    .D(MUX_RegIn_ID_EX_S), .Q(MUX_RegIn_EX_MEM_S), .clk(clk_proc), .clr(Reset));  // open: en
  Clock #(.phaseOffset(3)) clock_3 (.out(clk_mem));
  Clock #(.highDuration(2), .lowDuration(2), .phaseOffset(3)) clock_4 (.out(clk_proc));
  Clock #(.phaseOffset(3)) clock_5 (.out(clk_mem));
  Clock #(.highDuration(2), .lowDuration(2), .phaseOffset(3)) clock_6 (.out(clk_proc));
  Clock #(.phaseOffset(3)) clock_7 (.out(clk_mem));
  Clock #(.highDuration(2), .lowDuration(2), .phaseOffset(3)) clock_8 (.out(clk_proc));
  Clock #(.phaseOffset(3)) clock_9 (.out(clk_mem));
  Clock #(.highDuration(2), .lowDuration(2), .phaseOffset(3)) clock_10 (.out(clk_proc));
  Clock #(.phaseOffset(3)) u_clk_mem (.out(clk_mem));
  Clock #(.highDuration(2), .lowDuration(2), .phaseOffset(3)) clk_processador (.out(clk_proc));
  RAM #(.clearpin("true")) RAM_V3 (
    .addr(R_rb_EX_MEM_V3), .we(MemWrite_EX_MEM_V), .oe(1'b1), .clk(clk_mem), .din(R_ra_EX_MEM_V3),
    .dout(MemDataOut_MEM_V3), .clr(Reset));
  // Digital_Oscilloscope digital_oscilloscope_2: pin names not known; wires that end beside it: clk_mem, clk_proc
  // Digital_Oscilloscope digital_oscilloscope_3: pin names not known; wires that end beside it: clk_mem, clk_proc
  // Digital_Oscilloscope digital_oscilloscope_4: pin names not known; wires that end beside it: clk_mem, clk_proc
  RAM #(.clearpin("true")) RAM_V2 (
    .addr(R_rb_EX_MEM_V2), .we(MemWrite_EX_MEM_V), .oe(1'b1), .clk(clk_mem), .din(R_ra_EX_MEM_V2),
    .dout(MemDataOut_MEM_V2), .clr(Reset));
  RAM #(.clearpin("true")) RAM_V1 (
    .addr(R_rb_EX_MEM_V1), .we(MemWrite_EX_MEM_V), .oe(1'b1), .clk(clk_mem), .din(R_ra_EX_MEM_V1),
    .dout(MemDataOut_MEM_V1), .clr(Reset));
  // Digital_Oscilloscope digital_oscilloscope_5: pin names not known; wires that end beside it: clk_mem, clk_proc
  RAM #(.clearpin("true")) RAM_V0 (
    .addr(R_rb_EX_MEM_V0), .we(MemWrite_EX_MEM_V), .oe(1'b1), .clk(clk_mem), .din(R_ra_EX_MEM_V0),
    .dout(MemDataOut_MEM_V0), .clr(Reset));
  // Digital_Oscilloscope digital_oscilloscope_6: pin names not known; wires that end beside it: clk_mem, clk_proc
  Register #(.width(1)) register_27 (
    .D(RegWrite_EX_MEM_V), .Q(RegWrite_MEM_WB_V), .clk(clk_proc), .clr(Reset));  // open: en
  Register #(.width(2)) register_28 (
    .D(MUX_RegIn_EX_MEM_V), .Q(MUX_RegIn_MEM_WB_V), .clk(clk_proc), .clr(Reset));  // open: en
  Register #(.width(2)) register_29 (.D(rd_EX_MEM_V), .Q(rd_MEM_WB_V), .clk(clk_proc), .clr(Reset));  // open: en
  Register register_30 (.D(ULA_Out_EX_MEM_V3), .Q(ULA_Out_MEM_WB_V3), .clk(clk_proc), .clr(Reset));  // open: en
  Register register_31 (.D(MemDataOut_MEM_V3), .Q(MemDataOut_MEM_WB_V3), .clk(clk_proc), .clr(Reset));  // open: en
  Register register_32 (.D(Reg_Mv_EX_MEM_V3), .Q(Reg_Mv_MEM_WB_V3), .clk(clk_proc), .clr(Reset));  // open: en
  Register register_33 (.D(ULA_Out_EX_MEM_V2), .Q(ULA_Out_MEM_WB_V2), .clk(clk_proc), .clr(Reset));  // open: en
  Register register_34 (.D(MemDataOut_MEM_V2), .Q(MemDataOut_MEM_WB_V2), .clk(clk_proc), .clr(Reset));  // open: en
  Register register_35 (.D(Reg_Mv_EX_MEM_V2), .Q(Reg_Mv_MEM_WB_V2), .clk(clk_proc), .clr(Reset));  // open: en
  Register register_36 (.D(ULA_Out_EX_MEM_V1), .Q(ULA_Out_MEM_WB_V1), .clk(clk_proc), .clr(Reset));  // open: en
  Register register_37 (.D(MemDataOut_MEM_V1), .Q(MemDataOut_MEM_WB_V1), .clk(clk_proc), .clr(Reset));  // open: en
  Register register_38 (.D(Reg_Mv_EX_MEM_V1), .Q(Reg_Mv_MEM_WB_V1), .clk(clk_proc), .clr(Reset));  // open: en
  Register register_39 (.D(ULA_Out_EX_MEM_V0), .Q(ULA_Out_MEM_WB_V0), .clk(clk_proc), .clr(Reset));  // open: en
  Register register_40 (.D(MemDataOut_MEM_V0), .Q(MemDataOut_MEM_WB_V0), .clk(clk_proc), .clr(Reset));  // open: en
  Register register_41 (.D(Reg_Mv_EX_MEM_V0), .Q(Reg_Mv_MEM_WB_V0), .clk(clk_proc), .clr(Reset));  // open: en
  Register #(.width(1)) u_RegWrite_MEM_WB_S (
    .D(RegWrite_EX_MEM_S), .Q(RegWrite_MEM_WB_S), .clk(clk_proc), .clr(Reset));  // open: en
  Register #(.width(2)) u_MUX_RegIn_MEM_WB_S (
    .D(MUX_RegIn_EX_MEM_S), .Q(MUX_RegIn_MEM_WB_S), .clk(clk_proc), .clr(Reset));  // open: en
  Register u_ULA_Out_MEM_WB_S (.D(ULA_Out_EX_MEM_S), .Q(ULA_Out_MEM_WB_S), .clk(clk_proc), .clr(Reset));  // open: en
  Register u_MemDataOut_MEM_WB_S (
    .D(MemDataOut_MEM_S), .Q(MemDataOut_MEM_WB_S), .clk(clk_proc), .clr(Reset));  // open: en
  Register u_Reg_Mv_MEM_WB_S (.D(Reg_Mv_EX_MEM_S), .Q(Reg_Mv_MEM_WB_S), .clk(clk_proc), .clr(Reset));  // open: en
  Register u_R_rb_MEM_WB_S (.D(R_rb_EX_MEM_S), .Q(R_rb_MEM_WB_S), .clk(clk_proc), .clr(Reset));  // open: en
  Register #(.width(2)) u_rd_MEM_WB_S (.D(rd_EX_MEM_S), .Q(rd_MEM_WB_S), .clk(clk_proc), .clr(Reset));  // open: en
  Multiplexer #(.select(2), .width(8)) multiplexer_59 (
    .in0(ULA_Out_MEM_WB_V3), .in1(MemDataOut_MEM_WB_V3), .in2(Reg_Mv_MEM_WB_V3), .out(Data_WB_V3),
    .sel(MUX_RegIn_MEM_WB_V));  // open: in3
  Multiplexer #(.select(2), .width(8)) multiplexer_60 (
    .in0(ULA_Out_MEM_WB_V2), .in1(MemDataOut_MEM_WB_V2), .in2(Reg_Mv_MEM_WB_V2), .out(Data_WB_V2),
    .sel(MUX_RegIn_MEM_WB_V));  // open: in3
  Multiplexer #(.select(2), .width(8)) multiplexer_61 (
    .in0(ULA_Out_MEM_WB_V1), .in1(MemDataOut_MEM_WB_V1), .in2(Reg_Mv_MEM_WB_V1), .out(Data_WB_V1),
    .sel(MUX_RegIn_MEM_WB_V));  // open: in3
  Multiplexer #(.select(2), .width(8)) multiplexer_62 (
    .in0(ULA_Out_MEM_WB_V0), .in1(MemDataOut_MEM_WB_V0), .in2(Reg_Mv_MEM_WB_V0), .out(Data_WB_V0),
    .sel(MUX_RegIn_MEM_WB_V));  // open: in3
  Multiplexer #(.select(2), .width(8)) multiplexer_63 (
    .in0(ULA_Out_MEM_WB_S), .in1(MemDataOut_MEM_WB_S), .in2(Reg_Mv_MEM_WB_S), .in3(R_rb_MEM_WB_S),
    .out(Data_WB_S), .sel(MUX_RegIn_MEM_WB_S));

  // Other names for the same wires on the sheet: ALUOp_ID_S[1:0] = ALUOp_ID; ALUOp_ID_V = ALUOp_ID[0];
  //   Instrucao_IF_ID[3:0] = Imm_ID; rb_ID[1:0] = Imm_ID[1:0]; ra[1:0] = Imm_ID[3:2];
  //   Opcode_ID[3:0] = Instrucao_IF_ID; Stall_S = PE_ID

  // Notes on the sheet:
  //   Cálculo de PC_Next: PC + 1 ou Endereço Previsto ou Correção de Salto
  //   I. FETCH (IF)
  //   Memória de Instruções
  //   Memória de Dados
  //   IF/ID
  //   É Move?
  //   Se for, ra e rd igual a 1
  //   I. DECODE (ID)
  //   ID/EX
  //   ID/EX
  //   ID/EX
  //   FORWARDING
  //   Dado é adiantado? Daonde?
  //   Dado é adiantado? Daonde?
  //   Dado é adiantado? Daonde?
  //   Dado é adiantado? Daonde?
  //   Dado é adiantado? Daonde?
  //   EXECUTE (EX)
  //   EXECUTE (EX)
  //   Previção Certa?
  //   EX/MEM
  //   EX/MEM
  //   EX/MEM
  //   MemWrite_EX_MEM_S
  //   R_rb_EX_MEM_S
  //   1
  //   R_ra_EX_MEM_S
  //   A
  //   WE
  //   LE
  //   D
  //   MEMORY (MEM)
  //   MEMORY (MEM)
  //   Memória de
  //   Dados
  //   clk_mem
  //   D
  //   MemDataOut_MEM_S
  //   MEM/WB
  //   MEM/WB
  //   MEM/WB
  //   WRITE BACK (WB)
  //   WRITE BACK (WB)
  //   VPE3
  //   VPE2
  //   VPE1
  //   VPE0
  //   SPE
endmodule

module Banco_de_Registradores_S (
  input  clk,
  input  [7:0] RegIn,
  input  [1:0] rd,
  input  RegWrite,
  input  Reset,
  input  [1:0] ra,
  input  [1:0] rb,
  output [7:0] R_ra,
  output [7:0] R_rb
);

  wire [7:0] registradores_s_1_r_r0, registradores_s_1_r_r1, registradores_s_1_r_r2, registradores_s_1_r_r3;

  Registradores_S registradores_s_1 (
    .Reset(Reset), .RegWrite(RegWrite), .rd(rd), .RegIn(RegIn), .clk(clk), .R_r0(registradores_s_1_r_r0),
    .R_r1(registradores_s_1_r_r1), .R_r2(registradores_s_1_r_r2), .R_r3(registradores_s_1_r_r3));
  Multiplexer #(.select(2), .width(8)) multiplexer_1 (
    .in0(registradores_s_1_r_r0), .in1(registradores_s_1_r_r1), .in2(registradores_s_1_r_r2),
    .in3(registradores_s_1_r_r3), .out(R_ra), .sel(ra));
  Multiplexer #(.select(2), .width(8)) multiplexer_2 (
    .in0(registradores_s_1_r_r0), .in1(registradores_s_1_r_r1), .in2(registradores_s_1_r_r2),
    .in3(registradores_s_1_r_r3), .out(R_rb), .sel(rb));
endmodule

module Registradores_S (
  input  Reset,
  input  RegWrite,
  input  [1:0] rd,
  input  [7:0] RegIn,
  input  clk,
  output [7:0] R_r0,
  output [7:0] R_r1,
  output [7:0] R_r2,
  output [7:0] R_r3
);

  wire demultiplexer_1_out1, demultiplexer_1_out2, demultiplexer_1_out3;

  Demultiplexer #(.select(2)) demultiplexer_1 (
    .out1(demultiplexer_1_out1), .out2(demultiplexer_1_out2), .out3(demultiplexer_1_out3), .in(RegWrite),
    .sel(rd));  // open: out0
  Register r0 (.D({8{1'b0}}), .en(1'b0), .clk(clk), .Q(R_r0), .clr(Reset));
  Register r1 (.D(RegIn), .en(demultiplexer_1_out1), .clk(clk), .Q(R_r1), .clr(Reset));
  Register r2 (.D(RegIn), .en(demultiplexer_1_out2), .clk(clk), .Q(R_r2), .clr(Reset));
  Register r3 (.D(RegIn), .en(demultiplexer_1_out3), .clk(clk), .Q(R_r3), .clr(Reset));
endmodule

module PC (
  input  [7:0] PC_In,
  input  PCWrite,
  input  clk,
  input  Reset,
  output [7:0] PC_Out
);

  Register register_1 (.D(PC_In), .en(PCWrite), .clk(clk), .Q(PC_Out), .clr(Reset));
endmodule

module ULA_S (
  input  [7:0] ULA_A,
  input  [7:0] ULA_B,
  input  [1:0] ALUOp,
  output [7:0] ULA_Out
);

  wire [7:0] adder_1_out, and_1_out, subtractor_1_out;

  Adder adder_1 (.a(ULA_A), .b(ULA_B), .out(adder_1_out));  // open: cin, cout
  Subtractor subtractor_1 (.a(ULA_A), .b(ULA_B), .out(subtractor_1_out));  // open: bin, bout
  assign and_1_out = ULA_A & ULA_B;  // AND_Gate and_1, 8 bits wide
  Multiplexer #(.select(2), .width(8)) multiplexer_1 (
    .in0(adder_1_out), .in1(subtractor_1_out), .in2(and_1_out), .out(ULA_Out), .sel(ALUOp));  // open: in3
endmodule

module Branch_Control (
  input  Branch,
  input  [7:0] R_ra,
  output Taken
);

  wire nor_1_out;

  and and_1 (Taken, Branch, nor_1_out);
  nor nor_1 (nor_1_out, R_ra[0], R_ra[1], R_ra[2], R_ra[3], R_ra[4], R_ra[5], R_ra[6], R_ra[7]);

  // Notes on the sheet:
  //   Se 'for branch' e R[r0] == 0 OU 'for salto incondional', então desvie
endmodule

module Proximo_PC (
  input  MUX_PC,
  input  [7:0] PC_OUT,
  input  [7:0] Imm_Ext,
  input  [7:0] R_rb,
  input  MUX_SumPC,
  output [7:0] PC_In
);

  wire [7:0] adder_1_out, multiplexer_1_out;

  Multiplexer #(.width(8)) multiplexer_1 (.in0(8'h1), .in1(Imm_Ext), .out(multiplexer_1_out), .sel(MUX_SumPC));
  Multiplexer #(.width(8)) multiplexer_2 (.in0(adder_1_out), .in1(R_rb), .out(PC_In), .sel(MUX_PC));
  Adder adder_1 (.a(PC_OUT), .b(multiplexer_1_out), .out(adder_1_out));  // open: cin, cout
endmodule

module Shifter_Left (
  input  [7:0] ULA_A,
  input  [7:0] ULA_B,
  output [7:0] ULA_OUT
);

  wire or_1_out;
  wire [7:0] shifter_1_out;

  Shifter shifter_1 (.in(ULA_A), .\dist (ULA_B[2:0]), .out(shifter_1_out));
  Multiplexer #(.width(8)) multiplexer_1 (.in0(shifter_1_out), .in1({8{1'b0}}), .out(ULA_OUT), .sel(or_1_out));
  or or_1 (or_1_out, ULA_B[3], ULA_B[4], ULA_B[5], ULA_B[6], ULA_B[7]);

  // Notes on the sheet:
  //   Se o shift tiver overflow, então o resultado do shift será 0
endmodule

module Shift_Right (
  input  [7:0] ULA_A,
  input  [7:0] ULA_B,
  output [7:0] ULA_OUT
);

  wire or_1_out;
  wire [7:0] shifter_1_out;

  Shifter #(.shift("lr")) shifter_1 (.in(ULA_A), .\dist (ULA_B[2:0]), .out(shifter_1_out));
  Multiplexer #(.width(8)) multiplexer_1 (.in0(shifter_1_out), .in1({8{1'b0}}), .out(ULA_OUT), .sel(or_1_out));
  or or_1 (or_1_out, ULA_B[3], ULA_B[4], ULA_B[5], ULA_B[6], ULA_B[7]);

  // Notes on the sheet:
  //   Se o shift tiver overflow, então o resultado do shift será 0
endmodule

module Unidade_de_Controle (
  input  [3:0] Opcode,
  output [1:0] AluOp,
  output [1:0] MUX_RegIn,
  output RegWrite,
  output MemWrite,
  output Type_Inst,
  output PE,
  output Branch,
  output LI,
  output Move
);

  wire and_3_out, and_4_out, and_5_out, and_6_out, and_7_out, and_8_out, and_9_out, and_12_out, and_13_out,
       not_1_out, not_2_out, not_3_out;

  not not_1 (not_1_out, Opcode[3]);
  not not_2 (not_2_out, Opcode[2]);
  not not_3 (not_3_out, Opcode[1]);
  not not_4 (Move, Opcode[0]);
  and and_1 (AluOp[1], not_1_out, Opcode[1]);
  and and_2 (AluOp[0], not_3_out, Opcode[0]);
  and and_3 (and_3_out, not_2_out, Opcode[1]);
  and and_4 (and_4_out, Opcode[3], Opcode[1], Move);
  and and_5 (and_5_out, not_2_out, not_3_out);
  and and_6 (and_6_out, Opcode[3], Opcode[2], Opcode[1], Move);
  and and_7 (and_7_out, not_2_out, Opcode[1]);
  and and_8 (and_8_out, Opcode[2], not_3_out);
  and and_9 (and_9_out, Opcode[3], Opcode[1]);
  and and_10 (MemWrite, not_2_out, not_3_out, Opcode[0]);
  and and_11 (Type_Inst, not_2_out, Opcode[1]);
  and and_12 (and_12_out, Opcode[3], not_2_out);
  and and_13 (and_13_out, Opcode[3], not_3_out);
  and and_14 (Branch, not_1_out, Opcode[2], Opcode[1], Opcode[0]);
  and and_15 (LI, Opcode[3], Opcode[2], Opcode[1], Opcode[0]);
  or or_1 (MUX_RegIn[1], and_3_out, and_4_out);
  or or_2 (MUX_RegIn[0], and_5_out, and_6_out);
  or or_3 (RegWrite, Move, and_7_out, and_8_out, and_9_out);
  or or_4 (PE, and_12_out, and_13_out);
endmodule

module Teste_clk (
);

  wire clock_1_out, clock_2_out;

  Clock #(.phaseOffset(3)) clock_1 (.out(clock_1_out));
  Clock #(.highDuration(2), .lowDuration(2), .phaseOffset(3)) clock_2 (.out(clock_2_out));
  // Digital_Oscilloscope digital_oscilloscope_1: pin names not known; wires that end beside it: clock_1_out, clock_2_out
endmodule

module Controle_Forwading (
  input  ra_igual_rd_MEM,
  input  rb_igual_rd_MEM,
  input  ra_igual_rd_WB,
  input  rb_igual_rd_WB,
  output [1:0] ForwardA,
  output [1:0] ForwardB
);

  wire not_1_out, not_2_out;

  not not_1 (not_1_out, ra_igual_rd_MEM);
  not not_2 (not_2_out, rb_igual_rd_MEM);
  and and_1 (ForwardA[1], not_1_out, ra_igual_rd_WB);
  and and_2 (ForwardB[1], not_2_out, rb_igual_rd_WB);

  assign ForwardA[0] = ra_igual_rd_MEM;
  assign ForwardB[0] = rb_igual_rd_MEM;
endmodule

// UnidadeFowarding
module Unidade_Forwarding_S (
  input  [1:0] ra_ID_EX,
  input  [1:0] rb_ID_EX,
  input  [1:0] rd_MEM,
  input  [1:0] rd_WB,
  input  RegWrite_EX_MEM,
  input  RegWrite_MEM_WB,
  input  [3:0] Opcode_ID_EX,
  input  [7:0] ULA_Out_EX_MEM,
  input  [7:0] Reg_mv_EX_MEM,
  input  [7:0] R_rb_EX_MEM,
  input  [1:0] MUX_RegIn_EX_MEM,
  output [1:0] FwA,
  output [1:0] FwB,
  output [7:0] Data_EX_MEM
);

  wire and_1_out, and_2_out, and_3_out, and_4_out, comparator_1_eq, comparator_2_eq, comparator_3_eq,
       comparator_4_eq, detector_de_leitura_1_regreada, detector_de_leitura_1_regreadb;
  wire [1:0] controle_forwading_1_forwarda, controle_forwading_1_forwardb;

  Comparator #(.width(2)) comparator_1 (.a(ra_ID_EX), .b(rd_MEM), .eq(comparator_1_eq));  // open: gt, lt
  Comparator #(.width(2)) comparator_2 (.a(rb_ID_EX), .b(rd_MEM), .eq(comparator_2_eq));  // open: gt, lt
  Comparator #(.width(2)) comparator_3 (.a(ra_ID_EX), .b(rd_WB), .eq(comparator_3_eq));  // open: gt, lt
  Comparator #(.width(2)) comparator_4 (.a(rb_ID_EX), .b(rd_WB), .eq(comparator_4_eq));  // open: gt, lt
  and and_1 (and_1_out, RegWrite_EX_MEM, comparator_1_eq);
  and and_2 (and_2_out, RegWrite_EX_MEM, comparator_2_eq);
  and and_3 (and_3_out, RegWrite_MEM_WB, comparator_3_eq);
  and and_4 (and_4_out, RegWrite_MEM_WB, comparator_4_eq);
  Multiplexer #(.select(2), .width(8)) multiplexer_1 (
    .in0(ULA_Out_EX_MEM), .in2(Reg_mv_EX_MEM), .in3(R_rb_EX_MEM), .out(Data_EX_MEM), .sel(MUX_RegIn_EX_MEM));  // open: in1
  Controle_Forwading controle_forwading_1 (
    .ra_igual_rd_MEM(and_1_out), .rb_igual_rd_MEM(and_2_out), .ra_igual_rd_WB(and_3_out),
    .rb_igual_rd_WB(and_4_out), .ForwardA(controle_forwading_1_forwarda),
    .ForwardB(controle_forwading_1_forwardb));
  Detector_de_Leitura detector_de_leitura_1 (
    .Opcode(Opcode_ID_EX), .RegReadA(detector_de_leitura_1_regreada),
    .RegReadB(detector_de_leitura_1_regreadb));
  Multiplexer #(.width(2)) multiplexer_2 (
    .in0(2'b00), .in1(controle_forwading_1_forwarda), .out(FwA), .sel(detector_de_leitura_1_regreada));
  Multiplexer #(.width(2)) multiplexer_3 (
    .in0(2'b00), .in1(controle_forwading_1_forwardb), .out(FwB), .sel(detector_de_leitura_1_regreadb));

  // Notes on the sheet:
  //   Se o endereço de leitura e escrita são iguais em diferentes estágios
  //   E a instrução a frente escreve no banco de registradores
  //   E a instrução de trás lê do banco de registradores
  //   Qual dado adiantar do EX/MEM?
  //   Então adianda dado
  //   Dado normal
endmodule

module Detector_de_Leitura (
  input  [3:0] Opcode,
  output RegReadA,
  output RegReadB
);

  wire and_1_out, and_2_out, and_3_out, and_4_out, and_5_out, not_1_out, not_2_out, not_3_out, not_4_out;

  not not_1 (not_1_out, Opcode[3]);
  not not_2 (not_2_out, Opcode[2]);
  not not_3 (not_3_out, Opcode[1]);
  not not_4 (not_4_out, Opcode[0]);
  and and_1 (and_1_out, not_2_out, Opcode[1]);
  and and_2 (and_2_out, Opcode[2], not_3_out);
  and and_3 (and_3_out, not_1_out, Opcode[1]);
  and and_4 (and_4_out, not_1_out, Opcode[2]);
  and and_5 (and_5_out, Opcode[2], not_4_out);
  or or_1 (RegReadA, Opcode[0], and_1_out, and_2_out, and_3_out);
  or or_2 (RegReadB, not_3_out, and_4_out, and_5_out);
endmodule

module Hazard_Detectation_Unit (
  input  [3:0] Opcode_ID_EX_S,
  input  [1:0] ra_ID,
  input  [1:0] rd_ID_EX_S,
  input  [1:0] rb_ID,
  input  [3:0] Opcode_ID_EX_V,
  input  [1:0] rd_ID_EX_V,
  input  PE_ID,
  input  PE_ID_EX,
  input  [3:0] Opcode_ID,
  output Stall
);

  wire and_1_out, and_2_out, and_3_out, and_4_out, and_5_out, and_6_out, and_7_out, and_8_out,
       comparator_1_eq, comparator_2_eq, comparator_3_eq, comparator_4_eq, detector_de_leitura_1_regreada,
       detector_de_leitura_1_regreadb, or_1_out, or_2_out, xnor_1_out;

  and and_1 (and_1_out, ~Opcode_ID_EX_S[0], ~Opcode_ID_EX_S[1], ~Opcode_ID_EX_S[2], ~Opcode_ID_EX_S[3]);  // AND_Gate
  Comparator #(.width(2)) comparator_1 (.a(ra_ID), .b(rd_ID_EX_S), .eq(comparator_1_eq));  // open: gt, lt
  Comparator #(.width(2)) comparator_2 (.a(rd_ID_EX_S), .b(rb_ID), .eq(comparator_2_eq));  // open: gt, lt
  and and_2 (and_2_out, ~Opcode_ID_EX_V[0], ~Opcode_ID_EX_V[1], ~Opcode_ID_EX_V[2], Opcode_ID_EX_V[3]);  // AND_Gate
  Comparator #(.width(2)) comparator_3 (.a(ra_ID), .b(rd_ID_EX_V), .eq(comparator_3_eq));  // open: gt, lt
  Comparator #(.width(2)) comparator_4 (.a(rd_ID_EX_V), .b(rb_ID), .eq(comparator_4_eq));  // open: gt, lt
  xnor xnor_1 (xnor_1_out, PE_ID, PE_ID_EX);
  Detector_de_Leitura detector_de_leitura_1 (
    .Opcode(Opcode_ID), .RegReadA(detector_de_leitura_1_regreada), .RegReadB(detector_de_leitura_1_regreadb));
  and and_3 (and_3_out, xnor_1_out, detector_de_leitura_1_regreada, comparator_1_eq);
  and and_4 (and_4_out, xnor_1_out, detector_de_leitura_1_regreadb, comparator_2_eq);
  and and_5 (and_5_out, xnor_1_out, detector_de_leitura_1_regreada, comparator_3_eq);
  and and_6 (and_6_out, xnor_1_out, detector_de_leitura_1_regreadb, comparator_4_eq);
  or or_1 (or_1_out, and_3_out, and_4_out);
  or or_2 (or_2_out, and_5_out, and_6_out);
  and and_7 (and_7_out, and_1_out, or_1_out);
  and and_8 (and_8_out, and_2_out, or_2_out);
  or or_3 (Stall, and_7_out, and_8_out);

  // Notes on the sheet:
  //   Se  load em ID_EX
  //   E se as instruçes de ID e EX sõo do mesmo PE (vetorial ou escalar)
  //   E se endereço de leitura da instrução em ID e de escrita em EX são iguais
  //   E se a instrução em ID le registrador
  //   Existe dependência na instruço em ID_S
  //   Existe dependência na instruço em ID_V
  //   É Load em EX_S
  //   É Load em EX_V
  //   Stall em SPE
  //   Stall em VPE
endmodule

module BTB_e_Preditor (
  input  clk,
  input  Reset,
  input  Taken_EX,
  input  Branch_ID_EX,
  input  [7:0] R_rb,
  input  [7:0] PC_Out_ID_EX,
  input  [7:0] PC_Out_IF,
  output PredictTaken,
  output [7:0] Endereco_Previsto
);

  wire Bit_de_Validade, comparator_1_eq, Estado;
  wire [0:0] Estado_Atual;
  wire [1:0] NovoEstado;
  wire [3:0] BTB_Endereco, Index;

  Multiplexer #(.width(4)) multiplexer_1 (
    .in0(PC_Out_IF[3:0]), .in1(PC_Out_ID_EX[3:0]), .out(Index), .sel(Branch_ID_EX));
  RAM #(.addrWidth(4), .asyncread("true"), .dataWidth(4)) Endereco_Instrucao (
    .addr(Index), .we(Branch_ID_EX), .oe(1'b1), .clk(clk), .din(PC_Out_ID_EX[7:4]), .dout(BTB_Endereco));
  RAM #(.addrWidth(4), .asyncread("true")) Endereco_Desvio (
    .addr(Index), .we(Branch_ID_EX), .oe(1'b1), .clk(clk), .din(R_rb), .dout(Endereco_Previsto));
  RAM #(.addrWidth(4), .asyncread("true"), .dataWidth(2)) u_Estado (
    .addr(Index), .we(Branch_ID_EX), .oe(1'b1), .clk(clk), .din(NovoEstado), .dout({Estado, Estado_Atual[0]}));
  Mem_Validade_BTB mem_validade_btb_1 (
    .clk(clk), .Reset(Reset), .Index(Index), .Branch(Branch_ID_EX), .Valido(Bit_de_Validade));
  Novo_Estado novo_estado_1 (.Estado_Atual({Estado, Estado_Atual[0]}), .Taken(Taken_EX), .Novo_Estado(NovoEstado));
  Comparator #(.width(4)) comparator_1 (.a(BTB_Endereco), .b(PC_Out_IF[7:4]), .eq(comparator_1_eq));  // open: gt, lt
  and and_1 (PredictTaken, Estado, Bit_de_Validade, ~Branch_ID_EX, comparator_1_eq);  // AND_Gate

  // Other names for the same wires on the sheet: Branch_EX = Branch_ID_EX; Estado_Atual[1] = Estado;
  //   PC_Out_ID_EX_0_3[3:0] = PC_Out_ID_EX[3:0]; PC_Out_ID_EX_4_7[3:0] = PC_Out_ID_EX[7:4];
  //   PC_Out_IF_0_3[3:0] = PC_Out_IF[3:0]; PC_Out_IF_4_7[3:0] = PC_Out_IF[7:4]; PC_Salto_EX[7:0] = R_rb

  // Notes on the sheet:
  //   Se  branch no execute -> Circuito esté escrevendo
  //   Caso contrário -> Circuito está lendo a Cache e verificando se há predição
  //   Taken?
  //   Valid?
  //   Esta lendo?
  //   Hit?
endmodule

module Novo_Estado (
  input  [1:0] Estado_Atual,
  input  Taken,
  output [1:0] Novo_Estado
);

  wire and_1_out, and_2_out, and_3_out, and_4_out, and_5_out, and_6_out, not_1_out;

  not not_1 (not_1_out, Estado_Atual[0]);
  and and_1 (and_1_out, Estado_Atual[0], Taken);
  and and_2 (and_2_out, Estado_Atual[1], Taken);
  and and_3 (and_3_out, Estado_Atual[1], Estado_Atual[0]);
  and and_4 (and_4_out, not_1_out, Taken);
  and and_5 (and_5_out, Estado_Atual[1], not_1_out);
  and and_6 (and_6_out, Estado_Atual[1], Taken);
  or or_1 (Novo_Estado[1], and_1_out, and_2_out, and_3_out);
  or or_2 (Novo_Estado[0], and_4_out, and_5_out, and_6_out);
endmodule

module Unidade_de_Reset (
  input  Flush,
  input  Stall,
  input  Reset,
  output Write_IF_ID,
  output Reset_IF_ID,
  output Reset_ID_EX
);

  wire and_1_out, not_1_out, or_1_out;

  not not_1 (not_1_out, Flush);
  or or_1 (or_1_out, Stall, Flush);
  and and_1 (and_1_out, not_1_out, Stall);
  not not_2 (Write_IF_ID, and_1_out);
  or or_2 (Reset_IF_ID, Flush, Reset);
  or or_3 (Reset_ID_EX, or_1_out, Reset);

  // Other names for the same wires on the sheet: ResetInicial = Reset
endmodule

module Reset_Inicial (
  input  clk_mem,
  output Reset
);

  wire and_1_out, not_2_out, or_1_out, Z0, Z1;

  not not_1 (Reset, Z1);
  not not_2 (not_2_out, Z0);
  or or_1 (or_1_out, Z0, Z1);
  and and_1 (and_1_out, not_2_out, Reset);
  D_Flip_Flop d_ff_1 (.D(or_1_out), .clk(clk_mem), .Q(Z1));  // open: Qn, preset, reset
  D_Flip_Flop d_ff_2 (.D(and_1_out), .clk(clk_mem), .Q(Z0));  // open: Qn, preset, reset
endmodule

module Juntador (
  input  [7:0] R_ra,
  input  [3:0] Imm,
  input  Move,
  output [7:0] Reg_Moved
);

  Multiplexer #(.width(8)) multiplexer_1 (.in0({R_ra[7:4], Imm}), .in1({Imm, R_ra[3:0]}), .out(Reg_Moved), .sel(Move));

  // Notes on the sheet:
  //   MOVE LOW
  //   MOVE HIGH
endmodule

module ULA_V (
  input  [7:0] ULA_A,
  input  [7:0] ULA_B,
  input  ALUOp,
  output [7:0] ULA_OUT
);

  wire [7:0] adder_1_out, subtractor_1_out;

  Adder adder_1 (.a(ULA_A), .b(ULA_B), .out(adder_1_out));  // open: cin, cout
  Subtractor subtractor_1 (.a(ULA_A), .b(ULA_B), .out(subtractor_1_out));  // open: bin, bout
  Multiplexer #(.width(8)) multiplexer_1 (.in0(adder_1_out), .in1(subtractor_1_out), .out(ULA_OUT), .sel(ALUOp));
endmodule

module Unidade_Forwarding_V (
  input  [1:0] ra_ID_EX,
  input  [1:0] rb_ID_EX,
  input  [1:0] rd_MEM,
  input  [1:0] rd_WB,
  input  RegWrite_EX_MEM,
  input  RegWrite_MEM_WB,
  input  [3:0] Opcode_ID_EX,
  output [1:0] FwA,
  output [1:0] FwB
);

  wire and_1_out, and_2_out, and_3_out, and_4_out, comparator_1_eq, comparator_2_eq, comparator_3_eq,
       comparator_4_eq, detector_de_leitura_1_regreada, detector_de_leitura_1_regreadb;
  wire [1:0] controle_forwading_1_forwarda, controle_forwading_1_forwardb;

  Comparator #(.width(2)) comparator_1 (.a(ra_ID_EX), .b(rd_MEM), .eq(comparator_1_eq));  // open: gt, lt
  Comparator #(.width(2)) comparator_2 (.a(rb_ID_EX), .b(rd_MEM), .eq(comparator_2_eq));  // open: gt, lt
  Comparator #(.width(2)) comparator_3 (.a(ra_ID_EX), .b(rd_WB), .eq(comparator_3_eq));  // open: gt, lt
  Comparator #(.width(2)) comparator_4 (.a(rb_ID_EX), .b(rd_WB), .eq(comparator_4_eq));  // open: gt, lt
  and and_1 (and_1_out, RegWrite_EX_MEM, comparator_1_eq);
  and and_2 (and_2_out, RegWrite_EX_MEM, comparator_2_eq);
  and and_3 (and_3_out, RegWrite_MEM_WB, comparator_3_eq);
  and and_4 (and_4_out, RegWrite_MEM_WB, comparator_4_eq);
  Controle_Forwading controle_forwading_1 (
    .ra_igual_rd_MEM(and_1_out), .rb_igual_rd_MEM(and_2_out), .ra_igual_rd_WB(and_3_out),
    .rb_igual_rd_WB(and_4_out), .ForwardA(controle_forwading_1_forwarda),
    .ForwardB(controle_forwading_1_forwardb));
  Detector_de_Leitura detector_de_leitura_1 (
    .Opcode(Opcode_ID_EX), .RegReadA(detector_de_leitura_1_regreada),
    .RegReadB(detector_de_leitura_1_regreadb));
  Multiplexer #(.width(2)) multiplexer_1 (
    .in0(2'b00), .in1(controle_forwading_1_forwarda), .out(FwA), .sel(detector_de_leitura_1_regreada));
  Multiplexer #(.width(2)) multiplexer_2 (
    .in0(2'b00), .in1(controle_forwading_1_forwardb), .out(FwB), .sel(detector_de_leitura_1_regreadb));

  // Notes on the sheet:
  //   Se o endereço de leitura e escrita são iguais em diferentes estágios
  //   E a instrução a frente escreve no banco de registradores
  //   E a instrução de trás lê do banco de registradores
  //   Então adianda dado
  //   Dado normal
endmodule

module Banco_de_Registradores_V0 (
  input  clk,
  input  [7:0] RegIn,
  input  [1:0] rd,
  input  RegWrite,
  input  Reset,
  input  [1:0] ra,
  input  [1:0] rb,
  output [7:0] R_ra,
  output [7:0] R_rb
);

  wire [7:0] registradores_v0_1_r_r0, registradores_v0_1_r_r1, registradores_v0_1_r_r2,
       registradores_v0_1_r_r3;

  Registradores_V0 registradores_v0_1 (
    .Reset(Reset), .RegWrite(RegWrite), .rd(rd), .RegIn(RegIn), .clk(clk), .R_r0(registradores_v0_1_r_r0),
    .R_r1(registradores_v0_1_r_r1), .R_r2(registradores_v0_1_r_r2), .R_r3(registradores_v0_1_r_r3));
  Multiplexer #(.select(2), .width(8)) multiplexer_1 (
    .in0(registradores_v0_1_r_r0), .in1(registradores_v0_1_r_r1), .in2(registradores_v0_1_r_r2),
    .in3(registradores_v0_1_r_r3), .out(R_ra), .sel(ra));
  Multiplexer #(.select(2), .width(8)) multiplexer_2 (
    .in0(registradores_v0_1_r_r0), .in1(registradores_v0_1_r_r1), .in2(registradores_v0_1_r_r2),
    .in3(registradores_v0_1_r_r3), .out(R_rb), .sel(rb));
endmodule

module Registradores_V0 (
  input  Reset,
  input  RegWrite,
  input  [1:0] rd,
  input  [7:0] RegIn,
  input  clk,
  output [7:0] R_r0,
  output [7:0] R_r1,
  output [7:0] R_r2,
  output [7:0] R_r3
);

  wire demultiplexer_1_out1, demultiplexer_1_out2, demultiplexer_1_out3;

  Demultiplexer #(.select(2)) demultiplexer_1 (
    .out1(demultiplexer_1_out1), .out2(demultiplexer_1_out2), .out3(demultiplexer_1_out3), .in(RegWrite),
    .sel(rd));  // open: out0
  Register r0 (.D({8{1'b0}}), .en(1'b1), .clk(clk), .Q(R_r0), .clr(Reset));
  Register r1 (.D(RegIn), .en(demultiplexer_1_out1), .clk(clk), .Q(R_r1), .clr(Reset));
  Register r2 (.D(RegIn), .en(demultiplexer_1_out2), .clk(clk), .Q(R_r2), .clr(Reset));
  Register r3 (.D(RegIn), .en(demultiplexer_1_out3), .clk(clk), .Q(R_r3), .clr(Reset));
endmodule

module Registradores_V1 (
  input  Reset,
  input  RegWrite,
  input  [1:0] rd,
  input  [7:0] RegIn,
  input  clk,
  output [7:0] R_r0,
  output [7:0] R_r1,
  output [7:0] R_r2,
  output [7:0] R_r3
);

  wire demultiplexer_1_out1, demultiplexer_1_out2, demultiplexer_1_out3;

  Demultiplexer #(.select(2)) demultiplexer_1 (
    .out1(demultiplexer_1_out1), .out2(demultiplexer_1_out2), .out3(demultiplexer_1_out3), .in(RegWrite),
    .sel(rd));  // open: out0
  Register r0 (.D(8'h1), .en(1'b1), .clk(clk), .Q(R_r0));  // open: clr
  Register r1 (.D(RegIn), .en(demultiplexer_1_out1), .clk(clk), .Q(R_r1), .clr(Reset));
  Register r2 (.D(RegIn), .en(demultiplexer_1_out2), .clk(clk), .Q(R_r2), .clr(Reset));
  Register r3 (.D(RegIn), .en(demultiplexer_1_out3), .clk(clk), .Q(R_r3), .clr(Reset));
endmodule

module Mem_Validade_BTB (
  input  clk,
  input  Reset,
  input  [3:0] Index,
  input  Branch,
  output Valido
);

  wire demultiplexer_1_out0, demultiplexer_1_out1, demultiplexer_1_out2, demultiplexer_1_out3,
       demultiplexer_1_out4, demultiplexer_1_out5, demultiplexer_1_out6, demultiplexer_1_out7,
       demultiplexer_1_out8, demultiplexer_1_out9, demultiplexer_1_out10, demultiplexer_1_out11,
       demultiplexer_1_out12, demultiplexer_1_out13, demultiplexer_1_out14, demultiplexer_1_out15, r0_q,
       r1_q, r2_q, r3_q, r4_q, r5_q, r6_q, r7_q, r8_q, r9_q, r10_q, r11_q, r12_q, r13_q, r14_q, r15_q;

  Demultiplexer #(.select(4)) demultiplexer_1 (
    .out0(demultiplexer_1_out0), .out1(demultiplexer_1_out1), .out2(demultiplexer_1_out2),
    .out3(demultiplexer_1_out3), .out4(demultiplexer_1_out4), .out5(demultiplexer_1_out5),
    .out6(demultiplexer_1_out6), .out7(demultiplexer_1_out7), .out8(demultiplexer_1_out8),
    .out9(demultiplexer_1_out9), .out10(demultiplexer_1_out10), .out11(demultiplexer_1_out11),
    .out12(demultiplexer_1_out12), .out13(demultiplexer_1_out13), .out14(demultiplexer_1_out14),
    .out15(demultiplexer_1_out15), .in(Branch), .sel(Index));
  Register #(.width(1)) r0 (.D(1'b1), .en(demultiplexer_1_out0), .Q(r0_q), .clk(clk), .clr(Reset));
  Register #(.width(1)) r1 (.D(1'b1), .en(demultiplexer_1_out1), .Q(r1_q), .clk(clk), .clr(Reset));
  Register #(.width(1)) r2 (.D(1'b1), .en(demultiplexer_1_out2), .Q(r2_q), .clk(clk), .clr(Reset));
  Register #(.width(1)) r3 (.D(1'b1), .en(demultiplexer_1_out3), .Q(r3_q), .clk(clk), .clr(Reset));
  Register #(.width(1)) r4 (.D(1'b1), .en(demultiplexer_1_out4), .Q(r4_q), .clk(clk), .clr(Reset));
  Register #(.width(1)) r5 (.D(1'b1), .en(demultiplexer_1_out5), .Q(r5_q), .clk(clk), .clr(Reset));
  Register #(.width(1)) r6 (.D(1'b1), .en(demultiplexer_1_out6), .Q(r6_q), .clk(clk), .clr(Reset));
  Register #(.width(1)) r7 (.D(1'b1), .en(demultiplexer_1_out7), .Q(r7_q), .clk(clk), .clr(Reset));
  Register #(.width(1)) r8 (.D(1'b1), .en(demultiplexer_1_out8), .Q(r8_q), .clk(clk), .clr(Reset));
  Register #(.width(1)) r9 (.D(1'b1), .en(demultiplexer_1_out9), .Q(r9_q), .clk(clk), .clr(Reset));
  Register #(.width(1)) r10 (.D(1'b1), .en(demultiplexer_1_out10), .Q(r10_q), .clk(clk), .clr(Reset));
  Register #(.width(1)) r11 (.D(1'b1), .en(demultiplexer_1_out11), .Q(r11_q), .clk(clk), .clr(Reset));
  Register #(.width(1)) r12 (.D(1'b1), .en(demultiplexer_1_out12), .Q(r12_q), .clk(clk), .clr(Reset));
  Register #(.width(1)) r13 (.D(1'b1), .en(demultiplexer_1_out13), .Q(r13_q), .clk(clk), .clr(Reset));
  Register #(.width(1)) r14 (.D(1'b1), .en(demultiplexer_1_out14), .Q(r14_q), .clk(clk), .clr(Reset));
  Register #(.width(1)) r15 (.D(1'b1), .en(demultiplexer_1_out15), .Q(r15_q), .clk(clk), .clr(Reset));
  Multiplexer #(.select(4)) multiplexer_1 (
    .in0(r0_q), .in1(r1_q), .in2(r2_q), .in3(r3_q), .in4(r4_q), .in5(r5_q), .in6(r6_q), .in7(r7_q),
    .in8(r8_q), .in9(r9_q), .in10(r10_q), .in11(r11_q), .in12(r12_q), .in13(r13_q), .in14(r14_q),
    .in15(r15_q), .out(Valido), .sel(Index));
endmodule

module Registradores_V2 (
  input  Reset,
  input  RegWrite,
  input  [1:0] rd,
  input  [7:0] RegIn,
  input  clk,
  output [7:0] R_r0,
  output [7:0] R_r1,
  output [7:0] R_r2,
  output [7:0] R_r3
);

  wire demultiplexer_1_out1, demultiplexer_1_out2, demultiplexer_1_out3;

  Demultiplexer #(.select(2)) demultiplexer_1 (
    .out1(demultiplexer_1_out1), .out2(demultiplexer_1_out2), .out3(demultiplexer_1_out3), .in(RegWrite),
    .sel(rd));  // open: out0
  Register r0 (.D(8'h2), .en(1'b1), .clk(clk), .Q(R_r0));  // open: clr
  Register r1 (.D(RegIn), .en(demultiplexer_1_out1), .clk(clk), .Q(R_r1), .clr(Reset));
  Register r2 (.D(RegIn), .en(demultiplexer_1_out2), .clk(clk), .Q(R_r2), .clr(Reset));
  Register r3 (.D(RegIn), .en(demultiplexer_1_out3), .clk(clk), .Q(R_r3), .clr(Reset));
endmodule

module Registradores_V3 (
  input  Reset,
  input  RegWrite,
  input  [1:0] rd,
  input  [7:0] RegIn,
  input  clk,
  output [7:0] R_r0,
  output [7:0] R_r1,
  output [7:0] R_r2,
  output [7:0] R_r3
);

  wire demultiplexer_1_out1, demultiplexer_1_out2, demultiplexer_1_out3;

  Demultiplexer #(.select(2)) demultiplexer_1 (
    .out1(demultiplexer_1_out1), .out2(demultiplexer_1_out2), .out3(demultiplexer_1_out3), .in(RegWrite),
    .sel(rd));  // open: out0
  Register r0 (.D(8'h3), .en(1'b1), .clk(clk), .Q(R_r0));  // open: clr
  Register r1 (.D(RegIn), .en(demultiplexer_1_out1), .clk(clk), .Q(R_r1), .clr(Reset));
  Register r2 (.D(RegIn), .en(demultiplexer_1_out2), .clk(clk), .Q(R_r2), .clr(Reset));
  Register r3 (.D(RegIn), .en(demultiplexer_1_out3), .clk(clk), .Q(R_r3), .clr(Reset));
endmodule

module Banco_de_Registradores_V1 (
  input  clk,
  input  [7:0] RegIn,
  input  [1:0] rd,
  input  RegWrite,
  input  Reset,
  input  [1:0] ra,
  input  [1:0] rb,
  output [7:0] R_ra,
  output [7:0] R_rb
);

  wire [7:0] registradores_v1_1_r_r0, registradores_v1_1_r_r1, registradores_v1_1_r_r2,
       registradores_v1_1_r_r3;

  Registradores_V1 registradores_v1_1 (
    .Reset(Reset), .RegWrite(RegWrite), .rd(rd), .RegIn(RegIn), .clk(clk), .R_r0(registradores_v1_1_r_r0),
    .R_r1(registradores_v1_1_r_r1), .R_r2(registradores_v1_1_r_r2), .R_r3(registradores_v1_1_r_r3));
  Multiplexer #(.select(2), .width(8)) multiplexer_1 (
    .in0(registradores_v1_1_r_r0), .in1(registradores_v1_1_r_r1), .in2(registradores_v1_1_r_r2),
    .in3(registradores_v1_1_r_r3), .out(R_ra), .sel(ra));
  Multiplexer #(.select(2), .width(8)) multiplexer_2 (
    .in0(registradores_v1_1_r_r0), .in1(registradores_v1_1_r_r1), .in2(registradores_v1_1_r_r2),
    .in3(registradores_v1_1_r_r3), .out(R_rb), .sel(rb));
endmodule

module Banco_de_Registradores_V2 (
  input  clk,
  input  [7:0] RegIn,
  input  [1:0] rd,
  input  RegWrite,
  input  Reset,
  input  [1:0] ra,
  input  [1:0] rb,
  output [7:0] R_ra,
  output [7:0] R_rb
);

  wire [7:0] registradores_v2_1_r_r0, registradores_v2_1_r_r1, registradores_v2_1_r_r2,
       registradores_v2_1_r_r3;

  Registradores_V2 registradores_v2_1 (
    .Reset(Reset), .RegWrite(RegWrite), .rd(rd), .RegIn(RegIn), .clk(clk), .R_r0(registradores_v2_1_r_r0),
    .R_r1(registradores_v2_1_r_r1), .R_r2(registradores_v2_1_r_r2), .R_r3(registradores_v2_1_r_r3));
  Multiplexer #(.select(2), .width(8)) multiplexer_1 (
    .in0(registradores_v2_1_r_r0), .in1(registradores_v2_1_r_r1), .in2(registradores_v2_1_r_r2),
    .in3(registradores_v2_1_r_r3), .out(R_ra), .sel(ra));
  Multiplexer #(.select(2), .width(8)) multiplexer_2 (
    .in0(registradores_v2_1_r_r0), .in1(registradores_v2_1_r_r1), .in2(registradores_v2_1_r_r2),
    .in3(registradores_v2_1_r_r3), .out(R_rb), .sel(rb));
endmodule

module Banco_de_Registradores_V3 (
  input  clk,
  input  [7:0] RegIn,
  input  [1:0] rd,
  input  RegWrite,
  input  Reset,
  input  [1:0] ra,
  input  [1:0] rb,
  output [7:0] R_ra,
  output [7:0] R_rb
);

  wire [7:0] registradores_v3_1_r_r0, registradores_v3_1_r_r1, registradores_v3_1_r_r2,
       registradores_v3_1_r_r3;

  Registradores_V3 registradores_v3_1 (
    .Reset(Reset), .RegWrite(RegWrite), .rd(rd), .RegIn(RegIn), .clk(clk), .R_r0(registradores_v3_1_r_r0),
    .R_r1(registradores_v3_1_r_r1), .R_r2(registradores_v3_1_r_r2), .R_r3(registradores_v3_1_r_r3));
  Multiplexer #(.select(2), .width(8)) multiplexer_1 (
    .in0(registradores_v3_1_r_r0), .in1(registradores_v3_1_r_r1), .in2(registradores_v3_1_r_r2),
    .in3(registradores_v3_1_r_r3), .out(R_ra), .sel(ra));
  Multiplexer #(.select(2), .width(8)) multiplexer_2 (
    .in0(registradores_v3_1_r_r0), .in1(registradores_v3_1_r_r1), .in2(registradores_v3_1_r_r2),
    .in3(registradores_v3_1_r_r3), .out(R_rb), .sel(rb));
endmodule
