// Logisim project Testes_Reset.circ as structural Verilog: 19 circuits, main circuit Redux_V
module Redux_V (
  input  Reset
);

  wire Branch_ID, Branch_ID_EX, clk_mem, clk_proc, dualram_1_p1, Flush, JAR_ID, JAR_ID_EX, MemWrite_EX_MEM,
       MemWrite_ID, MemWrite_ID_EX, multiplexer_3_out, multiplexer_4_out, multiplexer_5_out,
       multiplexer_6_out, multiplexer_7_out, multiplexer_8_out, multiplexer_10_out, multiplexer_26_out,
       MUX_SumPC_ID, MUX_SumPC_ID_EX, MUX_Type, MUX_ULA_B_ID, MUX_ULA_B_ID_EX, or_2_out, PCWrite_Hazard,
       PredictTaken_ID_EX, PredictTaken_IF, PredictTaken_IF_ID, RegWrite_EX_MEM, RegWrite_ID, RegWrite_ID_EX,
       RegWrite_MEM_WB, Reset_EX_MEM, Reset_ID_EX, Reset_IF_ID, Reset_PC, Stall, Taken_1, Taken_EX,
       Write_IF_ID;
  wire [1:0] FwA, FwB, multiplexer_9_out, multiplexer_15_out, multiplexer_16_out, multiplexer_17_out,
       MUX_RegIn_EX_MEM, MUX_RegIn_ID, MUX_RegIn_ID_EX, MUX_RegIn_MEM_WB, ra_ID, ra_ID_EX, rb_ID_EX,
       rd_EX_MEM, rd_ID_EX, rd_MEM_WB;
  wire [2:0] ALUOp_ID, ALUOp_ID_EX, multiplexer_2_out;
  wire [3:0] Imediato_ID, multiplexer_18_out, Opcode_ID_EX;
  wire [7:0] adder_1_out, adder_2_out, Data_EX_MEM, Data_WB, Endereco_Previsto_IF, Imm_Ext_EX_MEM,
       Imm_Ext_ID, Imm_Ext_ID_EX, Imm_Ext_MEM_WB, Instrucao_IF, MemDataOut_MEM, MemDataOut_MEM_WB,
       multiplexer_11_out, multiplexer_12_out, multiplexer_13_out, multiplexer_14_out, multiplexer_22_out,
       multiplexer_24_out, multiplexer_27_out, multiplexer_28_out, PC_Next, PC_Out_ID_EX, PC_Out_IF,
       PC_Out_IF_ID, PC_Salto_EX, R_ra_EX, R_ra_EX_MEM, R_ra_ID, R_ra_ID_EX, R_rb_EX_1, R_rb_EX_2,
       R_rb_EX_MEM, R_rb_ID, R_rb_ID_EX, ULA_OUT_EX, ULA_OUT_EX_MEM, ULA_OUT_MEM_WB, Upper_Imm_EX,
       Upper_Imm_EX_MEM, Upper_Imm_MEM_WB;
  wire [7:4] Instrucao_IF_ID;

  assign Imm_Ext_ID = {{4{Imediato_ID[3]}}, Imediato_ID};  // Bit_Extender bit_extender_1
  Unidade_de_Reset unidade_de_reset_1 (
    .Flush(Flush), .Stall(Stall), .Reset(Reset), .Write_IF_ID(Write_IF_ID), .Reset_PC(Reset_PC),
    .Reset_IF_ID(Reset_IF_ID), .Reset_ID_EX(Reset_ID_EX), .Reset_EX_MEM(Reset_EX_MEM));
  Unidade_de_Controle Controle (
    .opcode(Instrucao_IF_ID), .MUX_Type(MUX_Type), .ALUOp(ALUOp_ID), .MUX_ULA_B(MUX_ULA_B_ID),
    .Branch(Branch_ID), .JAR(JAR_ID), .MUX_SumPC(MUX_SumPC_ID), .MemWrite(MemWrite_ID),
    .RegWrite(RegWrite_ID), .MUX_RegIn(MUX_RegIn_ID));
  Multiplexer #(.width(2)) multiplexer_1 (.in0(Imediato_ID[3:2]), .in1(2'b00), .out(ra_ID), .sel(MUX_Type));
  Hazard_Detectation_Unit hazard_detectation_unit_1 (
    .Opcode_ID_EX(Opcode_ID_EX), .Opcode_ID(Instrucao_IF_ID), .ra_ID(ra_ID), .rd_ID_EX(rd_ID_EX),
    .rb_ID(Imediato_ID[1:0]), .PCWrite(PCWrite_Hazard), .Stall(Stall));
  Banco_de_Registradores banco_de_registradores_1 (
    .Reset(Reset), .clk(clk_mem), .RegIn(Data_WB), .RegWrite(RegWrite_MEM_WB), .rd(rd_MEM_WB), .ra(ra_ID),
    .rb(Imediato_ID[1:0]), .R_ra(R_ra_ID), .R_rb(R_rb_ID));
  Multiplexer #(.width(3)) multiplexer_2 (.in0(ALUOp_ID), .in1(3'b100), .out(multiplexer_2_out), .sel(Reset_ID_EX));
  Multiplexer multiplexer_3 (.in0(MUX_ULA_B_ID), .in1(1'b1), .out(multiplexer_3_out), .sel(Reset_ID_EX));
  Multiplexer multiplexer_4 (.in0(Branch_ID), .in1(1'b0), .out(multiplexer_4_out), .sel(Reset_ID_EX));
  Multiplexer multiplexer_5 (.in0(JAR_ID), .in1(1'b0), .out(multiplexer_5_out), .sel(Reset_ID_EX));
  Multiplexer multiplexer_6 (.in0(MUX_SumPC_ID), .in1(1'b0), .out(multiplexer_6_out), .sel(Reset_ID_EX));
  Multiplexer multiplexer_7 (.in0(MemWrite_ID), .in1(1'b0), .out(multiplexer_7_out), .sel(Reset_ID_EX));
  Multiplexer multiplexer_8 (.in0(RegWrite_ID), .in1(1'b0), .out(multiplexer_8_out), .sel(Reset_ID_EX));
  Multiplexer #(.width(2)) multiplexer_9 (.in0(MUX_RegIn_ID), .in1(2'b00), .out(multiplexer_9_out), .sel(Reset_ID_EX));
  Multiplexer multiplexer_10 (.in0(PredictTaken_IF_ID), .in1(1'b0), .out(multiplexer_10_out), .sel(Reset_ID_EX));
  Multiplexer #(.width(8)) multiplexer_11 (
    .in0(PC_Out_IF_ID), .in1({8{1'b0}}), .out(multiplexer_11_out), .sel(Reset_ID_EX));
  Multiplexer #(.width(8)) multiplexer_12 (.in0(R_ra_ID), .in1({8{1'b0}}), .out(multiplexer_12_out), .sel(Reset_ID_EX));
  Multiplexer #(.width(8)) multiplexer_13 (.in0(R_rb_ID), .in1({8{1'b0}}), .out(multiplexer_13_out), .sel(Reset_ID_EX));
  Multiplexer #(.width(8)) multiplexer_14 (
    .in0(Imm_Ext_ID), .in1({8{1'b0}}), .out(multiplexer_14_out), .sel(Reset_ID_EX));
  Multiplexer #(.width(2)) multiplexer_15 (.in0(ra_ID), .in1(2'b00), .out(multiplexer_15_out), .sel(Reset_ID_EX));
  Multiplexer #(.width(2)) multiplexer_16 (.in0(ra_ID), .in1(2'b00), .out(multiplexer_16_out), .sel(Reset_ID_EX));
  Multiplexer #(.width(2)) multiplexer_17 (
    .in0(Imediato_ID[1:0]), .in1(2'b00), .out(multiplexer_17_out), .sel(Reset_ID_EX));
  Multiplexer #(.width(4)) multiplexer_18 (
    .in0(Instrucao_IF_ID), .in1(4'b0100), .out(multiplexer_18_out), .sel(Reset_ID_EX));
  Register #(.width(3)) u_ALUop_ID_EX (.D(multiplexer_2_out), .Q(ALUOp_ID_EX), .clk(clk_proc));  // open: en, clr
  Register #(.width(1)) u_MUX_ULA_B_ID_EX (
    .D(multiplexer_3_out), .Q(MUX_ULA_B_ID_EX), .clk(clk_proc));  // open: en, clr
  Register #(.width(1)) u_Branch_ID_EX (.D(multiplexer_4_out), .Q(Branch_ID_EX), .clk(clk_proc));  // open: en, clr
  Register #(.width(1)) u_JAR_ID_EX (.D(multiplexer_5_out), .Q(JAR_ID_EX), .clk(clk_proc));  // open: en, clr
  Register #(.width(1)) u_Mux_SumPC_ID_EX (
    .D(multiplexer_6_out), .Q(MUX_SumPC_ID_EX), .clk(clk_proc));  // open: en, clr
  Register #(.width(1)) u_MemWrite_ID_EX (.D(multiplexer_7_out), .Q(MemWrite_ID_EX), .clk(clk_proc));  // open: en, clr
  Register #(.width(1)) u_RegWrite_ID_EX (.D(multiplexer_8_out), .Q(RegWrite_ID_EX), .clk(clk_proc));  // open: en, clr
  Register #(.width(2)) u_MUX_RegIn_ID_EX (
    .D(multiplexer_9_out), .Q(MUX_RegIn_ID_EX), .clk(clk_proc));  // open: en, clr
  Register #(.width(1)) u_PredictTaken_ID_EX (
    .D(multiplexer_10_out), .Q(PredictTaken_ID_EX), .clk(clk_proc));  // open: en, clr
  Register u_PC_Out_ID_EX (.D(multiplexer_11_out), .Q(PC_Out_ID_EX), .clk(clk_proc));  // open: en, clr
  Register u_R_ra_ID_EX (.D(multiplexer_12_out), .Q(R_ra_ID_EX), .clk(clk_proc));  // open: en, clr
  Register u_R_rb_ID_EX (.D(multiplexer_13_out), .Q(R_rb_ID_EX), .clk(clk_proc));  // open: en, clr
  Register u_Imm_Ext_ID_EX (.D(multiplexer_14_out), .Q(Imm_Ext_ID_EX), .clk(clk_proc));  // open: en, clr
  Register #(.width(2)) u_rd_ID_EX (.D(multiplexer_15_out), .Q(rd_ID_EX), .clk(clk_proc));  // open: en, clr
  Register #(.width(2)) u_ra_ID_EX (.D(multiplexer_16_out), .Q(ra_ID_EX), .clk(clk_proc));  // open: en, clr
  Register #(.width(2)) u_rb_ID_EX (.D(multiplexer_17_out), .Q(rb_ID_EX), .clk(clk_proc));  // open: en, clr
  Register #(.width(4)) u_Opcode_ID_EX (.D(multiplexer_18_out), .Q(Opcode_ID_EX), .clk(clk_proc));  // open: en, clr
  Unidade_Forwarding unidade_forwarding_1 (
    .RegWrite_MEM_WB(RegWrite_MEM_WB), .RegWrite_EX_MEM(RegWrite_EX_MEM), .ra_ID_EX(ra_ID_EX),
    .rb_ID_EX(rb_ID_EX), .rd_MEM(rd_EX_MEM), .rd_WB(rd_MEM_WB), .Opcode_ID_EX(Opcode_ID_EX),
    .ULA_Out(ULA_OUT_EX_MEM), .Imm_Ext(Imm_Ext_EX_MEM), .Upper_Immediate(Upper_Imm_EX_MEM),
    .MUX_RegIn_EX_MEM(MUX_RegIn_EX_MEM), .FwA(FwA), .FwB(FwB), .Data_EX_MEM(Data_EX_MEM));
  Multiplexer #(.width(8)) multiplexer_19 (
    .in0(R_rb_ID_EX), .in1(Imm_Ext_ID_EX), .out(R_rb_EX_1), .sel(MUX_ULA_B_ID_EX));
  Multiplexer #(.select(2), .width(8)) multiplexer_20 (
    .in0(R_ra_ID_EX), .in1(Data_EX_MEM), .in2(Data_WB), .out(R_ra_EX), .sel(FwA));  // open: in3
  Multiplexer #(.select(2), .width(8)) multiplexer_21 (
    .in0(R_rb_EX_1), .in1(Data_EX_MEM), .in2(Data_WB), .out(R_rb_EX_2), .sel(FwB));  // open: in3
  Shifter shifter_1 (.in(Imm_Ext_ID_EX), .\dist (3'b100), .out(Upper_Imm_EX));
  Condicao_de_Salto condicao_de_salto_1 (.JAR(JAR_ID_EX), .Branch(Branch_ID_EX), .R_ra(R_ra_EX), .Taken(Taken_1));
  ULA ula_1 (.ULA_A(R_ra_EX), .ULA_B(R_rb_EX_2), .ALUOp(ALUOp_ID_EX), .ULA_OUT(ULA_OUT_EX));
  Multiplexer #(.width(8)) multiplexer_22 (
    .in0(8'h1), .in1(Imm_Ext_ID_EX), .out(multiplexer_22_out), .sel(MUX_SumPC_ID_EX));
  Adder adder_1 (.a(PC_Out_ID_EX), .b(multiplexer_22_out), .out(adder_1_out));  // open: cin, cout
  BTB_e_Preditor btb_e_preditor_1 (
    .clk(clk_proc), .Taken_EX(Taken_EX), .JI_ID_EX(MUX_SumPC_ID_EX), .JAR_ID_EX(JAR_ID_EX),
    .Branch_ID_EX(Branch_ID_EX), .PC_Salto_EX(PC_Salto_EX), .PC_Out_ID_EX(PC_Out_ID_EX),
    .PC_Out_IF(PC_Out_IF), .PredictTaken(PredictTaken_IF), .Endereco_Previsto(Endereco_Previsto_IF));
  Multiplexer #(.width(8)) multiplexer_23 (.in0(adder_1_out), .in1(R_rb_EX_2), .out(PC_Salto_EX), .sel(Taken_1));
  or or_1 (Taken_EX, Taken_1, MUX_SumPC_ID_EX);
  Adder adder_2 (.a(PC_Out_IF), .b(8'h1), .out(adder_2_out));  // open: cin, cout
  xor xor_1 (Flush, PredictTaken_ID_EX, Taken_EX);
  Multiplexer #(.width(8)) multiplexer_24 (
    .in0(adder_2_out), .in1(Endereco_Previsto_IF), .out(multiplexer_24_out), .sel(PredictTaken_IF));
  Multiplexer #(.width(8)) multiplexer_25 (.in0(multiplexer_24_out), .in1(PC_Salto_EX), .out(PC_Next), .sel(Flush));
  or or_2 (or_2_out, Flush, PCWrite_Hazard);
  Register u_ULA_OUT_EX_MEM (.D(ULA_OUT_EX), .Q(ULA_OUT_EX_MEM), .clk(clk_proc), .clr(Reset_EX_MEM));  // open: en
  Register u_Upper_Imm_EX_MEM (.D(Upper_Imm_EX), .Q(Upper_Imm_EX_MEM), .clk(clk_proc), .clr(Reset_EX_MEM));  // open: en
  Register u_R_ra_EX_MEM (.D(R_ra_EX), .Q(R_ra_EX_MEM), .clk(clk_proc), .clr(Reset_EX_MEM));  // open: en
  Register u_R_rb_EX_MEM (.D(R_rb_EX_2), .Q(R_rb_EX_MEM), .clk(clk_proc), .clr(Reset_EX_MEM));  // open: en
  Register #(.width(2)) u_rd_EX_MEM (.D(rd_ID_EX), .Q(rd_EX_MEM), .clk(clk_proc), .clr(Reset_EX_MEM));  // open: en
  Register u_Imm_Ext_EX_MEM (.D(Imm_Ext_ID_EX), .Q(Imm_Ext_EX_MEM), .clk(clk_proc), .clr(Reset_EX_MEM));  // open: en
  Register #(.width(1)) u_MemWrite_EX_MEM (
    .D(MemWrite_ID_EX), .Q(MemWrite_EX_MEM), .clk(clk_proc), .clr(Reset_EX_MEM));  // open: en
  Register #(.width(1)) u_RegWrite_EX_MEM (
    .D(RegWrite_ID_EX), .Q(RegWrite_EX_MEM), .clk(clk_proc), .clr(Reset_EX_MEM));  // open: en
  Register #(.width(2)) u_MUX_RegIn_EX_MEM (
    .D(MUX_RegIn_ID_EX), .Q(MUX_RegIn_EX_MEM), .clk(clk_proc), .clr(Reset_EX_MEM));  // open: en
  PC pc_1 (.PC_In(PC_Next), .PCWrite(or_2_out), .clk(clk_proc), .Reset(Reset_PC), .PC_Out(PC_Out_IF));
  Clock #(.phaseOffset(3)) u_clk_mem (.out(clk_mem));
  Clock #(.highDuration(2), .lowDuration(2), .phaseOffset(3)) clk_processador (.out(clk_proc));
  // DualRAM #(.asyncread("true"), .clearpin("true")) dualram_1: pin names not known; wires that end beside it: dualram_1_p1, PC_Out_IF, 1'b0, 1'b1, clk_mem, {8{1'b0}}, R_rb_EX_MEM, MemWrite_EX_MEM, 1'b1, clk_mem, R_ra_EX_MEM, Instrucao_IF, MemDataOut_MEM
  // Digital_Oscilloscope digital_oscilloscope_1: pin names not known; wires that end beside it: clk_mem, clk_proc
  Multiplexer multiplexer_26 (.in0(PredictTaken_IF), .in1(1'b0), .out(multiplexer_26_out), .sel(Reset_IF_ID));
  Multiplexer #(.width(8)) multiplexer_27 (
    .in0(PC_Out_IF), .in1({8{1'b0}}), .out(multiplexer_27_out), .sel(Reset_IF_ID));
  Multiplexer #(.width(8)) multiplexer_28 (
    .in0(Instrucao_IF), .in1(8'h64), .out(multiplexer_28_out), .sel(Reset_IF_ID));
  Register #(.width(1)) u_PredictTaken_IF_ID (
    .D(multiplexer_26_out), .en(Write_IF_ID), .Q(PredictTaken_IF_ID), .clk(clk_proc));  // open: clr
  Register u_PC_Out_IF_ID (.D(multiplexer_27_out), .en(Write_IF_ID), .Q(PC_Out_IF_ID), .clk(clk_proc));  // open: clr
  Register u_Instrucao_IF_ID (
    .D(multiplexer_28_out), .en(Write_IF_ID), .Q({Instrucao_IF_ID, Imediato_ID}), .clk(clk_proc));  // open: clr
  Register #(.width(1)) u_RegWrite_MEM_WB (
    .D(RegWrite_EX_MEM), .Q(RegWrite_MEM_WB), .clk(clk_proc), .clr(Reset));  // open: en
  Register #(.width(2)) u_MUX_RegIn_MEM_WB (
    .D(MUX_RegIn_EX_MEM), .Q(MUX_RegIn_MEM_WB), .clk(clk_proc), .clr(Reset));  // open: en
  Register u_ULA_Out_MEM_WB (.D(ULA_OUT_EX_MEM), .Q(ULA_OUT_MEM_WB), .clk(clk_proc), .clr(Reset));  // open: en
  Register u_MemDataOut_MEM_WB (.D(MemDataOut_MEM), .Q(MemDataOut_MEM_WB), .clk(clk_proc), .clr(Reset));  // open: en
  Register u_Imm_Ext_MEM_WB (.D(Imm_Ext_EX_MEM), .Q(Imm_Ext_MEM_WB), .clk(clk_proc), .clr(Reset));  // open: en
  Register u_Upper_Imm_MEM_WB (.D(Upper_Imm_EX_MEM), .Q(Upper_Imm_MEM_WB), .clk(clk_proc), .clr(Reset));  // open: en
  Register #(.width(2)) u_rd_MEM_WB (.D(rd_EX_MEM), .Q(rd_MEM_WB), .clk(clk_proc), .clr(Reset));  // open: en
  Multiplexer #(.select(2), .width(8)) multiplexer_29 (
    .in0(ULA_OUT_MEM_WB), .in1(MemDataOut_MEM_WB), .in2(Imm_Ext_MEM_WB), .in3(Upper_Imm_MEM_WB),
    .out(Data_WB), .sel(MUX_RegIn_MEM_WB));

  // Other names for the same wires on the sheet: Instrucao_IF_ID[3:0] = Imediato_ID; rb_ID[1:0] = Imediato_ID[1:0];
  //   ra[1:0] = Imediato_ID[3:2]; Opcode_ID[3:0] = Instrucao_IF_ID; MUX_Type_ID = MUX_Type; Taken_2 = MUX_SumPC_ID_EX

  // Notes on the sheet:
  //   I. DECODE (ID)
  //   ID/EX
  //   EXECUTE (EX)
  //   Cálculo do Salto
  //   Previção Certa?
  //   Cálculo de PC_Next: PC + 1 ou Endereço Previsto ou Correção de Salto
  //   EX/MEM
  //   I. FETCH (IF)
  //   Memória de Instruções
  //   MEMORY (MEM)
  //   Memória de Dados
  //   IF/ID
  //   MEM/WB
  //   WRITE BACK (WB)
endmodule

module Banco_de_Registradores (
  input  Reset,
  input  clk,
  input  [7:0] RegIn,
  input  RegWrite,
  input  [1:0] rd,
  input  [1:0] ra,
  input  [1:0] rb,
  output [7:0] R_ra,
  output [7:0] R_rb
);

  wire decoder_1_out0, decoder_1_out1, decoder_1_out2, decoder_1_out3;
  wire [7:0] registradores_1_r_r0, registradores_1_r_r1, registradores_1_r_r2, registradores_1_r_r3;

  Decoder #(.enable("false"), .select(2)) decoder_1 (
    .out0(decoder_1_out0), .out1(decoder_1_out1), .out2(decoder_1_out2), .out3(decoder_1_out3), .sel(rd));
  Registradores registradores_1 (
    .RegWrite(RegWrite), .RegIn(RegIn), .clk(clk), .En0(decoder_1_out0), .Reset(Reset), .En1(decoder_1_out1),
    .En2(decoder_1_out2), .En3(decoder_1_out3), .R_r0(registradores_1_r_r0), .R_r1(registradores_1_r_r1),
    .R_r2(registradores_1_r_r2), .R_r3(registradores_1_r_r3));
  Multiplexer #(.select(2), .width(8)) multiplexer_1 (
    .in0(registradores_1_r_r0), .in1(registradores_1_r_r1), .in2(registradores_1_r_r2),
    .in3(registradores_1_r_r3), .out(R_ra), .sel(ra));
  Multiplexer #(.select(2), .width(8)) multiplexer_2 (
    .in0(registradores_1_r_r0), .in1(registradores_1_r_r1), .in2(registradores_1_r_r2),
    .in3(registradores_1_r_r3), .out(R_rb), .sel(rb));
endmodule

module Registradores (
  input  RegWrite,
  input  [7:0] RegIn,
  input  clk,
  input  En0,
  input  Reset,
  input  En1,
  input  En2,
  input  En3,
  output [7:0] R_r0,
  output [7:0] R_r1,
  output [7:0] R_r2,
  output [7:0] R_r3
);

  wire and_1_out, and_2_out, and_3_out, and_4_out;

  and and_1 (and_1_out, En0, RegWrite);
  and and_2 (and_2_out, En1, RegWrite);
  and and_3 (and_3_out, En2, RegWrite);
  and and_4 (and_4_out, En3, RegWrite);
  Register r0 (.D(RegIn), .en(and_1_out), .clk(clk), .Q(R_r0), .clr(Reset));
  Register r1 (.D(RegIn), .en(and_2_out), .clk(clk), .Q(R_r1), .clr(Reset));
  Register r2 (.D(RegIn), .en(and_3_out), .clk(clk), .Q(R_r2), .clr(Reset));
  Register r3 (.D(RegIn), .en(and_4_out), .clk(clk), .Q(R_r3), .clr(Reset));
endmodule

module PC (
  input  [7:0] PC_In,
  input  PCWrite,
  input  clk,
  input  Reset,
  output [7:0] PC_Out
);

  Register register_1 (.D(PC_In), .en(PCWrite), .clk(clk), .Q(PC_Out), .clr(Reset));
endmodule

module ULA (
  input  [7:0] ULA_A,
  input  [7:0] ULA_B,
  input  [2:0] ALUOp,
  output [7:0] ULA_OUT
);

  wire [7:0] adder_1_out, and_1_out, negator_1_out, or_1_out, shift_right_1_ula_out, shifter_left_1_ula_out,
       subtractor_1_out, xor_1_out;

  Negator negator_1 (.in(ULA_B), .out(negator_1_out));
  assign and_1_out = ULA_A & ULA_B;  // AND_Gate and_1, 8 bits wide
  assign or_1_out = ULA_A | ULA_B;  // OR_Gate or_1, 8 bits wide
  Adder adder_1 (.a(ULA_A), .b(ULA_B), .out(adder_1_out));  // open: cin, cout
  Subtractor subtractor_1 (.a(ULA_A), .b(ULA_B), .out(subtractor_1_out));  // open: bin, bout
  assign xor_1_out = ULA_A ^ ULA_B;  // XOR_Gate xor_1, 8 bits wide
  Shifter_Left shifter_left_1 (.ULA_A(ULA_A), .ULA_B(ULA_B), .ULA_OUT(shifter_left_1_ula_out));
  Shift_Right shift_right_1 (.ULA_A(ULA_A), .ULA_B(ULA_B), .ULA_OUT(shift_right_1_ula_out));
  Multiplexer #(.select(3), .width(8)) multiplexer_1 (
    .in0(negator_1_out), .in1(and_1_out), .in2(or_1_out), .in3(xor_1_out), .in4(adder_1_out),
    .in5(subtractor_1_out), .in6(shifter_left_1_ula_out), .in7(shift_right_1_ula_out), .out(ULA_OUT),
    .sel(ALUOp));
endmodule

module Condicao_de_Salto (
  input  JAR,
  input  Branch,
  input  [7:0] R_ra,
  output Taken
);

  wire and_1_out, nor_1_out;

  and and_1 (and_1_out, Branch, nor_1_out);
  nor nor_1 (nor_1_out, R_ra[0], R_ra[1], R_ra[2], R_ra[3], R_ra[4], R_ra[5], R_ra[6], R_ra[7]);
  or or_1 (Taken, JAR, and_1_out);

  // Notes on the sheet:
  //   Se 'for branch' e R[r0] == 0 OU 'for salto incondional', então desvie
endmodule

module Proximo_PC (
  input  MUX_PC,
  input  [7:0] PC_OUT,
  input  [7:0] Imm_Ext,
  input  [7:0] R_rb,
  input  MUX_SumPC,
  output [7:0] PC_In
);

  wire [7:0] adder_1_out, multiplexer_1_out;

  Multiplexer #(.width(8)) multiplexer_1 (.in0(8'h1), .in1(Imm_Ext), .out(multiplexer_1_out), .sel(MUX_SumPC));
  Multiplexer #(.width(8)) multiplexer_2 (.in0(adder_1_out), .in1(R_rb), .out(PC_In), .sel(MUX_PC));
  Adder adder_1 (.a(PC_OUT), .b(multiplexer_1_out), .out(adder_1_out));  // open: cin, cout
endmodule

module Shifter_Left (
  input  [7:0] ULA_A,
  input  [7:0] ULA_B,
  output [7:0] ULA_OUT
);

  wire or_1_out;
  wire [7:0] shifter_1_out;

  Shifter shifter_1 (.in(ULA_A), .\dist (ULA_B[2:0]), .out(shifter_1_out));
  Multiplexer #(.width(8)) multiplexer_1 (.in0(shifter_1_out), .in1({8{1'b0}}), .out(ULA_OUT), .sel(or_1_out));
  or or_1 (or_1_out, ULA_B[3], ULA_B[4], ULA_B[5], ULA_B[6], ULA_B[7]);

  // Notes on the sheet:
  //   Se o shift tiver overflow, então o resultado do shift será 0
endmodule

module Shift_Right (
  input  [7:0] ULA_A,
  input  [7:0] ULA_B,
  output [7:0] ULA_OUT
);

  wire or_1_out;
  wire [7:0] shifter_1_out;

  Shifter #(.shift("lr")) shifter_1 (.in(ULA_A), .\dist (ULA_B[2:0]), .out(shifter_1_out));
  Multiplexer #(.width(8)) multiplexer_1 (.in0(shifter_1_out), .in1({8{1'b0}}), .out(ULA_OUT), .sel(or_1_out));
  or or_1 (or_1_out, ULA_B[3], ULA_B[4], ULA_B[5], ULA_B[6], ULA_B[7]);

  // Notes on the sheet:
  //   Se o shift tiver overflow, então o resultado do shift será 0
endmodule

module Unidade_de_Controle (
  input  [3:0] opcode,
  output MUX_Type,
  output [2:0] ALUOp,
  output MUX_ULA_B,
  output Branch,
  output JAR,
  output MUX_SumPC,
  output MemWrite,
  output RegWrite,
  output [1:0] MUX_RegIn
);

  wire and_1_out, and_2_out, and_3_out, and_4_out, and_5_out, and_10_out, and_11_out, and_12_out, and_13_out,
       not_1_out, not_2_out, not_3_out, not_4_out;

  not not_1 (not_1_out, opcode[3]);
  not not_2 (not_2_out, opcode[2]);
  not not_3 (not_3_out, opcode[1]);
  not not_4 (not_4_out, opcode[0]);
  and and_1 (and_1_out, not_1_out, not_3_out, opcode[0]);
  and and_2 (and_2_out, not_1_out, opcode[2], not_4_out);
  and and_3 (and_3_out, not_1_out, not_3_out);
  and and_4 (and_4_out, not_1_out, opcode[0]);
  and and_5 (and_5_out, not_1_out, opcode[2]);
  and and_6 (Branch, not_1_out, not_2_out, not_3_out, not_4_out);
  and and_7 (JAR, not_1_out, opcode[2], opcode[1], opcode[0]);
  and and_8 (MUX_SumPC, not_1_out, not_2_out, not_3_out, opcode[0]);
  and and_9 (MemWrite, not_1_out, not_2_out, opcode[1], opcode[0]);
  and and_10 (and_10_out, opcode[1], not_4_out);
  and and_11 (and_11_out, opcode[2], not_3_out);
  and and_12 (and_12_out, not_1_out, opcode[0]);
  and and_13 (and_13_out, not_1_out, opcode[2], opcode[1]);
  and and_14 (MUX_RegIn[0], not_1_out, opcode[1]);
  or or_1 (MUX_Type, and_1_out, and_2_out);
  or or_2 (MUX_ULA_B, and_3_out, and_4_out, and_5_out);
  or or_3 (RegWrite, and_10_out, and_11_out, opcode[3]);
  or or_4 (MUX_RegIn[1], and_12_out, and_13_out);

  assign ALUOp = opcode[2:0];
endmodule

module Teste_clk (
);

  wire clock_1_out, clock_2_out;

  Clock #(.phaseOffset(3)) clock_1 (.out(clock_1_out));
  Clock #(.highDuration(2), .lowDuration(2), .phaseOffset(3)) clock_2 (.out(clock_2_out));
  // Digital_Oscilloscope digital_oscilloscope_1: pin names not known; wires that end beside it: clock_1_out, clock_2_out
endmodule

module Controle_Forwading (
  input  ra_igual_rd_MEM,
  input  rb_igual_rd_MEM,
  input  ra_igual_rd_WB,
  input  rb_igual_rd_WB,
  output [1:0] ForwardA,
  output [1:0] ForwardB
);

  wire not_1_out, not_2_out;

  not not_1 (not_1_out, ra_igual_rd_MEM);
  not not_2 (not_2_out, rb_igual_rd_MEM);
  and and_1 (ForwardA[1], not_1_out, ra_igual_rd_WB);
  and and_2 (ForwardB[1], not_2_out, rb_igual_rd_WB);

  assign ForwardA[0] = ra_igual_rd_MEM;
  assign ForwardB[0] = rb_igual_rd_MEM;
endmodule

// UnidadeFowarding
module Unidade_Forwarding (
  input  RegWrite_MEM_WB,
  input  RegWrite_EX_MEM,
  input  [1:0] ra_ID_EX,
  input  [1:0] rb_ID_EX,
  input  [1:0] rd_MEM,
  input  [1:0] rd_WB,
  input  [3:0] Opcode_ID_EX,
  input  [7:0] ULA_Out,
  input  [7:0] Imm_Ext,
  input  [7:0] Upper_Immediate,
  input  [1:0] MUX_RegIn_EX_MEM,
  output [1:0] FwA,
  output [1:0] FwB,
  output [7:0] Data_EX_MEM
);

  wire and_1_out, and_2_out, and_3_out, and_4_out, comparator_1_eq, comparator_2_eq, comparator_3_eq,
       comparator_4_eq, detector_de_leitura_1_regreada, detector_de_leitura_1_regreadb;
  wire [1:0] controle_forwading_1_forwarda, controle_forwading_1_forwardb;

  Comparator #(.width(2)) comparator_1 (.a(ra_ID_EX), .b(rd_MEM), .eq(comparator_1_eq));  // open: gt, lt
  Comparator #(.width(2)) comparator_2 (.a(rb_ID_EX), .b(rd_MEM), .eq(comparator_2_eq));  // open: gt, lt
  Comparator #(.width(2)) comparator_3 (.a(ra_ID_EX), .b(rd_WB), .eq(comparator_3_eq));  // open: gt, lt
  Comparator #(.width(2)) comparator_4 (.a(rb_ID_EX), .b(rd_WB), .eq(comparator_4_eq));  // open: gt, lt
  Multiplexer #(.select(2), .width(8)) multiplexer_1 (
    .in0(ULA_Out), .in2(Imm_Ext), .in3(Upper_Immediate), .out(Data_EX_MEM), .sel(MUX_RegIn_EX_MEM));  // open: in1
  and and_1 (and_1_out, RegWrite_EX_MEM, comparator_1_eq);
  and and_2 (and_2_out, RegWrite_EX_MEM, comparator_2_eq);
  and and_3 (and_3_out, RegWrite_MEM_WB, comparator_3_eq);
  and and_4 (and_4_out, RegWrite_MEM_WB, comparator_4_eq);
  Controle_Forwading controle_forwading_1 (
    .ra_igual_rd_MEM(and_1_out), .rb_igual_rd_MEM(and_2_out), .ra_igual_rd_WB(and_3_out),
    .rb_igual_rd_WB(and_4_out), .ForwardA(controle_forwading_1_forwarda),
    .ForwardB(controle_forwading_1_forwardb));
  Detector_de_Leitura detector_de_leitura_1 (
    .Opcode(Opcode_ID_EX), .RegReadA(detector_de_leitura_1_regreada),
    .RegReadB(detector_de_leitura_1_regreadb));
  Multiplexer #(.width(2)) multiplexer_2 (
    .in0(2'b00), .in1(controle_forwading_1_forwarda), .out(FwA), .sel(detector_de_leitura_1_regreada));
  Multiplexer #(.width(2)) multiplexer_3 (
    .in0(2'b00), .in1(controle_forwading_1_forwardb), .out(FwB), .sel(detector_de_leitura_1_regreadb));

  // Notes on the sheet:
  //   RegWrite
endmodule

module Detector_de_Leitura (
  input  [3:0] Opcode,
  output RegReadA,
  output RegReadB
);

  wire and_1_out, and_2_out, and_3_out, and_4_out, and_5_out, and_6_out, and_7_out, and_8_out, and_9_out,
       not_1_out, not_2_out, not_3_out, not_4_out;

  not not_1 (not_1_out, Opcode[3]);
  not not_2 (not_2_out, Opcode[2]);
  not not_3 (not_3_out, Opcode[1]);
  not not_4 (not_4_out, Opcode[0]);
  and and_1 (and_1_out, not_2_out, Opcode[1]);
  and and_2 (and_2_out, Opcode[3], Opcode[0]);
  and and_3 (and_3_out, not_1_out, not_3_out, not_4_out);
  and and_4 (and_4_out, Opcode[3], Opcode[2]);
  and and_5 (and_5_out, not_1_out, not_2_out, not_4_out);
  and and_6 (and_6_out, Opcode[1], Opcode[0]);
  and and_7 (and_7_out, Opcode[3], Opcode[0]);
  and and_8 (and_8_out, Opcode[3], Opcode[2]);
  and and_9 (and_9_out, not_2_out, Opcode[1]);
  or or_1 (RegReadA, and_1_out, and_2_out, and_3_out, and_4_out);
  or or_2 (RegReadB, and_5_out, and_6_out, and_7_out, and_8_out, and_9_out);
endmodule

module Hazard_Detectation_Unit (
  input  [3:0] Opcode_ID_EX,
  input  [3:0] Opcode_ID,
  input  [1:0] ra_ID,
  input  [1:0] rd_ID_EX,
  input  [1:0] rb_ID,
  output PCWrite,
  output Stall
);

  wire and_1_out, and_2_out, and_3_out, comparator_1_eq, comparator_2_eq, detector_de_leitura_1_regreada,
       detector_de_leitura_1_regreadb, or_1_out;

  and and_1 (and_1_out, ~Opcode_ID_EX[0], Opcode_ID_EX[1], ~Opcode_ID_EX[2], ~Opcode_ID_EX[3]);  // AND_Gate
  Comparator #(.width(2)) comparator_1 (.a(ra_ID), .b(rd_ID_EX), .eq(comparator_1_eq));  // open: gt, lt
  Comparator #(.width(2)) comparator_2 (.a(rd_ID_EX), .b(rb_ID), .eq(comparator_2_eq));  // open: gt, lt
  Detector_de_Leitura detector_de_leitura_1 (
    .Opcode(Opcode_ID), .RegReadA(detector_de_leitura_1_regreada), .RegReadB(detector_de_leitura_1_regreadb));
  and and_2 (and_2_out, detector_de_leitura_1_regreada, comparator_1_eq);
  and and_3 (and_3_out, detector_de_leitura_1_regreadb, comparator_2_eq);
  or or_1 (or_1_out, and_2_out, and_3_out);
  and and_4 (Stall, and_1_out, or_1_out);
  not not_1 (PCWrite, Stall);

  // Notes on the sheet:
  //   É Load
  //   Existe dependência
  //   Stall
endmodule

module BTB_e_Preditor (
  input  clk,
  input  Taken_EX,
  input  JI_ID_EX,
  input  JAR_ID_EX,
  input  Branch_ID_EX,
  input  [7:0] PC_Salto_EX,
  input  [7:0] PC_Out_ID_EX,
  input  [7:0] PC_Out_IF,
  output PredictTaken,
  output [7:0] Endereco_Previsto
);

  wire Bit_de_Validade, comparator_1_eq, Estado, Operacao_Salto;
  wire [0:0] Estado_Atual;
  wire [1:0] NovoEstado;
  wire [3:0] BTB_Endereco, Index;

  or or_1 (Operacao_Salto, JI_ID_EX, JAR_ID_EX, Branch_ID_EX);
  Multiplexer #(.width(4)) multiplexer_1 (
    .in0(PC_Out_IF[3:0]), .in1(PC_Out_ID_EX[3:0]), .out(Index), .sel(Operacao_Salto));
  RAM #(.addrWidth(4), .asyncread("true"), .dataWidth(4)) Endereco_Instrucao (
    .addr(Index), .we(Operacao_Salto), .oe(1'b1), .clk(clk), .din(PC_Out_ID_EX[7:4]), .dout(BTB_Endereco));
  RAM #(.addrWidth(4), .asyncread("true")) Endereco_Desvio (
    .addr(Index), .we(Operacao_Salto), .oe(1'b1), .clk(clk), .din(PC_Salto_EX), .dout(Endereco_Previsto));
  RAM #(.addrWidth(4), .asyncread("true"), .dataWidth(1)) Validade (
    .addr(Index), .we(Operacao_Salto), .oe(1'b1), .clk(clk), .din(1'b1), .dout(Bit_de_Validade));
  RAM #(.addrWidth(4), .asyncread("true"), .dataWidth(2)) u_Estado (
    .addr(Index), .we(Operacao_Salto), .oe(1'b1), .clk(clk), .din(NovoEstado),
    .dout({Estado, Estado_Atual[0]}));
  Novo_Estado novo_estado_1 (.Estado_Atual({Estado, Estado_Atual[0]}), .Taken(Taken_EX), .Novo_Estado(NovoEstado));
  Comparator #(.width(4)) comparator_1 (.a(BTB_Endereco), .b(PC_Out_IF[7:4]), .eq(comparator_1_eq));  // open: gt, lt
  and and_1 (PredictTaken, Estado, Bit_de_Validade, ~Operacao_Salto, comparator_1_eq);  // AND_Gate

  // Other names for the same wires on the sheet: Estado_Atual[1] = Estado; PC_Out_ID_EX_0_3[3:0] = PC_Out_ID_EX[3:0];
  //   PC_Out_ID_EX_4_7[3:0] = PC_Out_ID_EX[7:4]; PC_Out_IF_0_3[3:0] = PC_Out_IF[3:0];
  //   PC_Out_IF_4_7[3:0] = PC_Out_IF[7:4]

  // Notes on the sheet:
  //   Taken?
  //   Valid?
  //   Esta lendo?
  //   Hit?
endmodule

module Novo_Estado (
  input  [1:0] Estado_Atual,
  input  Taken,
  output [1:0] Novo_Estado
);

  wire and_1_out, and_2_out, and_3_out, and_4_out, and_5_out, and_6_out, not_1_out;

  not not_1 (not_1_out, Estado_Atual[0]);
  and and_1 (and_1_out, Estado_Atual[0], Taken);
  and and_2 (and_2_out, Estado_Atual[1], Taken);
  and and_3 (and_3_out, Estado_Atual[1], Estado_Atual[0]);
  and and_4 (and_4_out, not_1_out, Taken);
  and and_5 (and_5_out, Estado_Atual[1], not_1_out);
  and and_6 (and_6_out, Estado_Atual[1], Taken);
  or or_1 (Novo_Estado[1], and_1_out, and_2_out, and_3_out);
  or or_2 (Novo_Estado[0], and_4_out, and_5_out, and_6_out);
endmodule

module Unidade_de_Reset (
  input  Flush,
  input  Stall,
  input  Reset,
  output Write_IF_ID,
  output Reset_PC,
  output Reset_IF_ID,
  output Reset_ID_EX,
  output Reset_EX_MEM
);

  wire and_1_out, not_1_out, or_1_out;

  not not_1 (not_1_out, Flush);
  or or_1 (or_1_out, Stall, Flush);
  and and_1 (and_1_out, not_1_out, Stall);
  not not_2 (Write_IF_ID, and_1_out);
  or or_2 (Reset_IF_ID, Flush, Reset);
  or or_3 (Reset_ID_EX, or_1_out, Reset);

  assign Reset_EX_MEM = Reset;
  assign Reset_PC = Reset;

  // Other names for the same wires on the sheet: ResetInicial = Reset
endmodule

module Reset_Inicial (
  input  clk_mem,
  output Reset
);

  wire and_1_out, not_2_out, or_1_out, Z0, Z1;

  not not_1 (Reset, Z1);
  not not_2 (not_2_out, Z0);
  or or_1 (or_1_out, Z0, Z1);
  and and_1 (and_1_out, not_2_out, Reset);
  D_Flip_Flop d_ff_1 (.D(or_1_out), .clk(clk_mem), .Q(Z1));  // open: Qn, preset, reset
  D_Flip_Flop d_ff_2 (.D(and_1_out), .clk(clk_mem), .Q(Z0));  // open: Qn, preset, reset
endmodule
