// Logisim project teste_mem.circ as structural Verilog: 1 circuit, main circuit main
module main (
  input  [7:0] endereco
);

  RAM ram_1 ();  // open: addr, we, oe, clk, din, dout
  RAM ram_2 ();  // open: addr, we, oe, clk, din, dout
  // DualRAM dualram_1: pin names not known

  // Other names for the same wires on the sheet: end_mod_4[1:0] = endereco[1:0]
endmodule
