// Logisim project vliw.circ as structural Verilog: 16 circuits, main circuit VLIW
module VLIW (
  input  RST
);

  wire CLK, decodificador_1_branch, decodificador_1_condition, decodificador_1_jr,
       decodificador_1_l1regwrite, decodificador_1_memread, decodificador_1_memwrite,
       decodificador_1_mux_imm, decodificador_1_mux_regin, decodificador_1_mux_ula_bl3,
       decodificador_1_mux_ula_bl4, decodificador_1_regwritel3, decodificador_1_regwritel4,
       decodificador_1_relative, decodificador_1_tipo_i_lane1, decodificador_1_tipo_i_lane2, Flush,
       L1_MUX_RegIn, L1_RegWrite, l1MuxRegin, l1RegWrite, L3RegWrite, L3RegWrite2, L4RegWrite, L4RegWrite2,
       or_1_out, registrador_id_ex_1_p42, registrador_id_ex_1_p43, registrador_id_ex_1_p44,
       registrador_id_ex_1_p45, registrador_id_ex_1_p50, registrador_id_ex_1_p51, registrador_id_ex_1_p52,
       registrador_id_ex_1_p58, registrador_id_ex_1_p59, registrador_id_ex_1_p60, registrador_id_ex_1_p61,
       registrador_id_ex_1_p64, registrador_id_ex_1_p65, registrador_id_ex_1_p66, registrador_id_ex_1_p71,
       registrador_id_ex_1_p73, registrador_id_ex_1_p76, Tipo_I_L1, Tipo_I_L2, Tipo_I_L12, Tipo_I_L22;
  wire [1:0] decodificador_1_imm_l3, decodificador_1_imm_l4, decodificador_1_rd_l1, decodificador_1_rd_l3,
       decodificador_1_rd_l4, decodificador_1_sel_lane1, multiplexer_2_out, multiplexer_3_out, ra_L2addr,
       rb_addr, rb_L2addr, Rd_L1, rd_l1_t, Rd_L3, rd_l3_t, Rd_L4, rd_l4_t, ReadAddr1, ReadAddr2, ReadAddr3,
       ReadAddr4, ReadAddr5, ReadAddr6, ReadAddr7, ReadAddr8;
  wire [2:0] decodificador_1_aluopl3, decodificador_1_aluopl4, registrador_id_ex_1_p68,
       registrador_id_ex_1_p77;
  wire [3:0] decodificador_1_imm_l1, decodificador_1_imm_l2, registrador_id_ex_1_p53, registrador_id_ex_1_p54;
  wire [7:0] adder_1_out, lan1_out, lane_1_1_p14, multiplexer_1_out, multiplexer_4_out, NewPc, PC1, PC_q,
       R0_out, ReadData1, ReadData2, ReadData3, ReadData4, ReadData5, ReadData6, ReadData7, ReadData8,
       registrador_id_ex_1_p46, registrador_id_ex_1_p47, registrador_id_ex_1_p48, registrador_id_ex_1_p49,
       ULA_A, ULA_A_resultado, ULA_B, ULA_B_resultado;
  wire [31:0] instmem_1_instout, registrador_if_id_1_decoder;

  Multiplexer #(.width(8)) multiplexer_1 (.in0(adder_1_out), .in1(NewPc), .out(multiplexer_1_out), .sel(Flush));
  Register PC (.D(multiplexer_1_out), .en(1'b1), .clk(CLK), .Q(PC_q), .clr(RST));
  Clock u_CLK (.out(CLK));
  Adder adder_1 (.a(PC_q), .b(8'h1), .out(adder_1_out));  // open: cin, cout
  InstMem instmem_1 (.Address(PC_q), .InstOut(instmem_1_instout));
  Multiplexer #(.width(2)) multiplexer_2 (.in0(rd_l1_t), .in1(2'b00), .out(multiplexer_2_out), .sel(Tipo_I_L12));
  or or_1 (or_1_out, L3RegWrite2, L4RegWrite2);
  Multiplexer #(.width(2)) multiplexer_3 (.in0(rd_l3_t), .in1(rd_l4_t), .out(multiplexer_3_out), .sel(L3RegWrite2));
  Registrador_IF_ID registrador_if_id_1 (
    .ROM(instmem_1_instout), .PC(adder_1_out), .Flush(Flush), .Clock(CLK), .rst(RST), .stall(RST),
    .Decoder(registrador_if_id_1_decoder), .PC1(PC1));
  Multiplexer #(.width(8)) multiplexer_4 (.in0(ULA_A), .in1(ULA_B), .out(multiplexer_4_out), .sel(L3RegWrite2));
  reg_bank reg_bank_1 (
    .WrData1(lan1_out), .WrData2(multiplexer_4_out), .ReadAddr1(ReadAddr1), .clk(CLK), .ReadAddr2(ReadAddr2),
    .rst(RST), .ReadAddr3(ReadAddr3), .ReadAddr4(ReadAddr4), .ReadAddr5(ReadAddr5), .ReadAddr6(ReadAddr6),
    .ReadAddr7(ReadAddr7), .ReadAddr8(ReadAddr8), .WrAddr1(multiplexer_2_out), .WE1(L1_RegWrite),
    .WE2(or_1_out), .WrAddr2(multiplexer_3_out), .ReadData1(ReadData1), .ReadData2(ReadData2),
    .ReadData3(ReadData3), .ReadData4(ReadData4), .ReadData5(ReadData5), .ReadData6(ReadData6),
    .ReadData7(ReadData7), .ReadData8(ReadData8), .R0_out(R0_out));
  Decodificador decodificador_1 (
    .Instr_32b(registrador_if_id_1_decoder), .RdAddr_L1_Ra(ReadAddr1), .RdAddr_L2_Ra(ReadAddr3),
    .RdAddr_L3_Ra(ReadAddr5), .RdAddr_L4_Ra(ReadAddr7), .RdAddr_L1_Rb(ReadAddr2), .RdAddr_L2_Rb(ReadAddr4),
    .RdAddr_L3_Rb(ReadAddr6), .RdAddr_L4_Rb(ReadAddr8), .Rd_L1(decodificador_1_rd_l1),
    .Rd_L3(decodificador_1_rd_l3), .Rd_L4(decodificador_1_rd_l4), .Imm_L1(decodificador_1_imm_l1),
    .Imm_L2(decodificador_1_imm_l2), .Imm_L3(decodificador_1_imm_l3), .Imm_L4(decodificador_1_imm_l4),
    .Sel_lane1(decodificador_1_sel_lane1), .MUX_Imm(decodificador_1_mux_imm),
    .MemRead(decodificador_1_memread), .MemWrite(decodificador_1_memwrite),
    .l1RegWrite(decodificador_1_l1regwrite), .Mux_RegIn(decodificador_1_mux_regin),
    .Condition(decodificador_1_condition), .Relative(decodificador_1_relative), .JR(decodificador_1_jr),
    .Branch(decodificador_1_branch), .MUX_ULA_BL3(decodificador_1_mux_ula_bl3),
    .RegWriteL3(decodificador_1_regwritel3), .ALUOpL3(decodificador_1_aluopl3),
    .MUX_ULA_BL4(decodificador_1_mux_ula_bl4), .RegWriteL4(decodificador_1_regwritel4),
    .ALUOpL4(decodificador_1_aluopl4), .Tipo_I_lane1(decodificador_1_tipo_i_lane1),
    .Tipo_i_lane2(decodificador_1_tipo_i_lane2));  // open: Opcode_lane1
  // Registrador_ID_EX registrador_id_ex_1: pin names not known; wires that end beside it: ReadData1, ReadData2, ReadData3, ReadData4, ReadData5, ReadData6, ReadData7, ReadData8, PC1, decodificador_1_imm_l2, decodificador_1_imm_l1, decodificador_1_imm_l4, decodificador_1_imm_l3, decodificador_1_rd_l4, decodificador_1_rd_l3, decodificador_1_rd_l1, decodificador_1_relative, decodificador_1_jr, decodificador_1_branch, decodificador_1_mux_imm, decodificador_1_mux_regin, decodificador_1_l1regwrite, decodificador_1_memwrite, decodificador_1_memread, decodificador_1_mux_ula_bl4, decodificador_1_regwritel4, decodificador_1_aluopl3[0], decodificador_1_aluopl3[1], decodificador_1_aluopl3[2], decodificador_1_mux_ula_bl3, decodificador_1_regwritel3, decodificador_1_condition, decodificador_1_tipo_i_lane2, decodificador_1_tipo_i_lane1, decodificador_1_sel_lane1, decodificador_1_aluopl4[0], decodificador_1_aluopl4[1], decodificador_1_aluopl4[2], CLK, Flush, RST, registrador_id_ex_1_p42, registrador_id_ex_1_p43, registrador_id_ex_1_p44, registrador_id_ex_1_p45, registrador_id_ex_1_p46, registrador_id_ex_1_p47, registrador_id_ex_1_p48, registrador_id_ex_1_p49, registrador_id_ex_1_p50, registrador_id_ex_1_p51, registrador_id_ex_1_p52, registrador_id_ex_1_p53, registrador_id_ex_1_p54, Rd_L4, Rd_L3, Rd_L1, registrador_id_ex_1_p58, registrador_id_ex_1_p59, registrador_id_ex_1_p60, registrador_id_ex_1_p61, l1MuxRegin, l1RegWrite, registrador_id_ex_1_p64, registrador_id_ex_1_p65, registrador_id_ex_1_p66, L4RegWrite, registrador_id_ex_1_p68[0], registrador_id_ex_1_p68[1], registrador_id_ex_1_p68[2], registrador_id_ex_1_p71, L3RegWrite, registrador_id_ex_1_p73, Tipo_I_L2, Tipo_I_L1, registrador_id_ex_1_p76, registrador_id_ex_1_p77[0], registrador_id_ex_1_p77[1], registrador_id_ex_1_p77[2]
  // Extensao_reg_id_ex extensao_reg_id_ex_1: pin names not known; wires that end beside it: ReadAddr3, ReadAddr4, ReadAddr2, CLK, Flush, RST, RST, RST, RST, RST, RST, RST, ra_L2addr, rb_L2addr, rb_addr, rb_addr, rb_addr
  // lane_1 lane_1_1: pin names not known; wires that end beside it: registrador_id_ex_1_p42, registrador_id_ex_1_p43, registrador_id_ex_1_p64, registrador_id_ex_1_p65, registrador_id_ex_1_p76, registrador_id_ex_1_p61, CLK, registrador_id_ex_1_p52, lan1_out, L1_RegWrite, rb_addr, rd_l1_t, registrador_id_ex_1_p45, lane_1_1_p14
  ULA_VLIW u_ULA_A (
    .Ra(registrador_id_ex_1_p46), .Rb(registrador_id_ex_1_p47), .Imm(registrador_id_ex_1_p54),
    .MUX_ULA_B(registrador_id_ex_1_p71), .ALUOp(registrador_id_ex_1_p68), .Resultado(ULA_A_resultado));
  ULA_VLIW u_ULA_B (
    .Ra(registrador_id_ex_1_p48), .Rb(registrador_id_ex_1_p49), .Imm(registrador_id_ex_1_p53),
    .MUX_ULA_B(registrador_id_ex_1_p66), .ALUOp(registrador_id_ex_1_p77), .Resultado(ULA_B_resultado));
  // lane_2 lane_2_1: pin names not known; wires that end beside it: registrador_id_ex_1_p44, registrador_id_ex_1_p45, R0_out, registrador_id_ex_1_p51, registrador_id_ex_1_p50, registrador_id_ex_1_p60, registrador_id_ex_1_p59, registrador_id_ex_1_p58, registrador_id_ex_1_p73, lan1_out, L1_RegWrite, rd_l1_t, rb_L2addr, ra_L2addr, NewPc, Flush
  Registrador_EX_WB registrador_ex_wb_1 (
    .lane1_out(lane_1_1_p14), .ULA_A(ULA_A_resultado), .ULA_B(ULA_B_resultado), .L1_MUX_RegIn(l1MuxRegin),
    .L1_RegWrite(l1RegWrite), .Rd_L4(Rd_L4), .Rd_L3(Rd_L3), .Rd_L1(Rd_L1), .Tipo_I_L1(Tipo_I_L1),
    .Tipo_I_L2(Tipo_I_L2), .L4_RegWrite(L4RegWrite), .L3_RegWrite(L3RegWrite), .CLK(CLK), .rst(RST),
    .lane1_outS(lan1_out), .ULA_AS(ULA_A), .ULA_BS(ULA_B), .L1_MUX_RegInS(L1_MUX_RegIn),
    .L1_RegWriteS(L1_RegWrite), .Rd_L4S(rd_l4_t), .Rd_L3S(rd_l3_t), .Rd_L1S(rd_l1_t),
    .Tipo_I_L1S(Tipo_I_L12), .Tipo_I_L2S(Tipo_I_L22), .L4_RegWriteS(L4RegWrite2), .L3_RegWriteS(L3RegWrite2));

  // Notes on the sheet:
  //   MUX PC
  //   ESTÁGIO IF
  //   PC +1
  //   MUX WrAddr2
  //   REGISTRADOR IF/ID
  //   MUX_TIPO_INSTRUCAO_LANE1
  //   Mux WrData2
  //   ESTÁGIO ID
  //   REGISTRADOR ID/EX
  //   ESTÁGIO EX
  //   REGISTRADOR EX/WB
  //   ESTÁGIO WB
endmodule

module VLIW_V2 (
  input  RST
);

  wire CLK, comparator_1_eq, comparator_2_eq, comparator_3_eq, comparator_4_eq, comparator_5_eq,
       comparator_6_eq, comparator_7_eq, comparator_8_eq, comparator_9_eq, comparator_10_eq,
       comparator_11_eq, comparator_12_eq, comparator_13_eq, comparator_14_eq, decodificador_1_branch,
       decodificador_1_condition, decodificador_1_jr, decodificador_1_l1regwrite, decodificador_1_memread,
       decodificador_1_memwrite, decodificador_1_mux_imm, decodificador_1_mux_regin,
       decodificador_1_mux_ula_bl3, decodificador_1_mux_ula_bl4, decodificador_1_regwritel3,
       decodificador_1_regwritel4, decodificador_1_relative, decodificador_1_tipo_i_lane1,
       decodificador_1_tipo_i_lane2, Flush, L1_MUX_REGINWB, l1_regwrite, L1_RegWriteWB, l3_regwrite,
       L3_RegWriteWB, l4_regwrite, L4_RegWriteWB, m1_ReadData3, m1_ReadData4, m1_ReadData5, m1_ReadData6,
       m1_ReadData7, m1_ReadData8, m2_ReadData3, m2_ReadData4, m2_ReadData5, m2_ReadData6, m2_ReadData7,
       m2_ReadData8, mux_regin, not_1_out, or_1_out, or_2_out, or_3_out, or_4_out, or_5_out, or_6_out,
       or_7_out, or_8_out, ReadData1SelEx, ReadData2SelEx, registrador_id_ex_1_branchs,
       registrador_id_ex_1_jrs, registrador_id_ex_1_l2conditions, registrador_id_ex_1_l3mux_ula_bs,
       registrador_id_ex_1_l4mux_ula_bs, registrador_id_ex_1_memreads, registrador_id_ex_1_memwrites,
       registrador_id_ex_1_mux_imms, registrador_id_ex_1_relatives, Stall, tipo_I_l1, Tipo_I_L1WB, tipo_I_l2,
       Tipo_I_L2WB;
  wire [1:0] decodificador_1_imm_l3, decodificador_1_imm_l4, decodificador_1_rd_l1, decodificador_1_rd_l3,
       decodificador_1_rd_l4, decodificador_1_sel_lane1, extensao_reg_id_ex_1_ra_l1_addr,
       extensao_reg_id_ex_1_ra_l2_addr, extensao_reg_id_ex_1_ra_l3_addr, extensao_reg_id_ex_1_ra_l4_addr,
       extensao_reg_id_ex_1_rb_l1_addr, extensao_reg_id_ex_1_rb_l2_addr, extensao_reg_id_ex_1_rb_l3_addr,
       extensao_reg_id_ex_1_rb_l4_addr, l1_rd, l3_rd, l4_rd, multiplexer_2_out, multiplexer_3_out,
       multiplexer_6_out, Rd_L1Wb, Rd_L3Wb, Rd_L4Wb, ReadAddr1, ReadAddr2, ReadAddr3, ReadAddr4, ReadAddr5,
       ReadAddr6, ReadAddr7, ReadAddr8, registrador_id_ex_1_l3s, registrador_id_ex_1_l4s,
       registrador_id_ex_1_sel_lane1s, WrAddr2Ex, WriteAddr1_EX;
  wire [2:0] decodificador_1_aluopl3, decodificador_1_aluopl4, registrador_id_ex_1_l3aluop_0s,
       registrador_id_ex_1_l4aluop_0s;
  wire [3:0] decodificador_1_imm_l1, decodificador_1_imm_l2, decodificador_1_opcode_lane1, opcode_l1,
       registrador_id_ex_1_l1s, registrador_id_ex_1_l2s;
  wire [7:0] adder_1_out, lane1_out_EX, lane1_outWB, multiplexer_1_out, multiplexer_4_out,
       multiplexer_11_out, multiplexer_12_out, multiplexer_13_out, multiplexer_14_out, multiplexer_15_out,
       multiplexer_16_out, NewPC, PC1, PC_q, R0_out, ReadData1, ReadData2, ReadData3, ReadData4, ReadData5,
       ReadData6, ReadData7, ReadData8, reg_bank_1_readdata1, reg_bank_1_readdata2, reg_bank_1_readdata3,
       reg_bank_1_readdata4, reg_bank_1_readdata5, reg_bank_1_readdata6, reg_bank_1_readdata7,
       reg_bank_1_readdata8, registrador_id_ex_1_l1_ras, registrador_id_ex_1_l1_rbs,
       registrador_id_ex_1_l2_ras, registrador_id_ex_1_l2_rbs, registrador_id_ex_1_l3_ras,
       registrador_id_ex_1_l3_rbs, registrador_id_ex_1_l4_ras, registrador_id_ex_1_l4_rbs,
       registrador_id_ex_1_pc1s, ULA_A_EX, ULA_AWB, ULA_B_EX, ULA_BWB, WrData2Ex;
  wire [31:0] instmem_1_instout, registrador_if_id_1_decoder;

  Multiplexer #(.width(8)) multiplexer_1 (.in0(adder_1_out), .in1(NewPC), .out(multiplexer_1_out), .sel(Flush));
  not not_1 (not_1_out, Stall);
  Clock u_CLK (.out(CLK));
  Register PC (.D(multiplexer_1_out), .en(not_1_out), .clk(CLK), .Q(PC_q), .clr(RST));
  Adder adder_1 (.a(PC_q), .b(8'h1), .out(adder_1_out));  // open: cin, cout
  InstMem instmem_1 (.Address(PC_q), .InstOut(instmem_1_instout));
  Registrador_IF_ID registrador_if_id_1 (
    .ROM(instmem_1_instout), .PC(adder_1_out), .Flush(Flush), .Clock(CLK), .rst(RST), .stall(Stall),
    .Decoder(registrador_if_id_1_decoder), .PC1(PC1));
  Multiplexer #(.width(2)) multiplexer_2 (.in0(Rd_L1Wb), .in1(2'b00), .out(multiplexer_2_out), .sel(Tipo_I_L1WB));
  or or_1 (or_1_out, L4_RegWriteWB, L3_RegWriteWB);
  Multiplexer #(.width(2)) multiplexer_3 (.in0(Rd_L4Wb), .in1(Rd_L3Wb), .out(multiplexer_3_out), .sel(L3_RegWriteWB));
  Decodificador decodificador_1 (
    .Instr_32b(registrador_if_id_1_decoder), .RdAddr_L1_Ra(ReadAddr1), .RdAddr_L2_Ra(ReadAddr3),
    .RdAddr_L3_Ra(ReadAddr5), .RdAddr_L4_Ra(ReadAddr7), .RdAddr_L1_Rb(ReadAddr2), .RdAddr_L2_Rb(ReadAddr4),
    .RdAddr_L3_Rb(ReadAddr6), .RdAddr_L4_Rb(ReadAddr8), .Rd_L1(decodificador_1_rd_l1),
    .Rd_L3(decodificador_1_rd_l3), .Rd_L4(decodificador_1_rd_l4), .Imm_L1(decodificador_1_imm_l1),
    .Imm_L2(decodificador_1_imm_l2), .Imm_L3(decodificador_1_imm_l3), .Imm_L4(decodificador_1_imm_l4),
    .Sel_lane1(decodificador_1_sel_lane1), .MUX_Imm(decodificador_1_mux_imm),
    .MemRead(decodificador_1_memread), .MemWrite(decodificador_1_memwrite),
    .l1RegWrite(decodificador_1_l1regwrite), .Mux_RegIn(decodificador_1_mux_regin),
    .Condition(decodificador_1_condition), .Relative(decodificador_1_relative), .JR(decodificador_1_jr),
    .Branch(decodificador_1_branch), .MUX_ULA_BL3(decodificador_1_mux_ula_bl3),
    .RegWriteL3(decodificador_1_regwritel3), .ALUOpL3(decodificador_1_aluopl3),
    .MUX_ULA_BL4(decodificador_1_mux_ula_bl4), .RegWriteL4(decodificador_1_regwritel4),
    .ALUOpL4(decodificador_1_aluopl4), .Tipo_I_lane1(decodificador_1_tipo_i_lane1),
    .Tipo_i_lane2(decodificador_1_tipo_i_lane2), .Opcode_lane1(decodificador_1_opcode_lane1));
  Multiplexer #(.width(8)) multiplexer_4 (.in0(ULA_BWB), .in1(ULA_AWB), .out(multiplexer_4_out), .sel(L3_RegWriteWB));
  Comparator #(.width(2)) comparator_1 (.a(ReadAddr3), .b(WriteAddr1_EX), .eq(comparator_1_eq));  // open: gt, lt
  or or_2 (or_2_out, l3_regwrite, l4_regwrite);
  Comparator #(.width(2)) comparator_2 (.a(ReadAddr3), .b(WrAddr2Ex), .eq(comparator_2_eq));  // open: gt, lt
  Comparator #(.width(2)) comparator_3 (.a(ReadAddr4), .b(WriteAddr1_EX), .eq(comparator_3_eq));  // open: gt, lt
  or or_3 (or_3_out, l3_regwrite, l4_regwrite);
  Comparator #(.width(2)) comparator_4 (.a(ReadAddr4), .b(WrAddr2Ex), .eq(comparator_4_eq));  // open: gt, lt
  Comparator #(.width(2)) comparator_5 (.a(ReadAddr5), .b(WriteAddr1_EX), .eq(comparator_5_eq));  // open: gt, lt
  or or_4 (or_4_out, l3_regwrite, l4_regwrite);
  Comparator #(.width(2)) comparator_6 (.a(ReadAddr5), .b(WrAddr2Ex), .eq(comparator_6_eq));  // open: gt, lt
  Comparator #(.width(2)) comparator_7 (.a(ReadAddr6), .b(WriteAddr1_EX), .eq(comparator_7_eq));  // open: gt, lt
  or or_5 (or_5_out, l3_regwrite, l4_regwrite);
  Comparator #(.width(2)) comparator_8 (.a(ReadAddr6), .b(WrAddr2Ex), .eq(comparator_8_eq));  // open: gt, lt
  Comparator #(.width(2)) comparator_9 (.a(ReadAddr7), .b(WriteAddr1_EX), .eq(comparator_9_eq));  // open: gt, lt
  or or_6 (or_6_out, l3_regwrite, l4_regwrite);
  Comparator #(.width(2)) comparator_10 (.a(ReadAddr7), .b(WrAddr2Ex), .eq(comparator_10_eq));  // open: gt, lt
  Comparator #(.width(2)) comparator_11 (.a(ReadAddr8), .b(WriteAddr1_EX), .eq(comparator_11_eq));  // open: gt, lt
  or or_7 (or_7_out, l3_regwrite, l4_regwrite);
  Comparator #(.width(2)) comparator_12 (.a(ReadAddr8), .b(WrAddr2Ex), .eq(comparator_12_eq));  // open: gt, lt
  Multiplexer #(.width(2)) multiplexer_5 (.in0(l1_rd), .in1(2'b00), .out(WriteAddr1_EX), .sel(tipo_I_l1));
  Multiplexer #(.width(2)) multiplexer_6 (.in0(l1_rd), .in1(2'b00), .out(multiplexer_6_out), .sel(tipo_I_l1));
  Multiplexer #(.width(2)) multiplexer_7 (.in0(l4_rd), .in1(l3_rd), .out(WrAddr2Ex), .sel(l3_regwrite));
  Multiplexer #(.width(8)) multiplexer_8 (.in0(ULA_B_EX), .in1(ULA_A_EX), .out(WrData2Ex), .sel(l3_regwrite));
  and and_1 (m1_ReadData3, l1_regwrite, comparator_1_eq);
  and and_2 (m2_ReadData3, or_2_out, comparator_2_eq);
  and and_3 (m1_ReadData4, l1_regwrite, comparator_3_eq);
  and and_4 (m2_ReadData4, or_3_out, comparator_4_eq);
  and and_5 (m1_ReadData5, l1_regwrite, comparator_5_eq);
  and and_6 (m2_ReadData5, or_4_out, comparator_6_eq);
  and and_7 (m1_ReadData6, l1_regwrite, comparator_7_eq);
  and and_8 (m2_ReadData6, or_5_out, comparator_8_eq);
  and and_9 (m1_ReadData7, l1_regwrite, comparator_9_eq);
  and and_10 (m2_ReadData7, or_6_out, comparator_10_eq);
  and and_11 (m1_ReadData8, l1_regwrite, comparator_11_eq);
  and and_12 (m2_ReadData8, or_7_out, comparator_12_eq);
  reg_bank reg_bank_1 (
    .WrData1(lane1_outWB), .WrData2(multiplexer_4_out), .ReadAddr1(ReadAddr1), .clk(CLK),
    .ReadAddr2(ReadAddr2), .rst(RST), .ReadAddr3(ReadAddr3), .ReadAddr4(ReadAddr4), .ReadAddr5(ReadAddr5),
    .ReadAddr6(ReadAddr6), .ReadAddr7(ReadAddr7), .ReadAddr8(ReadAddr8), .WrAddr1(multiplexer_2_out),
    .WE1(L1_RegWriteWB), .WE2(or_1_out), .WrAddr2(multiplexer_3_out), .ReadData1(reg_bank_1_readdata1),
    .ReadData2(reg_bank_1_readdata2), .ReadData3(reg_bank_1_readdata3), .ReadData4(reg_bank_1_readdata4),
    .ReadData5(reg_bank_1_readdata5), .ReadData6(reg_bank_1_readdata6), .ReadData7(reg_bank_1_readdata7),
    .ReadData8(reg_bank_1_readdata8), .R0_out(R0_out));
  and and_13 (ReadData1SelEx, l1_regwrite, comparator_13_eq);
  Comparator #(.width(2)) comparator_13 (.a(WriteAddr1_EX), .b(ReadAddr1), .eq(comparator_13_eq));  // open: gt, lt
  and and_14 (ReadData2SelEx, l1_regwrite, comparator_14_eq);
  Comparator #(.width(2)) comparator_14 (.a(multiplexer_6_out), .b(ReadAddr2), .eq(comparator_14_eq));  // open: gt, lt
  hazard_detector hazard_detector_1 (
    .opcode_lane1_IDEX(opcode_l1), .rd_l1_IDEX(l1_rd), .ra_lane1_ID(ReadAddr1), .rb_lane1_ID(ReadAddr2),
    .ra_lane2_ID(ReadAddr3), .rb_lane2_ID(ReadAddr4), .ra_lane3_ID(ReadAddr5), .rb_lane3_ID(ReadAddr6),
    .ra_lane4_ID(ReadAddr7), .rb_lane4_ID(ReadAddr8), .stall(Stall));
  Multiplexer #(.width(8)) multiplexer_9 (
    .in0(reg_bank_1_readdata1), .in1(lane1_out_EX), .out(ReadData1), .sel(ReadData1SelEx));
  Multiplexer #(.width(8)) multiplexer_10 (
    .in0(reg_bank_1_readdata2), .in1(lane1_out_EX), .out(ReadData2), .sel(ReadData2SelEx));
  Multiplexer #(.width(8)) multiplexer_11 (
    .in0(reg_bank_1_readdata3), .in1(lane1_out_EX), .out(multiplexer_11_out), .sel(m1_ReadData3));
  Multiplexer #(.width(8)) multiplexer_12 (
    .in0(reg_bank_1_readdata4), .in1(lane1_out_EX), .out(multiplexer_12_out), .sel(m1_ReadData4));
  Multiplexer #(.width(8)) multiplexer_13 (
    .in0(reg_bank_1_readdata5), .in1(lane1_out_EX), .out(multiplexer_13_out), .sel(m1_ReadData5));
  Multiplexer #(.width(8)) multiplexer_14 (
    .in0(reg_bank_1_readdata6), .in1(lane1_out_EX), .out(multiplexer_14_out), .sel(m1_ReadData6));
  Multiplexer #(.width(8)) multiplexer_15 (
    .in0(reg_bank_1_readdata7), .in1(lane1_out_EX), .out(multiplexer_15_out), .sel(m1_ReadData7));
  Multiplexer #(.width(8)) multiplexer_16 (
    .in0(reg_bank_1_readdata8), .in1(lane1_out_EX), .out(multiplexer_16_out), .sel(m1_ReadData8));
  Multiplexer #(.width(8)) multiplexer_17 (
    .in0(multiplexer_11_out), .in1(WrData2Ex), .out(ReadData3), .sel(m2_ReadData3));
  Multiplexer #(.width(8)) multiplexer_18 (
    .in0(multiplexer_12_out), .in1(WrData2Ex), .out(ReadData4), .sel(m2_ReadData4));
  Multiplexer #(.width(8)) multiplexer_19 (
    .in0(multiplexer_13_out), .in1(WrData2Ex), .out(ReadData5), .sel(m2_ReadData5));
  Multiplexer #(.width(8)) multiplexer_20 (
    .in0(multiplexer_14_out), .in1(WrData2Ex), .out(ReadData6), .sel(m2_ReadData6));
  Multiplexer #(.width(8)) multiplexer_21 (
    .in0(multiplexer_15_out), .in1(WrData2Ex), .out(ReadData7), .sel(m2_ReadData7));
  Multiplexer #(.width(8)) multiplexer_22 (
    .in0(multiplexer_16_out), .in1(WrData2Ex), .out(ReadData8), .sel(m2_ReadData8));
  or or_8 (or_8_out, Flush, Stall);
  Registrador_ID_EX registrador_id_ex_1 (
    .L1_Ra(ReadData1), .L1_Rb(ReadData2), .L2_Ra(ReadData3), .L2_Rb(ReadData4), .L3_Ra(ReadData5),
    .L3_Rb(ReadData6), .L4_Ra(ReadData7), .L4_Rb(ReadData8), .PC1(PC1), .L2(decodificador_1_imm_l2),
    .L1(decodificador_1_imm_l1), .L4(decodificador_1_imm_l4), .L3(decodificador_1_imm_l3),
    .Rd_L4(decodificador_1_rd_l4), .Rd_L3(decodificador_1_rd_l3), .Rd_L1(decodificador_1_rd_l1),
    .Relative(decodificador_1_relative), .JR(decodificador_1_jr), .Branch(decodificador_1_branch),
    .MUX_Imm(decodificador_1_mux_imm), .MUX_RegIn(decodificador_1_mux_regin),
    .L1RegWrite(decodificador_1_l1regwrite), .MemWrite(decodificador_1_memwrite),
    .MemRead(decodificador_1_memread), .L4MUX_ULA_B(decodificador_1_mux_ula_bl4),
    .L4RegWrite(decodificador_1_regwritel4), .L3AluOp_0(decodificador_1_aluopl3[0]),
    .L3AluOp_1(decodificador_1_aluopl3[1]), .L3AluOp_2(decodificador_1_aluopl3[2]),
    .L3MUX_ULA_B(decodificador_1_mux_ula_bl3), .L3RegWrite(decodificador_1_regwritel3),
    .L2Condition(decodificador_1_condition), .Tipo_I_2(decodificador_1_tipo_i_lane2),
    .Tipo_I_L1(decodificador_1_tipo_i_lane1), .Sel_Lane1(decodificador_1_sel_lane1),
    .L4AluOp_0(decodificador_1_aluopl4[0]), .L4AluOp_1(decodificador_1_aluopl4[1]),
    .L4AluOp_2(decodificador_1_aluopl4[2]), .CLK(CLK), .Flush_OR_Stall(or_8_out), .rst(RST),
    .L1_RaS(registrador_id_ex_1_l1_ras), .L1_RbS(registrador_id_ex_1_l1_rbs),
    .L2_RaS(registrador_id_ex_1_l2_ras), .L2_RbS(registrador_id_ex_1_l2_rbs),
    .L3_RaS(registrador_id_ex_1_l3_ras), .L3_RbS(registrador_id_ex_1_l3_rbs),
    .L4_RaS(registrador_id_ex_1_l4_ras), .L4_RbS(registrador_id_ex_1_l4_rbs),
    .PC1S(registrador_id_ex_1_pc1s), .L2S(registrador_id_ex_1_l2s), .L1S(registrador_id_ex_1_l1s),
    .L4S(registrador_id_ex_1_l4s), .L3S(registrador_id_ex_1_l3s), .Rd_L4S(l4_rd), .Rd_L3S(l3_rd),
    .Rd_L1S(l1_rd), .RelativeS(registrador_id_ex_1_relatives), .JRS(registrador_id_ex_1_jrs),
    .BranchS(registrador_id_ex_1_branchs), .MUX_ImmS(registrador_id_ex_1_mux_imms), .MUX_RegInS(mux_regin),
    .L1RegWriteS(l1_regwrite), .MemWriteS(registrador_id_ex_1_memwrites),
    .MemReadS(registrador_id_ex_1_memreads), .L4MUX_ULA_BS(registrador_id_ex_1_l4mux_ula_bs),
    .L4Reg_WriteS(l4_regwrite), .L3ALUOp_0S(registrador_id_ex_1_l3aluop_0s[0]),
    .L3ALUOp_1S(registrador_id_ex_1_l3aluop_0s[1]), .L3ALUOp_2S(registrador_id_ex_1_l3aluop_0s[2]),
    .L3MUX_ULA_BS(registrador_id_ex_1_l3mux_ula_bs), .L3RegWriteS(l3_regwrite),
    .L2ConditionS(registrador_id_ex_1_l2conditions), .Tipo_I_L2S(tipo_I_l2), .Tipo_I_L1S(tipo_I_l1),
    .Sel_lane1S(registrador_id_ex_1_sel_lane1s), .L4ALUOp_0S(registrador_id_ex_1_l4aluop_0s[0]),
    .L4ALUOp_1S(registrador_id_ex_1_l4aluop_0s[1]), .L4ALUOp_2S(registrador_id_ex_1_l4aluop_0s[2]));
  Extensao_reg_id_ex extensao_reg_id_ex_1 (
    .RdAddr_l3_ra(ReadAddr5), .RdAddr_l2_ra(ReadAddr3), .RdAddr_l2_rb(ReadAddr4), .RdAddr_l1_rb(ReadAddr2),
    .RdAddr_l3_rb(ReadAddr6), .RdAddr_l4_ra(ReadAddr7), .RdAddr_l4_rb(ReadAddr8), .RdAddr_l1_ra(ReadAddr1),
    .Opcode_l1_ex(decodificador_1_opcode_lane1), .CLK(CLK), .Flush(or_8_out), .rst(RST),
    .ra_l3_addr(extensao_reg_id_ex_1_ra_l3_addr), .ra_l2_addr(extensao_reg_id_ex_1_ra_l2_addr),
    .rb_l2_addr(extensao_reg_id_ex_1_rb_l2_addr), .rb_l1_addr(extensao_reg_id_ex_1_rb_l1_addr),
    .rb_l3_addr(extensao_reg_id_ex_1_rb_l3_addr), .ra_l4_addr(extensao_reg_id_ex_1_ra_l4_addr),
    .rb_l4_addr(extensao_reg_id_ex_1_rb_l4_addr), .ra_l1_addr(extensao_reg_id_ex_1_ra_l1_addr),
    .opcode_l1_exS(opcode_l1));
  lane_1 lane_1_1 (
    .Ra_data(registrador_id_ex_1_l1_ras), .ula_a(ULA_AWB), .ula_b(ULA_BWB),
    .Rb_data(registrador_id_ex_1_l1_rbs), .MemWrite(registrador_id_ex_1_memwrites),
    .MemRead(registrador_id_ex_1_memreads), .Sel_lane1(registrador_id_ex_1_sel_lane1s),
    .Mux_Imm(registrador_id_ex_1_mux_imms), .clk(CLK), .Imm(registrador_id_ex_1_l1s),
    .fwd_lane1_out(lane1_outWB), .fwd_l1regWrite(L1_RegWriteWB), .l3regwrite(L3_RegWriteWB),
    .l4regwrite(L4_RegWriteWB), .ra_addr(extensao_reg_id_ex_1_ra_l1_addr), .rd_L1_EXWB(Rd_L1Wb),
    .rb_addr(extensao_reg_id_ex_1_rb_l1_addr), .rd_l3(Rd_L3Wb), .rd_l4(Rd_L4Wb), .lane1_out(lane1_out_EX));
  lane_2 lane_2_1 (
    .Ra(registrador_id_ex_1_l2_ras), .ula_a(ULA_AWB), .ula_b(ULA_BWB), .Rb(registrador_id_ex_1_l2_rbs),
    .R0(R0_out), .Imm(registrador_id_ex_1_l2s), .PC1(registrador_id_ex_1_pc1s),
    .Branch(registrador_id_ex_1_branchs), .JR(registrador_id_ex_1_jrs),
    .Relative(registrador_id_ex_1_relatives), .Condition(registrador_id_ex_1_l2conditions),
    .fwd_lane1_out(lane1_outWB), .tipo_I_lane2(Tipo_I_L2WB), .l1_regwrite(L1_RegWriteWB),
    .l3regwrite(L3_RegWriteWB), .l4regwrite(L4_RegWriteWB), .ra_addr(extensao_reg_id_ex_1_ra_l2_addr),
    .rd_L1_EXWB(Rd_L1Wb), .rb_addr(extensao_reg_id_ex_1_rb_l2_addr), .rd_l3(Rd_L3Wb), .rd_l4(Rd_L4Wb),
    .NewPC(NewPC), .Flush(Flush));
  ULA_VLIW_fwd ULA_A (
    .Ra(registrador_id_ex_1_l3_ras), .fwd_lane1_out(lane1_outWB), .ula_a(ULA_AWB), .ula_b(ULA_BWB),
    .Rb(registrador_id_ex_1_l3_rbs), .l1_regwrite_EXWB(L1_RegWriteWB), .l3regwrite(L3_RegWriteWB),
    .l4regwrite(L4_RegWriteWB), .ra_addr(extensao_reg_id_ex_1_ra_l3_addr), .rd_L1_EXWB(Rd_L1Wb),
    .rb_addr(extensao_reg_id_ex_1_rb_l3_addr), .rd_l3(Rd_L3Wb), .rd_l4(Rd_L4Wb),
    .Imm(registrador_id_ex_1_l3s), .MUX_ULA_B(registrador_id_ex_1_l3mux_ula_bs),
    .ALUOp(registrador_id_ex_1_l3aluop_0s), .Resultado(ULA_A_EX));
  ULA_VLIW_fwd ULA_B (
    .Ra(registrador_id_ex_1_l4_ras), .fwd_lane1_out(lane1_outWB), .ula_a(ULA_AWB), .ula_b(ULA_BWB),
    .Rb(registrador_id_ex_1_l4_rbs), .l1_regwrite_EXWB(L1_RegWriteWB), .l3regwrite(L3_RegWriteWB),
    .l4regwrite(L4_RegWriteWB), .ra_addr(extensao_reg_id_ex_1_ra_l4_addr), .rd_L1_EXWB(Rd_L1Wb),
    .rb_addr(extensao_reg_id_ex_1_rb_l4_addr), .rd_l3(Rd_L3Wb), .rd_l4(Rd_L4Wb),
    .Imm(registrador_id_ex_1_l4s), .MUX_ULA_B(registrador_id_ex_1_l4mux_ula_bs),
    .ALUOp(registrador_id_ex_1_l4aluop_0s), .Resultado(ULA_B_EX));
  Registrador_EX_WB registrador_ex_wb_1 (
    .lane1_out(lane1_out_EX), .ULA_A(ULA_A_EX), .ULA_B(ULA_B_EX), .L1_MUX_RegIn(mux_regin),
    .L1_RegWrite(l1_regwrite), .Rd_L4(l4_rd), .Rd_L3(l3_rd), .Rd_L1(l1_rd), .Tipo_I_L1(tipo_I_l1),
    .Tipo_I_L2(tipo_I_l2), .L4_RegWrite(l4_regwrite), .L3_RegWrite(l3_regwrite), .CLK(CLK), .rst(RST),
    .lane1_outS(lane1_outWB), .ULA_AS(ULA_AWB), .ULA_BS(ULA_BWB), .L1_MUX_RegInS(L1_MUX_REGINWB),
    .L1_RegWriteS(L1_RegWriteWB), .Rd_L4S(Rd_L4Wb), .Rd_L3S(Rd_L3Wb), .Rd_L1S(Rd_L1Wb),
    .Tipo_I_L1S(Tipo_I_L1WB), .Tipo_I_L2S(Tipo_I_L2WB), .L4_RegWriteS(L4_RegWriteWB),
    .L3_RegWriteS(L3_RegWriteWB));

  // Other names for the same wires on the sheet: rd_l1[1:0] = l1_rd

  // Notes on the sheet:
  //   MUX PC
  //   ESTÁGIO IF
  //   PC +1
  //   REGISTRADOR IF/ID
  //   MUX WrAddr2
  //   MUX_TIPO_INSTRUCAO_LANE1
  //   Mux WrData2
  //   ESTÁGIO ID
  //   REGISTRADOR ID/EX
  //   ESTÁGIO EX
  //   REGISTRADOR EX/WB
  //   ESTÁGIO WB
endmodule

module reg_bank (
  input  [7:0] WrData1,
  input  [7:0] WrData2,
  input  [1:0] ReadAddr1,
  input  clk,
  input  [1:0] ReadAddr2,
  input  rst,
  input  [1:0] ReadAddr3,
  input  [1:0] ReadAddr4,
  input  [1:0] ReadAddr5,
  input  [1:0] ReadAddr6,
  input  [1:0] ReadAddr7,
  input  [1:0] ReadAddr8,
  input  [1:0] WrAddr1,
  input  WE1,
  input  WE2,
  input  [1:0] WrAddr2,
  output [7:0] ReadData1,
  output [7:0] ReadData2,
  output [7:0] ReadData3,
  output [7:0] ReadData4,
  output [7:0] ReadData5,
  output [7:0] ReadData6,
  output [7:0] ReadData7,
  output [7:0] ReadData8,
  output [7:0] R0_out
);

  wire AND_1A, AND_1B, AND_1C, AND_1D, AND_2A, AND_2B, AND_2C, AND_2D, decoder_1_out0, decoder_1_out1,
       decoder_1_out2, decoder_1_out3, decoder_2_out0, decoder_2_out1, decoder_2_out2, decoder_2_out3, EN0,
       EN1, EN2, EN3;
  wire [7:0] multiplexer_6_out, multiplexer_7_out, multiplexer_8_out, R0_D, R0_q, R1_D, R1_q, R2_D, R2_q,
       R3_D, R3_q;

  Decoder #(.enable("false"), .select(2)) decoder_1 (
    .out0(decoder_1_out0), .out1(decoder_1_out1), .out2(decoder_1_out2), .out3(decoder_1_out3), .sel(WrAddr1));
  Decoder #(.enable("false"), .select(2)) decoder_2 (
    .out0(decoder_2_out0), .out1(decoder_2_out1), .out2(decoder_2_out2), .out3(decoder_2_out3), .sel(WrAddr2));
  Multiplexer #(.width(8)) multiplexer_1 (.in0(WrData1), .in1(WrData2), .out(R0_D), .sel(AND_2A));
  Multiplexer #(.width(8)) multiplexer_2 (.in0(WrData1), .in1(WrData2), .out(R1_D), .sel(AND_2B));
  Multiplexer #(.width(8)) multiplexer_3 (.in0(WrData1), .in1(WrData2), .out(R2_D), .sel(AND_2C));
  Multiplexer #(.width(8)) multiplexer_4 (.in0(WrData1), .in1(WrData2), .out(R3_D), .sel(AND_2D));
  and and_1 (AND_1A, decoder_1_out0, WE1);
  and and_2 (AND_1B, decoder_1_out1, WE1);
  and and_3 (AND_1C, decoder_1_out2, WE1);
  and and_4 (AND_1D, decoder_1_out3, WE1);
  and and_5 (AND_2A, decoder_2_out0, WE2);
  and and_6 (AND_2B, decoder_2_out1, WE2);
  and and_7 (AND_2C, decoder_2_out2, WE2);
  and and_8 (AND_2D, decoder_2_out3, WE2);
  or or_1 (EN0, AND_1A, AND_2A);
  or or_2 (EN1, AND_1B, AND_2B);
  or or_3 (EN2, AND_1C, AND_2C);
  or or_4 (EN3, AND_1D, AND_2D);
  Register R0 (.D(R0_D), .en(EN0), .clk(clk), .Q(R0_q), .clr(rst));
  Register R1 (.D(R1_D), .en(EN1), .clk(clk), .Q(R1_q), .clr(rst));
  Register R2 (.D(R2_D), .en(EN2), .clk(clk), .Q(R2_q), .clr(rst));
  Register R3 (.D(R3_D), .en(EN3), .clk(clk), .Q(R3_q), .clr(rst));
  Multiplexer #(.width(8)) multiplexer_5 (.in0(R0_q), .in1(R0_D), .out(R0_out), .sel(EN0));
  Multiplexer #(.width(8)) multiplexer_6 (.in0(R1_q), .in1(R1_D), .out(multiplexer_6_out), .sel(EN1));
  Multiplexer #(.width(8)) multiplexer_7 (.in0(R2_q), .in1(R2_D), .out(multiplexer_7_out), .sel(EN2));
  Multiplexer #(.width(8)) multiplexer_8 (.in0(R3_q), .in1(R3_D), .out(multiplexer_8_out), .sel(EN3));
  Multiplexer #(.select(2), .width(8)) multiplexer_9 (
    .in0(R0_out), .in1(multiplexer_6_out), .in2(multiplexer_7_out), .in3(multiplexer_8_out), .out(ReadData1),
    .sel(ReadAddr1));
  Multiplexer #(.select(2), .width(8)) multiplexer_10 (
    .in0(R0_out), .in1(multiplexer_6_out), .in2(multiplexer_7_out), .in3(multiplexer_8_out), .out(ReadData2),
    .sel(ReadAddr2));
  Multiplexer #(.select(2), .width(8)) multiplexer_11 (
    .in0(R0_out), .in1(multiplexer_6_out), .in2(multiplexer_7_out), .in3(multiplexer_8_out), .out(ReadData3),
    .sel(ReadAddr3));
  Multiplexer #(.select(2), .width(8)) multiplexer_12 (
    .in0(R0_out), .in1(multiplexer_6_out), .in2(multiplexer_7_out), .in3(multiplexer_8_out), .out(ReadData4),
    .sel(ReadAddr4));
  Multiplexer #(.select(2), .width(8)) multiplexer_13 (
    .in0(R0_out), .in1(multiplexer_6_out), .in2(multiplexer_7_out), .in3(multiplexer_8_out), .out(ReadData5),
    .sel(ReadAddr5));
  Multiplexer #(.select(2), .width(8)) multiplexer_14 (
    .in0(R0_out), .in1(multiplexer_6_out), .in2(multiplexer_7_out), .in3(multiplexer_8_out), .out(ReadData6),
    .sel(ReadAddr6));
  Multiplexer #(.select(2), .width(8)) multiplexer_15 (
    .in0(R0_out), .in1(multiplexer_6_out), .in2(multiplexer_7_out), .in3(multiplexer_8_out), .out(ReadData7),
    .sel(ReadAddr7));
  Multiplexer #(.select(2), .width(8)) multiplexer_16 (
    .in0(R0_out), .in1(multiplexer_6_out), .in2(multiplexer_7_out), .in3(multiplexer_8_out), .out(ReadData8),
    .sel(ReadAddr8));
endmodule

module ULA_VLIW (
  input  [7:0] Ra,
  input  [7:0] Rb,
  input  [3:0] Imm,
  input  MUX_ULA_B,
  input  [2:0] ALUOp,
  output [7:0] Resultado
);

  wire not_1_out, or_2_out, or_3_out, or_4_out;
  wire [7:0] B_sel, bit_extender_1_out, bit_extender_2_out, koggestone8bit_1_soma, multiplexer_2_out,
       multiplexer_3_out, or_1_out, shifter_1_out, shifter_2_out, subtractor_1_out;

  assign bit_extender_1_out = {{4{Imm[3]}}, Imm};  // Bit_Extender bit_extender_1
  Multiplexer #(.width(8)) multiplexer_1 (.in0(Rb), .in1(bit_extender_1_out), .out(B_sel), .sel(MUX_ULA_B));
  Subtractor subtractor_1 (.a(Ra), .b(B_sel), .out(subtractor_1_out));  // open: bin, bout
  assign or_1_out = Ra | B_sel;  // OR_Gate or_1, 8 bits wide
  or or_2 (or_2_out, B_sel[0], B_sel[1], B_sel[2], B_sel[3], B_sel[4], B_sel[5], B_sel[6], B_sel[7]);
  Shifter shifter_1 (.in(Ra), .\dist (B_sel[2:0]), .out(shifter_1_out));
  or or_3 (or_3_out, B_sel[3], B_sel[4], B_sel[5], B_sel[6], B_sel[7]);
  Shifter #(.shift("lr")) shifter_2 (.in(Ra), .\dist (B_sel[2:0]), .out(shifter_2_out));
  or or_4 (or_4_out, B_sel[3], B_sel[4], B_sel[5], B_sel[6], B_sel[7]);
  KoggeStone8Bit koggestone8bit_1 (.A(Ra), .B(B_sel), .Soma(koggestone8bit_1_soma));  // open: Cout
  assign bit_extender_2_out = {{7{not_1_out}}, not_1_out};  // Bit_Extender bit_extender_2
  not not_1 (not_1_out, or_2_out);
  Multiplexer #(.width(8)) multiplexer_2 (
    .in0(shifter_1_out), .in1({8{1'b0}}), .out(multiplexer_2_out), .sel(or_3_out));
  Multiplexer #(.width(8)) multiplexer_3 (
    .in0(shifter_2_out), .in1({8{1'b0}}), .out(multiplexer_3_out), .sel(or_4_out));
  Multiplexer #(.select(3), .width(8)) multiplexer_4 (
    .in0(koggestone8bit_1_soma), .in1(subtractor_1_out), .in2(or_1_out), .in3(bit_extender_2_out),
    .in4(multiplexer_2_out), .in5(multiplexer_3_out), .in6({8{1'b0}}), .in7({8{1'b0}}), .out(Resultado),
    .sel(ALUOp));
endmodule

module lane_1 (
  input  [7:0] Ra_data,
  input  [7:0] ula_a,
  input  [7:0] ula_b,
  input  [7:0] Rb_data,
  input  MemWrite,
  input  MemRead,
  input  [1:0] Sel_lane1,
  input  Mux_Imm,
  input  clk,
  input  [3:0] Imm,
  input  [7:0] fwd_lane1_out,
  input  fwd_l1regWrite,
  input  l3regwrite,
  input  l4regwrite,
  input  [1:0] ra_addr,
  input  [1:0] rd_L1_EXWB,
  input  [1:0] rb_addr,
  input  [1:0] rd_l3,
  input  [1:0] rd_l4,
  output [7:0] lane1_out
);

  wire comparator_1_eq, comparator_2_eq, comparator_3_eq, comparator_4_eq, comparator_5_eq, comparator_6_eq,
       fwd_l3_ra, fwd_l3_rb, fwd_l4_ra, fwd_l4_rb, fwd_ra, fwd_rb;
  wire [1:0] rb_sel, S1, S1_b, S2, S2_b, S3;
  wire [3:0] movh;
  wire [7:0] Imediato_montado, MemOut, Mux_0, Ra, Rb;
  wire [7:4] movl;

  Comparator #(.width(2)) comparator_1 (.a(ra_addr), .b(rd_L1_EXWB), .eq(comparator_1_eq));  // open: gt, lt
  Comparator #(.width(2)) comparator_2 (.a(rd_L1_EXWB), .b(rb_addr), .eq(comparator_2_eq));  // open: gt, lt
  Comparator #(.width(2)) comparator_3 (.a(rd_l3), .b(ra_addr), .eq(comparator_3_eq));  // open: gt, lt
  Comparator #(.width(2)) comparator_4 (.a(ra_addr), .b(rd_l4), .eq(comparator_4_eq));  // open: gt, lt
  Comparator #(.width(2)) comparator_5 (.a(rb_addr), .b(rd_l3), .eq(comparator_5_eq));  // open: gt, lt
  Comparator #(.width(2)) comparator_6 (.a(rb_addr), .b(rd_l4), .eq(comparator_6_eq));  // open: gt, lt
  Multiplexer #(.select(2), .width(8)) multiplexer_1 (
    .in0(Ra_data), .in2(ula_a), .in3(ula_b), .out(Ra), .sel(S3));  // open: in1
  Multiplexer #(.select(2), .width(8)) multiplexer_2 (
    .in0(Rb_data), .in1(fwd_lane1_out), .in2(ula_a), .in3(ula_b), .out(Rb), .sel(rb_sel));
  Multiplexer #(.width(8)) multiplexer_3 (.in0(Ra), .in1(fwd_lane1_out), .out({movl, movh}), .sel(fwd_l1regWrite));
  and and_1 (fwd_ra, comparator_1_eq, fwd_l1regWrite);
  and and_2 (fwd_rb, comparator_2_eq, fwd_l1regWrite);
  Multiplexer #(.width(2)) multiplexer_4 (.in0(2'b00), .in1(2'b11), .out(S1), .sel(fwd_l4_ra));
  Multiplexer #(.width(2)) multiplexer_5 (.in0(S1), .in1(2'b10), .out(S2), .sel(fwd_l3_ra));
  Multiplexer #(.width(2)) multiplexer_6 (.in0(S2), .in1(2'b01), .out(S3), .sel(fwd_ra));
  Multiplexer #(.width(2)) multiplexer_7 (.in0(2'b00), .in1(2'b11), .out(S1_b), .sel(fwd_l4_rb));
  Multiplexer #(.width(2)) multiplexer_8 (.in0(S1_b), .in1(2'b10), .out(S2_b), .sel(fwd_l3_rb));
  Multiplexer #(.width(2)) multiplexer_9 (.in0(S2_b), .in1(2'b01), .out(rb_sel), .sel(fwd_rb));
  and and_3 (fwd_l3_ra, comparator_3_eq, l3regwrite);
  and and_4 (fwd_l4_ra, comparator_4_eq, l4regwrite);
  buf and_5 (fwd_l3_rb, comparator_5_eq);  // AND_Gate
  and and_6 (fwd_l4_rb, comparator_6_eq, l4regwrite);
  RAM #(.asyncread("true")) ram_1 (.addr(Rb), .we(MemWrite), .oe(MemRead), .clk(clk), .din(Ra), .dout(MemOut));
  Multiplexer #(.width(8)) multiplexer_10 (.in0({movl, Imm}), .in1({Imm, movh}), .out(Imediato_montado), .sel(Mux_Imm));
  assign Mux_0 = MemOut & {8{MemRead}};  // AND_Gate and_7, 8 bits wide
  Multiplexer #(.select(2), .width(8)) multiplexer_11 (
    .in0(Mux_0), .in1(Imediato_montado), .in2(Rb), .in3({8{1'b0}}), .out(lane1_out), .sel(Sel_lane1));

  // Other names for the same wires on the sheet: fwd_lane1out[7:0] = fwd_lane1_out; movh[7:4] = Imm; movl[3:0] = Imm
endmodule

module lane_2 (
  input  [7:0] Ra,
  input  [7:0] ula_a,
  input  [7:0] ula_b,
  input  [7:0] Rb,
  input  [7:0] R0,
  input  [3:0] Imm,
  input  [7:0] PC1,
  input  Branch,
  input  JR,
  input  Relative,
  input  Condition,
  input  [7:0] fwd_lane1_out,
  input  tipo_I_lane2,
  input  l1_regwrite,
  input  l3regwrite,
  input  l4regwrite,
  input  [1:0] ra_addr,
  input  [1:0] rd_L1_EXWB,
  input  [1:0] rb_addr,
  input  [1:0] rd_l3,
  input  [1:0] rd_l4,
  output [7:0] NewPC,
  output Flush
);

  wire and_1_out, and_2_out, and_3_out, and_4_out, and_5_out, and_6_out, and_13_out, comparator_1_eq,
       comparator_2_eq, comparator_3_eq, comparator_4_eq, comparator_5_eq, comparator_6_eq, fwd_l3_ra,
       fwd_l3_rb, fwd_l4_ra, fwd_l4_rb, fwd_ra, fwd_rb, not_tipo_I, Zero;
  wire [1:0] ra_sel, rb_sel, S1, S1_b, S2, S2_b;
  wire [7:0] adder_1_out, bit_extender_1_out, multiplexer_1_out, multiplexer_2_out, multiplexer_9_out;

  not not_1 (not_tipo_I, tipo_I_lane2);
  Comparator #(.width(2)) comparator_1 (.a(ra_addr), .b(rd_L1_EXWB), .eq(comparator_1_eq));  // open: gt, lt
  Comparator #(.width(2)) comparator_2 (.a(rd_L1_EXWB), .b(rb_addr), .eq(comparator_2_eq));  // open: gt, lt
  Comparator #(.width(2)) comparator_3 (.a(rd_l3), .b(ra_addr), .eq(comparator_3_eq));  // open: gt, lt
  Comparator #(.width(2)) comparator_4 (.a(ra_addr), .b(rd_l4), .eq(comparator_4_eq));  // open: gt, lt
  Comparator #(.width(2)) comparator_5 (.a(rb_addr), .b(rd_l3), .eq(comparator_5_eq));  // open: gt, lt
  Comparator #(.width(2)) comparator_6 (.a(rb_addr), .b(rd_l4), .eq(comparator_6_eq));  // open: gt, lt
  Multiplexer #(.select(2), .width(8)) multiplexer_1 (
    .in0(Ra), .in1(fwd_lane1_out), .in2(ula_a), .in3(ula_b), .out(multiplexer_1_out), .sel(ra_sel));
  Multiplexer #(.select(2), .width(8)) multiplexer_2 (
    .in0(Rb), .in1(fwd_lane1_out), .in2(ula_a), .in3(ula_b), .out(multiplexer_2_out), .sel(rb_sel));
  and and_1 (and_1_out, comparator_1_eq, l1_regwrite);
  and and_2 (and_2_out, comparator_2_eq, l1_regwrite);
  and and_3 (and_3_out, comparator_3_eq, l3regwrite);
  and and_4 (and_4_out, comparator_4_eq, l4regwrite);
  buf and_5 (and_5_out, comparator_5_eq);  // AND_Gate
  and and_6 (and_6_out, comparator_6_eq, l4regwrite);
  Multiplexer #(.width(2)) multiplexer_3 (.in0(2'b00), .in1(2'b11), .out(S1), .sel(fwd_l4_ra));
  Multiplexer #(.width(2)) multiplexer_4 (.in0(S1), .in1(2'b10), .out(S2), .sel(fwd_l3_ra));
  Multiplexer #(.width(2)) multiplexer_5 (.in0(S2), .in1(2'b01), .out(ra_sel), .sel(fwd_ra));
  Multiplexer #(.width(2)) multiplexer_6 (.in0(2'b00), .in1(2'b11), .out(S1_b), .sel(fwd_l4_rb));
  Multiplexer #(.width(2)) multiplexer_7 (.in0(S1_b), .in1(2'b10), .out(S2_b), .sel(fwd_l3_rb));
  Multiplexer #(.width(2)) multiplexer_8 (.in0(S2_b), .in1(2'b01), .out(rb_sel), .sel(fwd_rb));
  Multiplexer #(.width(8)) multiplexer_9 (.in0(multiplexer_1_out), .in1(R0), .out(multiplexer_9_out), .sel(Condition));
  and and_7 (fwd_ra, not_tipo_I, and_1_out);
  and and_8 (fwd_rb, not_tipo_I, and_2_out);
  and and_9 (fwd_l3_ra, not_tipo_I, and_3_out);
  and and_10 (fwd_l4_ra, not_tipo_I, and_4_out);
  and and_11 (fwd_l3_rb, not_tipo_I, and_5_out);
  and and_12 (fwd_l4_rb, not_tipo_I, and_6_out);
  assign bit_extender_1_out = {{4{Imm[3]}}, Imm};  // Bit_Extender bit_extender_1
  and and_13 (and_13_out, Branch, Zero);
  nor nor_1 (Zero, multiplexer_9_out[0], multiplexer_9_out[1], multiplexer_9_out[2], multiplexer_9_out[3], multiplexer_9_out[4], multiplexer_9_out[5], multiplexer_9_out[6], multiplexer_9_out[7]);
  Adder adder_1 (.a(bit_extender_1_out), .b(PC1), .out(adder_1_out));  // open: cin, cout
  Multiplexer #(.width(8)) multiplexer_10 (.in0(multiplexer_2_out), .in1(adder_1_out), .out(NewPC), .sel(Relative));
  or or_1 (Flush, and_13_out, JR);

  // Other names for the same wires on the sheet: lane1_out[7:0] = fwd_lane1_out
endmodule

module ULA_VLIW_fwd (
  input  [7:0] Ra,
  input  [7:0] fwd_lane1_out,
  input  [7:0] ula_a,
  input  [7:0] ula_b,
  input  [7:0] Rb,
  input  l1_regwrite_EXWB,
  input  l3regwrite,
  input  l4regwrite,
  input  [1:0] ra_addr,
  input  [1:0] rd_L1_EXWB,
  input  [1:0] rb_addr,
  input  [1:0] rd_l3,
  input  [1:0] rd_l4,
  input  [1:0] Imm,
  input  MUX_ULA_B,
  input  [2:0] ALUOp,
  output [7:0] Resultado
);

  wire comparator_1_eq, comparator_2_eq, comparator_3_eq, comparator_4_eq, comparator_5_eq, comparator_6_eq,
       fwd_l3_ra, fwd_l3_rb, fwd_l4_ra, fwd_l4_rb, fwd_ra, fwd_rb, not_1_out, or_2_out, or_3_out, or_4_out;
  wire [1:0] S1, S1_b, S2, S2_b, S3, S3_b;
  wire [7:0] B_sel, bit_extender_1_out, bit_extender_2_out, koggestone8bit_1_soma, multiplexer_10_out,
       multiplexer_11_out, or_1_out, Ra_t, Rb_t, shifter_1_out, shifter_2_out, subtractor_1_out;

  Comparator #(.width(2)) comparator_1 (.a(ra_addr), .b(rd_L1_EXWB), .eq(comparator_1_eq));  // open: gt, lt
  Comparator #(.width(2)) comparator_2 (.a(rd_L1_EXWB), .b(rb_addr), .eq(comparator_2_eq));  // open: gt, lt
  Comparator #(.width(2)) comparator_3 (.a(rd_l3), .b(ra_addr), .eq(comparator_3_eq));  // open: gt, lt
  Comparator #(.width(2)) comparator_4 (.a(ra_addr), .b(rd_l4), .eq(comparator_4_eq));  // open: gt, lt
  Comparator #(.width(2)) comparator_5 (.a(rb_addr), .b(rd_l3), .eq(comparator_5_eq));  // open: gt, lt
  Comparator #(.width(2)) comparator_6 (.a(rb_addr), .b(rd_l4), .eq(comparator_6_eq));  // open: gt, lt
  assign bit_extender_1_out = {{6{Imm[1]}}, Imm};  // Bit_Extender bit_extender_1
  Multiplexer #(.select(2), .width(8)) multiplexer_1 (
    .in0(Ra), .in1(fwd_lane1_out), .in2(ula_a), .in3(ula_b), .out(Ra_t), .sel(S3));
  Multiplexer #(.select(2), .width(8)) multiplexer_2 (
    .in0(Rb), .in1(fwd_lane1_out), .in2(ula_a), .in3(ula_b), .out(Rb_t), .sel(S3_b));
  and and_1 (fwd_ra, comparator_1_eq, l1_regwrite_EXWB);
  and and_2 (fwd_rb, comparator_2_eq, l1_regwrite_EXWB);
  and and_3 (fwd_l3_ra, comparator_3_eq, l3regwrite);
  and and_4 (fwd_l4_ra, comparator_4_eq, l4regwrite);
  buf and_5 (fwd_l3_rb, comparator_5_eq);  // AND_Gate
  and and_6 (fwd_l4_rb, comparator_6_eq, l4regwrite);
  Multiplexer #(.width(2)) multiplexer_3 (.in0(2'b00), .in1(2'b11), .out(S1), .sel(fwd_l4_ra));
  Multiplexer #(.width(2)) multiplexer_4 (.in0(S1), .in1(2'b10), .out(S2), .sel(fwd_l3_ra));
  Multiplexer #(.width(2)) multiplexer_5 (.in0(S2), .in1(2'b01), .out(S3), .sel(fwd_ra));
  Multiplexer #(.width(2)) multiplexer_6 (.in0(2'b00), .in1(2'b11), .out(S1_b), .sel(fwd_l4_rb));
  Multiplexer #(.width(2)) multiplexer_7 (.in0(S1_b), .in1(2'b10), .out(S2_b), .sel(fwd_l3_rb));
  Multiplexer #(.width(2)) multiplexer_8 (.in0(S2_b), .in1(2'b01), .out(S3_b), .sel(fwd_rb));
  Multiplexer #(.width(8)) multiplexer_9 (.in0(Rb_t), .in1(bit_extender_1_out), .out(B_sel), .sel(MUX_ULA_B));
  Subtractor subtractor_1 (.a(Ra_t), .b(B_sel), .out(subtractor_1_out));  // open: bin, bout
  assign or_1_out = Ra_t | B_sel;  // OR_Gate or_1, 8 bits wide
  or or_2 (or_2_out, B_sel[0], B_sel[1], B_sel[2], B_sel[3], B_sel[4], B_sel[5], B_sel[6], B_sel[7]);
  Shifter shifter_1 (.in(Ra_t), .\dist (B_sel[2:0]), .out(shifter_1_out));
  or or_3 (or_3_out, B_sel[3], B_sel[4], B_sel[5], B_sel[6], B_sel[7]);
  Shifter #(.shift("lr")) shifter_2 (.in(Ra_t), .\dist (B_sel[2:0]), .out(shifter_2_out));
  or or_4 (or_4_out, B_sel[3], B_sel[4], B_sel[5], B_sel[6], B_sel[7]);
  KoggeStone8Bit koggestone8bit_1 (.A(Ra_t), .B(B_sel), .Soma(koggestone8bit_1_soma));  // open: Cout
  assign bit_extender_2_out = {{7{not_1_out}}, not_1_out};  // Bit_Extender bit_extender_2
  not not_1 (not_1_out, or_2_out);
  Multiplexer #(.width(8)) multiplexer_10 (
    .in0(shifter_1_out), .in1({8{1'b0}}), .out(multiplexer_10_out), .sel(or_3_out));
  Multiplexer #(.width(8)) multiplexer_11 (
    .in0(shifter_2_out), .in1({8{1'b0}}), .out(multiplexer_11_out), .sel(or_4_out));
  Multiplexer #(.select(3), .width(8)) multiplexer_12 (
    .in0(koggestone8bit_1_soma), .in1(subtractor_1_out), .in2(or_1_out), .in3(bit_extender_2_out),
    .in4(multiplexer_10_out), .in5(multiplexer_11_out), .in6({8{1'b0}}), .in7({8{1'b0}}), .out(Resultado),
    .sel(ALUOp));
endmodule

module Registrador_IF_ID (
  input  [31:0] ROM,
  input  [7:0] PC,
  input  Flush,
  input  Clock,
  input  rst,
  input  stall,
  output [31:0] Decoder,
  output [7:0] PC1
);

  wire not_1_out;
  wire [39:0] multiplexer_1_out;

  not not_1 (not_1_out, stall);
  Multiplexer #(.width(40)) multiplexer_1 (.in0({PC, ROM}), .in1(40'hffffffff), .out(multiplexer_1_out), .sel(Flush));
  Register #(.width(40)) register_1 (.D(multiplexer_1_out), .en(not_1_out), .clk(Clock), .Q({PC1, Decoder}), .clr(rst));
endmodule

module Registrador_ID_EX (
  input  [7:0] L1_Ra,
  input  [7:0] L1_Rb,
  input  [7:0] L2_Ra,
  input  [7:0] L2_Rb,
  input  [7:0] L3_Ra,
  input  [7:0] L3_Rb,
  input  [7:0] L4_Ra,
  input  [7:0] L4_Rb,
  input  [7:0] PC1,
  input  [3:0] L2,
  input  [3:0] L1,
  input  [1:0] L4,
  input  [1:0] L3,
  input  [1:0] Rd_L4,
  input  [1:0] Rd_L3,
  input  [1:0] Rd_L1,
  input  Relative,
  input  JR,
  input  Branch,
  input  MUX_Imm,
  input  MUX_RegIn,
  input  L1RegWrite,
  input  MemWrite,
  input  MemRead,
  input  L4MUX_ULA_B,
  input  L4RegWrite,
  input  L3AluOp_0,
  input  L3AluOp_1,
  input  L3AluOp_2,
  input  L3MUX_ULA_B,
  input  L3RegWrite,
  input  L2Condition,
  input  Tipo_I_2,
  input  Tipo_I_L1,
  input  [1:0] Sel_Lane1,
  input  L4AluOp_0,
  input  L4AluOp_1,
  input  L4AluOp_2,
  input  CLK,
  input  Flush_OR_Stall,
  input  rst,
  output [7:0] L1_RaS,
  output [7:0] L1_RbS,
  output [7:0] L2_RaS,
  output [7:0] L2_RbS,
  output [7:0] L3_RaS,
  output [7:0] L3_RbS,
  output [7:0] L4_RaS,
  output [7:0] L4_RbS,
  output [7:0] PC1S,
  output [3:0] L2S,
  output [3:0] L1S,
  output [1:0] L4S,
  output [1:0] L3S,
  output [1:0] Rd_L4S,
  output [1:0] Rd_L3S,
  output [1:0] Rd_L1S,
  output RelativeS,
  output JRS,
  output BranchS,
  output MUX_ImmS,
  output MUX_RegInS,
  output L1RegWriteS,
  output MemWriteS,
  output MemReadS,
  output L4MUX_ULA_BS,
  output L4Reg_WriteS,
  output L3ALUOp_0S,
  output L3ALUOp_1S,
  output L3ALUOp_2S,
  output L3MUX_ULA_BS,
  output L3RegWriteS,
  output L2ConditionS,
  output Tipo_I_L2S,
  output Tipo_I_L1S,
  output [1:0] Sel_lane1S,
  output L4ALUOp_0S,
  output L4ALUOp_1S,
  output L4ALUOp_2S
);

  wire [0:0] RegO_q;
  wire [1:0] RegL_q;
  wire [7:0] multiplexer_1_out, multiplexer_2_out, multiplexer_3_out, multiplexer_4_out, multiplexer_5_out,
       multiplexer_6_out, multiplexer_7_out, multiplexer_8_out, multiplexer_9_out, multiplexer_10_out,
       multiplexer_11_out, multiplexer_12_out, multiplexer_13_out, multiplexer_14_out, multiplexer_15_out;
  wire [7:4] RegK_q;

  Multiplexer #(.width(8)) multiplexer_1 (.in0(L1_Ra), .in1({8{1'b0}}), .out(multiplexer_1_out), .sel(Flush_OR_Stall));
  Multiplexer #(.width(8)) multiplexer_2 (.in0(L1_Rb), .in1({8{1'b0}}), .out(multiplexer_2_out), .sel(Flush_OR_Stall));
  Register RegA (.D(multiplexer_1_out), .en(1'b1), .clk(CLK), .Q(L1_RaS), .clr(rst));
  Register RegB (.D(multiplexer_2_out), .en(1'b1), .clk(CLK), .Q(L1_RbS), .clr(rst));
  Register RegC (.D(multiplexer_3_out), .en(1'b1), .clk(CLK), .Q(L2_RaS), .clr(rst));
  Multiplexer #(.width(8)) multiplexer_3 (.in0(L2_Ra), .in1({8{1'b0}}), .out(multiplexer_3_out), .sel(Flush_OR_Stall));
  Register RegD (.D(multiplexer_4_out), .en(1'b1), .clk(CLK), .Q(L2_RbS), .clr(rst));
  Multiplexer #(.width(8)) multiplexer_4 (.in0(L2_Rb), .in1({8{1'b0}}), .out(multiplexer_4_out), .sel(Flush_OR_Stall));
  Register RegE (.D(multiplexer_5_out), .en(1'b1), .clk(CLK), .Q(L3_RaS), .clr(rst));
  Multiplexer #(.width(8)) multiplexer_5 (.in0(L3_Ra), .in1({8{1'b0}}), .out(multiplexer_5_out), .sel(Flush_OR_Stall));
  Register RegF (.D(multiplexer_6_out), .en(1'b1), .clk(CLK), .Q(L3_RbS), .clr(rst));
  Multiplexer #(.width(8)) multiplexer_6 (.in0(L3_Rb), .in1({8{1'b0}}), .out(multiplexer_6_out), .sel(Flush_OR_Stall));
  Register RegG (.D(multiplexer_7_out), .en(1'b1), .clk(CLK), .Q(L4_RaS), .clr(rst));
  Multiplexer #(.width(8)) multiplexer_7 (.in0(L4_Ra), .in1({8{1'b0}}), .out(multiplexer_7_out), .sel(Flush_OR_Stall));
  Register RegH (.D(multiplexer_8_out), .en(1'b1), .clk(CLK), .Q(L4_RbS), .clr(rst));
  Multiplexer #(.width(8)) multiplexer_8 (.in0(L4_Rb), .in1({8{1'b0}}), .out(multiplexer_8_out), .sel(Flush_OR_Stall));
  Register RegI (.D(multiplexer_9_out), .en(1'b1), .clk(CLK), .Q(PC1S), .clr(rst));
  Multiplexer #(.width(8)) multiplexer_9 (.in0(PC1), .in1({8{1'b0}}), .out(multiplexer_9_out), .sel(Flush_OR_Stall));
  Register RegJ (.D(multiplexer_10_out), .en(1'b1), .clk(CLK), .Q({L1S, L2S}), .clr(rst));
  Multiplexer #(.width(8)) multiplexer_10 (
    .in0({L1, L2}), .in1({8{1'b0}}), .out(multiplexer_10_out), .sel(Flush_OR_Stall));
  Register RegK (.D(multiplexer_11_out), .en(1'b1), .clk(CLK), .Q({RegK_q, L3S, L4S}), .clr(rst));
  Multiplexer #(.width(8)) multiplexer_11 (
    .in0({4'b0000, L3, L4}), .in1({8{1'b0}}), .out(multiplexer_11_out), .sel(Flush_OR_Stall));
  Register RegL (.D(multiplexer_12_out), .en(1'b1), .clk(CLK), .Q({Rd_L1S, Rd_L3S, Rd_L4S, RegL_q}), .clr(rst));
  Multiplexer #(.width(8)) multiplexer_12 (
    .in0({Rd_L1, Rd_L3, Rd_L4, 2'b00}), .in1({8{1'b0}}), .out(multiplexer_12_out), .sel(Flush_OR_Stall));
  Register RegM (
    .D(multiplexer_13_out), .en(1'b1), .clk(CLK),
    .Q({MemReadS, MemWriteS, L1RegWriteS, MUX_RegInS, MUX_ImmS, BranchS, JRS, RelativeS}), .clr(rst));
  Multiplexer #(.width(8)) multiplexer_13 (
    .in0({MemRead, MemWrite, L1RegWrite, MUX_RegIn, MUX_Imm, Branch, JR, Relative}), .in1({8{1'b0}}),
    .out(multiplexer_13_out), .sel(Flush_OR_Stall));
  Register RegN (
    .D(multiplexer_14_out), .en(1'b1), .clk(CLK),
    .Q({L2ConditionS, L3RegWriteS, L3MUX_ULA_BS, L3ALUOp_2S, L3ALUOp_1S, L3ALUOp_0S, L4Reg_WriteS, L4MUX_ULA_BS}),
    .clr(rst));
  Multiplexer #(.width(8)) multiplexer_14 (
    .in0({L2Condition, L3RegWrite, L3MUX_ULA_B, L3AluOp_2, L3AluOp_1, L3AluOp_0, L4RegWrite, L4MUX_ULA_B}),
    .in1({8{1'b0}}), .out(multiplexer_14_out), .sel(Flush_OR_Stall));
  Register RegO (
    .D(multiplexer_15_out), .en(1'b1), .clk(CLK),
    .Q({L4ALUOp_2S, L4ALUOp_1S, L4ALUOp_0S, Sel_lane1S, Tipo_I_L1S, Tipo_I_L2S, RegO_q[0]}), .clr(rst));
  Multiplexer #(.width(8)) multiplexer_15 (
    .in0({L4AluOp_2, L4AluOp_1, L4AluOp_0, Sel_Lane1, Tipo_I_L1, Tipo_I_2, 1'b0}), .in1({8{1'b0}}),
    .out(multiplexer_15_out), .sel(Flush_OR_Stall));
endmodule

module Extensao_reg_id_ex (
  input  [1:0] RdAddr_l3_ra,
  input  [1:0] RdAddr_l2_ra,
  input  [1:0] RdAddr_l2_rb,
  input  [1:0] RdAddr_l1_rb,
  input  [1:0] RdAddr_l3_rb,
  input  [1:0] RdAddr_l4_ra,
  input  [1:0] RdAddr_l4_rb,
  input  [1:0] RdAddr_l1_ra,
  input  [3:0] Opcode_l1_ex,
  input  CLK,
  input  Flush,
  input  rst,
  output [1:0] ra_l3_addr,
  output [1:0] ra_l2_addr,
  output [1:0] rb_l2_addr,
  output [1:0] rb_l1_addr,
  output [1:0] rb_l3_addr,
  output [1:0] ra_l4_addr,
  output [1:0] rb_l4_addr,
  output [1:0] ra_l1_addr,
  output [3:0] opcode_l1_exS
);

  wire [7:0] multiplexer_1_out, multiplexer_2_out, multiplexer_3_out;
  wire [7:4] register_1_q, undriven;

  Register RegA (
    .D(multiplexer_1_out), .en(1'b1), .clk(CLK), .Q({rb_l1_addr, rb_l2_addr, ra_l2_addr, ra_l3_addr}),
    .clr(rst));
  Multiplexer #(.width(8)) multiplexer_1 (
    .in0({RdAddr_l1_rb, RdAddr_l2_rb, RdAddr_l2_ra, RdAddr_l3_ra}), .in1({8{1'b0}}), .out(multiplexer_1_out),
    .sel(Flush));
  Register RegB (
    .D(multiplexer_2_out), .en(1'b1), .clk(CLK), .Q({ra_l1_addr, rb_l4_addr, ra_l4_addr, rb_l3_addr}),
    .clr(rst));
  Multiplexer #(.width(8)) multiplexer_2 (
    .in0({RdAddr_l1_ra, RdAddr_l4_rb, RdAddr_l4_ra, RdAddr_l3_rb}), .in1({8{1'b0}}), .out(multiplexer_2_out),
    .sel(Flush));
  Register register_1 (.D(multiplexer_3_out), .en(1'b1), .clk(CLK), .Q({register_1_q, opcode_l1_exS}), .clr(rst));
  Multiplexer #(.width(8)) multiplexer_3 (
    .in0({undriven, Opcode_l1_ex}), .in1({8{1'b0}}), .out(multiplexer_3_out), .sel(Flush));
endmodule

module Registrador_EX_WB (
  input  [7:0] lane1_out,
  input  [7:0] ULA_A,
  input  [7:0] ULA_B,
  input  L1_MUX_RegIn,
  input  L1_RegWrite,
  input  [1:0] Rd_L4,
  input  [1:0] Rd_L3,
  input  [1:0] Rd_L1,
  input  Tipo_I_L1,
  input  Tipo_I_L2,
  input  L4_RegWrite,
  input  L3_RegWrite,
  input  CLK,
  input  rst,
  output [7:0] lane1_outS,
  output [7:0] ULA_AS,
  output [7:0] ULA_BS,
  output L1_MUX_RegInS,
  output L1_RegWriteS,
  output [1:0] Rd_L4S,
  output [1:0] Rd_L3S,
  output [1:0] Rd_L1S,
  output Tipo_I_L1S,
  output Tipo_I_L2S,
  output L4_RegWriteS,
  output L3_RegWriteS
);

  wire [3:0] RegE_q;

  Register RegA (.D(lane1_out), .en(1'b1), .clk(CLK), .Q(lane1_outS), .clr(rst));
  Register RegB (.D(ULA_A), .en(1'b1), .clk(CLK), .Q(ULA_AS), .clr(rst));
  Register RegC (.D(ULA_B), .en(1'b1), .clk(CLK), .Q(ULA_BS), .clr(rst));
  Register RegD (
    .D({Rd_L1, Rd_L3, Rd_L4, L1_RegWrite, L1_MUX_RegIn}), .en(1'b1), .clk(CLK),
    .Q({Rd_L1S, Rd_L3S, Rd_L4S, L1_RegWriteS, L1_MUX_RegInS}), .clr(rst));
  Register RegE (
    .D({L3_RegWrite, L4_RegWrite, Tipo_I_L2, Tipo_I_L1, 4'b0000}), .en(1'b1), .clk(CLK),
    .Q({L3_RegWriteS, L4_RegWriteS, Tipo_I_L2S, Tipo_I_L1S, RegE_q}), .clr(rst));
endmodule

module Decodificador (
  input  [31:0] Instr_32b,
  output [1:0] RdAddr_L1_Ra,
  output [1:0] RdAddr_L2_Ra,
  output [1:0] RdAddr_L3_Ra,
  output [1:0] RdAddr_L4_Ra,
  output [1:0] RdAddr_L1_Rb,
  output [1:0] RdAddr_L2_Rb,
  output [1:0] RdAddr_L3_Rb,
  output [1:0] RdAddr_L4_Rb,
  output [1:0] Rd_L1,
  output [1:0] Rd_L3,
  output [1:0] Rd_L4,
  output [3:0] Imm_L1,
  output [3:0] Imm_L2,
  output [1:0] Imm_L3,
  output [1:0] Imm_L4,
  output [1:0] Sel_lane1,
  output MUX_Imm,
  output MemRead,
  output MemWrite,
  output l1RegWrite,
  output Mux_RegIn,
  output Condition,
  output Relative,
  output JR,
  output Branch,
  output MUX_ULA_BL3,
  output RegWriteL3,
  output [2:0] ALUOpL3,
  output MUX_ULA_BL4,
  output RegWriteL4,
  output [2:0] ALUOpL4,
  output Tipo_I_lane1,
  output Tipo_i_lane2,
  output [3:0] Opcode_lane1
);

  ROM #(.addrWidth(4), .dataWidth(7)) rom_1 (
    .addr(Instr_32b[31:28]), .data({Mux_RegIn, l1RegWrite, MemWrite, MemRead, MUX_Imm, Sel_lane1}));
  ROM #(.addrWidth(4), .dataWidth(4)) rom_2 (.addr(Instr_32b[23:20]), .data({Branch, JR, Relative, Condition}));
  ROM #(.addrWidth(4), .dataWidth(5)) rom_3 (.addr(Instr_32b[15:12]), .data({ALUOpL3, RegWriteL3, MUX_ULA_BL3}));
  ROM #(.addrWidth(4), .dataWidth(5)) rom_4 (.addr(Instr_32b[7:4]), .data({ALUOpL4, RegWriteL4, MUX_ULA_BL4}));
  Detector_tipo_I detector_tipo_i_1 (.Opcode(Instr_32b[31:28]), .is_I(Tipo_I_lane1));
  Detector_tipo_I detector_tipo_i_2 (.Opcode(Instr_32b[23:20]), .is_I(Tipo_i_lane2));

  assign Imm_L1 = Instr_32b[27:24];
  assign Imm_L2 = Instr_32b[19:16];
  assign Imm_L3 = Instr_32b[9:8];
  assign Imm_L4 = Instr_32b[1:0];
  assign Opcode_lane1 = Instr_32b[31:28];
  assign Rd_L1 = Instr_32b[27:26];
  assign Rd_L3 = Instr_32b[11:10];
  assign Rd_L4 = Instr_32b[3:2];
  assign RdAddr_L1_Ra = Instr_32b[27:26];
  assign RdAddr_L1_Rb = Instr_32b[25:24];
  assign RdAddr_L2_Ra = Instr_32b[19:18];
  assign RdAddr_L2_Rb = Instr_32b[17:16];
  assign RdAddr_L3_Ra = Instr_32b[11:10];
  assign RdAddr_L3_Rb = Instr_32b[9:8];
  assign RdAddr_L4_Ra = Instr_32b[3:2];
  assign RdAddr_L4_Rb = Instr_32b[1:0];

  // Other names for the same wires on the sheet: Lane4_ULAB[7:0] = Instr_32b[7:0]; Rb_Lane4[1:0] = Instr_32b[1:0];
  //   Ra_Lane4[1:0] = Instr_32b[3:2]; Opcode_Lane4[3:0] = Instr_32b[7:4]; Lane3_ULAA[7:0] = Instr_32b[15:8];
  //   Rb_Lane3[1:0] = Instr_32b[9:8]; Ra_Lane3[1:0] = Instr_32b[11:10]; Opcode_Lane3[3:0] = Instr_32b[15:12];
  //   Lane2_Desvios[7:0] = Instr_32b[23:16]; Rb_Lane2[1:0] = Instr_32b[17:16]; Ra_Lane2[1:0] = Instr_32b[19:18];
  //   Opcode_Lane2[3:0] = Instr_32b[23:20]; Lane1_Memoria[7:0] = Instr_32b[31:24]; Rb_Lane1[1:0] = Instr_32b[25:24];
  //   Ra_Lane1[1:0] = Instr_32b[27:26]

  // Notes on the sheet:
  //   contents of rom_1 (hex, n*v repeats v):
  //   4*3 28 13 65 61 3 3 62 5*3
  //   contents of rom_2 (hex, n*v repeats v):
  //   8 b 4
  //   contents of rom_3 (hex, n*v repeats v):
  //   1c 1c 1c 3 4*1c 2 6 1c a e 12 16 1c
  //   contents of rom_4 (hex, n*v repeats v):
  //   1c 1c 1c 3 4*1c 2 6 1c a e 12 16 1c
endmodule

module Detector_tipo_I (
  input  [3:0] Opcode,
  output is_I
);

  wire comparator_1_eq, comparator_2_eq, comparator_3_eq;

  Comparator #(.width(4)) comparator_1 (.a(Opcode), .b(4'b0110), .eq(comparator_1_eq));  // open: gt, lt
  Comparator #(.width(4)) comparator_2 (.a(Opcode), .b(4'b0111), .eq(comparator_2_eq));  // open: gt, lt
  Comparator #(.width(4)) comparator_3 (.a(Opcode), .b(4'b0001), .eq(comparator_3_eq));  // open: gt, lt
  or or_1 (is_I, comparator_1_eq, comparator_2_eq, comparator_3_eq);
endmodule

module InstMem (
  input  [7:0] Address,
  output [31:0] InstOut
);

  ROM #(.dataWidth(32)) rom_1 (.addr(Address), .data(InstOut));

  // Notes on the sheet:
  //   contents of rom_1 (hex, n*v repeats v):
  //   61ffffff 78ffffff a8ffffff 60ffffff 70ffffff a4ffffff 60ffffff 7cffffff acffffff 56ff3fff ffff3935
  //   61ffffff 78ffffff ff0cffff 60ffffff 79ffffff ff20ffff ffffffff ffffffff ffffffff
endmodule

module hazard_detector (
  input  [3:0] opcode_lane1_IDEX,
  input  [1:0] rd_l1_IDEX,
  input  [1:0] ra_lane1_ID,
  input  [1:0] rb_lane1_ID,
  input  [1:0] ra_lane2_ID,
  input  [1:0] rb_lane2_ID,
  input  [1:0] ra_lane3_ID,
  input  [1:0] rb_lane3_ID,
  input  [1:0] ra_lane4_ID,
  input  [1:0] rb_lane4_ID,
  output stall
);

  wire any_match, comparator_2_eq, comparator_3_eq, comparator_4_eq, comparator_5_eq, comparator_6_eq,
       comparator_7_eq, comparator_8_eq, comparator_9_eq, is_ld;

  Comparator #(.width(4)) comparator_1 (.a(opcode_lane1_IDEX), .b(4'b0100), .eq(is_ld));  // open: gt, lt
  Comparator #(.width(2)) comparator_2 (.a(rd_l1_IDEX), .b(ra_lane1_ID), .eq(comparator_2_eq));  // open: gt, lt
  Comparator #(.width(2)) comparator_3 (.a(rd_l1_IDEX), .b(rb_lane1_ID), .eq(comparator_3_eq));  // open: gt, lt
  Comparator #(.width(2)) comparator_4 (.a(rd_l1_IDEX), .b(ra_lane2_ID), .eq(comparator_4_eq));  // open: gt, lt
  Comparator #(.width(2)) comparator_5 (.a(rd_l1_IDEX), .b(rb_lane2_ID), .eq(comparator_5_eq));  // open: gt, lt
  Comparator #(.width(2)) comparator_6 (.a(rd_l1_IDEX), .b(ra_lane3_ID), .eq(comparator_6_eq));  // open: gt, lt
  Comparator #(.width(2)) comparator_7 (.a(rd_l1_IDEX), .b(rb_lane3_ID), .eq(comparator_7_eq));  // open: gt, lt
  Comparator #(.width(2)) comparator_8 (.a(rd_l1_IDEX), .b(ra_lane4_ID), .eq(comparator_8_eq));  // open: gt, lt
  Comparator #(.width(2)) comparator_9 (.a(rd_l1_IDEX), .b(rb_lane4_ID), .eq(comparator_9_eq));  // open: gt, lt
  or or_1 (any_match, comparator_2_eq, comparator_3_eq, comparator_4_eq, comparator_5_eq, comparator_6_eq, comparator_7_eq, comparator_8_eq, comparator_9_eq);
  and and_1 (stall, is_ld, any_match);
endmodule

module forwardingUnit_ID (
  input  [7:0] ReadData1,
  input  [7:0] ReadData2,
  input  [1:0] ReadAddr1,
  input  [1:0] ReadAddr2,
  input  RegWrite,
  input  [1:0] WriteAddr,
  input  [7:0] WriteData,
  output [7:0] OutData1,
  output [7:0] OutData2
);

  wire and_1_out, and_2_out, comparator_1_eq, comparator_2_eq;

  Comparator #(.width(2)) comparator_1 (.a(WriteAddr), .b(ReadAddr1), .eq(comparator_1_eq));  // open: gt, lt
  Comparator #(.width(2)) comparator_2 (.a(WriteAddr), .b(ReadAddr2), .eq(comparator_2_eq));  // open: gt, lt
  and and_1 (and_1_out, RegWrite, comparator_1_eq);
  and and_2 (and_2_out, comparator_2_eq, RegWrite);
  Multiplexer #(.width(8)) multiplexer_1 (.in0(ReadData1), .in1(WriteData), .out(OutData1), .sel(and_1_out));
  Multiplexer #(.width(8)) multiplexer_2 (.in0(ReadData2), .in1(WriteData), .out(OutData2), .sel(and_2_out));
endmodule
